// Logisim project TOY_16(16 bits CPU).circ as structural Verilog
module full_circuit (
  input  A,
  input  B,
  input  CIN,
  output SUM,
  output COUT
);

  wire and_1_out, and_2_out, xor_1_out;

  xor xor_1 (xor_1_out, A, B);
  and and_1 (and_1_out, A, B);
  xor xor_2 (SUM, xor_1_out, CIN);
  and and_2 (and_2_out, xor_1_out, CIN);
  or or_1 (COUT, and_1_out, and_2_out);
  // Probe on {COUT, SUM}
endmodule

module ADDER_8_bit (
  input  [7:0] A,
  input  [7:0] B,
  input  CIN,
  output [7:0] out_4,
  output out_5
);

  wire full_circuit_1_cout, full_circuit_2_cout, full_circuit_3_cout, full_circuit_4_cout,
       full_circuit_5_cout, full_circuit_6_cout, full_circuit_7_cout;

  // Probe on B
  // Probe on A
  full_circuit full_circuit_1 (.A(A[0]), .B(B[0]), .CIN(CIN), .SUM(out_4[0]), .COUT(full_circuit_1_cout));
  full_circuit full_circuit_2 (
    .A(A[1]), .B(B[1]), .CIN(full_circuit_1_cout), .SUM(out_4[1]), .COUT(full_circuit_2_cout));
  full_circuit full_circuit_3 (
    .A(A[2]), .B(B[2]), .CIN(full_circuit_2_cout), .SUM(out_4[2]), .COUT(full_circuit_3_cout));
  full_circuit full_circuit_4 (
    .A(A[3]), .B(B[3]), .CIN(full_circuit_3_cout), .SUM(out_4[3]), .COUT(full_circuit_4_cout));
  full_circuit full_circuit_5 (
    .A(A[4]), .B(B[4]), .CIN(full_circuit_4_cout), .SUM(out_4[4]), .COUT(full_circuit_5_cout));
  full_circuit full_circuit_6 (
    .A(A[5]), .B(B[5]), .CIN(full_circuit_5_cout), .SUM(out_4[5]), .COUT(full_circuit_6_cout));
  full_circuit full_circuit_7 (
    .A(A[6]), .B(B[6]), .CIN(full_circuit_6_cout), .SUM(out_4[6]), .COUT(full_circuit_7_cout));
  full_circuit full_circuit_8 (.A(A[7]), .B(B[7]), .CIN(full_circuit_7_cout), .SUM(out_4[7]), .COUT(out_5));
  // Probe on {out_5, out_4}
endmodule

module MUX (
  input  [3:0] in_1,
  input  [3:0] in_2,
  input  [3:0] in_3,
  input  [3:0] in_4,
  input  in_5,
  input  in_6,
  output [3:0] out_7
);

  wire and_1_out, and_2_out, and_3_out, nor_1_out, not_1_out, not_2_out;
  wire [3:0] controlled_buffer_1_out, controlled_buffer_2_out, controlled_buffer_3_out,
       controlled_buffer_4_out;

  assign controlled_buffer_1_out = nor_1_out ? in_1 : 4'bz;  // Controlled_Buffer controlled_buffer_1
  assign controlled_buffer_2_out = and_2_out ? in_2 : 4'bz;  // Controlled_Buffer controlled_buffer_2
  assign controlled_buffer_3_out = and_3_out ? in_3 : 4'bz;  // Controlled_Buffer controlled_buffer_3
  assign controlled_buffer_4_out = and_1_out ? in_4 : 4'bz;  // Controlled_Buffer controlled_buffer_4
  and and_1 (and_1_out, in_5, in_6);
  nor nor_1 (nor_1_out, in_5, in_6);
  not not_1 (not_1_out, in_5);
  Pull_Resistor pull_resistor_1 (.node(controlled_buffer_3_out));
  Pull_Resistor pull_resistor_2 (.node(controlled_buffer_4_out));
  and and_2 (and_2_out, not_1_out, in_6);
  Pull_Resistor pull_resistor_3 (.node(controlled_buffer_1_out));
  Pull_Resistor pull_resistor_4 (.node(controlled_buffer_2_out));
  and and_3 (and_3_out, not_2_out, in_5);
  not not_2 (not_2_out, in_6);
  assign out_7 = controlled_buffer_1_out | controlled_buffer_2_out | controlled_buffer_3_out | controlled_buffer_4_out;  // OR_Gate_part or_1, 4 bits wide
  // Probe on out_7
endmodule

module De_Coder (
  input  in_1,
  input  in_2,
  input  in_3,
  output _0,
  output _1,
  output _2,
  output _3,
  output _4,
  output _5,
  output _6,
  output _7
);

  wire not_1_out, not_2_out, not_3_out, not_4_out, not_5_out, not_6_out, not_7_out;

  // Probe on {in_1, in_2, in_3}
  not not_1 (not_1_out, in_2);
  not not_2 (not_2_out, in_1);
  not not_3 (not_3_out, in_3);
  not not_4 (not_4_out, in_1);
  not not_5 (not_5_out, in_1);
  not not_6 (not_6_out, in_3);
  not not_7 (not_7_out, in_2);
  and and_1 (_1, in_3, not_1_out, not_2_out);
  and and_2 (_2, not_3_out, in_2, not_4_out);
  and and_3 (_3, in_3, in_2, not_5_out);
  and and_4 (_4, not_6_out, not_7_out, in_1);
  and and_5 (_5, in_3, ~in_2, in_1);  // AND_Gate_part
  and and_6 (_6, ~in_3, in_2, in_1);  // AND_Gate_part
  and and_7 (_7, in_3, in_2, in_1);
  nor nor_1 (_0, in_3, in_2, in_1);
endmodule

module De_mux (
  input  in_1,
  input  in_2,
  input  in_3,
  input  [3:0] X,
  output [3:0] out_5,
  output [3:0] out_6,
  output [3:0] _2,
  output [3:0] _3,
  output [3:0] _4,
  output [3:0] _5,
  output [3:0] _6,
  output [3:0] _7
);

  wire and_1_out, and_2_out, and_3_out, and_4_out, and_5_out, and_6_out, and_7_out, nor_1_out, not_1_out,
       not_2_out, not_3_out, not_4_out, not_5_out, not_6_out, not_7_out;

  // Probe on {in_1, in_2, in_3}
  not not_1 (not_1_out, in_2);
  not not_2 (not_2_out, in_1);
  not not_3 (not_3_out, in_3);
  not not_4 (not_4_out, in_1);
  not not_5 (not_5_out, in_1);
  not not_6 (not_6_out, in_3);
  not not_7 (not_7_out, in_2);
  and and_1 (and_1_out, in_3, not_1_out, not_2_out);
  and and_2 (and_2_out, not_3_out, in_2, not_4_out);
  and and_3 (and_3_out, in_3, in_2, not_5_out);
  and and_4 (and_4_out, not_6_out, not_7_out, in_1);
  and and_5 (and_5_out, in_3, ~in_2, in_1);  // AND_Gate_part
  and and_6 (and_6_out, ~in_3, in_2, in_1);  // AND_Gate_part
  and and_7 (and_7_out, in_3, in_2, in_1);
  Pull_Resistor pull_resistor_1 (.node(out_5));
  assign out_5 = nor_1_out ? X : 4'bz;  // Controlled_Buffer controlled_buffer_1
  nor nor_1 (nor_1_out, in_3, in_2, in_1);
  Pull_Resistor pull_resistor_2 (.node(out_6));
  assign out_6 = and_1_out ? X : 4'bz;  // Controlled_Buffer controlled_buffer_2
  Pull_Resistor pull_resistor_3 (.node(_2));
  assign _2 = and_2_out ? X : 4'bz;  // Controlled_Buffer controlled_buffer_3
  Pull_Resistor pull_resistor_4 (.node(_3));
  assign _3 = and_3_out ? X : 4'bz;  // Controlled_Buffer controlled_buffer_4
  Pull_Resistor pull_resistor_5 (.node(_4));
  assign _4 = and_4_out ? X : 4'bz;  // Controlled_Buffer controlled_buffer_5
  Pull_Resistor pull_resistor_6 (.node(_5));
  assign _5 = and_5_out ? X : 4'bz;  // Controlled_Buffer controlled_buffer_6
  Pull_Resistor pull_resistor_7 (.node(_6));
  assign _6 = and_6_out ? X : 4'bz;  // Controlled_Buffer controlled_buffer_7
  Pull_Resistor pull_resistor_8 (.node(_7));
  assign _7 = and_7_out ? X : 4'bz;  // Controlled_Buffer controlled_buffer_8

  // Notes on the sheet:
  //   0
  //   1
endmodule

module De_coder_MUX (
  input  in_1,
  input  in_2,
  input  in_3,
  input  [3:0] X,
  output [3:0] out_5,
  output out_6,
  output [3:0] out_7,
  output out_8,
  output [3:0] _2,
  output out_10,
  output [3:0] _3,
  output out_12,
  output [3:0] _4,
  output out_14,
  output [3:0] _5,
  output out_16,
  output [3:0] _6,
  output out_18,
  output [3:0] _7,
  output out_20
);

  wire not_1_out, not_2_out, not_3_out, not_4_out, not_5_out, not_6_out, not_7_out;

  // Probe on {in_1, in_2, in_3}
  not not_1 (not_1_out, in_2);
  not not_2 (not_2_out, in_1);
  not not_3 (not_3_out, in_3);
  not not_4 (not_4_out, in_1);
  not not_5 (not_5_out, in_1);
  not not_6 (not_6_out, in_3);
  not not_7 (not_7_out, in_2);
  and and_1 (out_8, in_3, not_1_out, not_2_out);
  and and_2 (out_10, not_3_out, in_2, not_4_out);
  and and_3 (out_12, in_3, in_2, not_5_out);
  and and_4 (out_14, not_6_out, not_7_out, in_1);
  and and_5 (out_16, in_3, ~in_2, in_1);  // AND_Gate_part
  and and_6 (out_18, ~in_3, in_2, in_1);  // AND_Gate_part
  and and_7 (out_20, in_3, in_2, in_1);
  Pull_Resistor pull_resistor_1 (.node(out_5));
  assign out_5 = out_6 ? X : 4'bz;  // Controlled_Buffer controlled_buffer_1
  nor nor_1 (out_6, in_3, in_2, in_1);
  Pull_Resistor pull_resistor_2 (.node(out_7));
  assign out_7 = out_8 ? X : 4'bz;  // Controlled_Buffer controlled_buffer_2
  Pull_Resistor pull_resistor_3 (.node(_2));
  assign _2 = out_10 ? X : 4'bz;  // Controlled_Buffer controlled_buffer_3
  Pull_Resistor pull_resistor_4 (.node(_3));
  assign _3 = out_12 ? X : 4'bz;  // Controlled_Buffer controlled_buffer_4
  Pull_Resistor pull_resistor_5 (.node(_4));
  assign _4 = out_14 ? X : 4'bz;  // Controlled_Buffer controlled_buffer_5
  Pull_Resistor pull_resistor_6 (.node(_5));
  assign _5 = out_16 ? X : 4'bz;  // Controlled_Buffer controlled_buffer_6
  Pull_Resistor pull_resistor_7 (.node(_6));
  assign _6 = out_18 ? X : 4'bz;  // Controlled_Buffer controlled_buffer_7
  Pull_Resistor pull_resistor_8 (.node(_7));
  assign _7 = out_20 ? X : 4'bz;  // Controlled_Buffer controlled_buffer_8

  // Notes on the sheet:
  //   0
  //   1
endmodule

module ALU (
  input  [7:0] in_1,
  input  [7:0] in_2,
  input  in_3,
  input  in_4,
  input  in_5,
  output [7:0] out_6
);

  wire [7:0] adder_8_bit_1_out_4, and_gate_8bit_1_out_3, xor_gate_8bit_1_out_3;

  XOR_Gate_8bit xor_gate_8bit_1 (.in_1(in_1), .in_2(in_2), .out_3(xor_gate_8bit_1_out_3));
  AND_Gate_8bit and_gate_8bit_1 (.in_1(in_1), .in_2(in_2), .out_3(and_gate_8bit_1_out_3));
  ADDER_8_bit adder_8_bit_1 (.A(in_1), .B(in_2), .CIN(1'b0), .out_4(adder_8_bit_1_out_4));  // open: out_5
  assign out_6 = in_4 ? xor_gate_8bit_1_out_3 : 8'bz;  // Controlled_Buffer controlled_buffer_1
  assign out_6 = in_5 ? and_gate_8bit_1_out_3 : 8'bz;  // Controlled_Buffer controlled_buffer_2
  assign out_6 = in_3 ? adder_8_bit_1_out_4 : 8'bz;  // Controlled_Buffer controlled_buffer_3
  Pull_Resistor pull_resistor_1 (.node(out_6));
endmodule

module Right_bitshifter (
  input  [7:0] in_1,
  input  [7:0] in_2,
  output [7:0] out_3
);

  wire [7:0] mux_2to1_1_p4, mux_2to1_2_p4, mux_2to1_3_p4, mux_2to1_4_p4, mux_2to1_5_p4, mux_2to1_6_p4,
       mux_2to1_7_p4, mux_2to1_8_p4, mux_2to1_9_oi, mux_2to1_10_oi, mux_2to1_11_oi, mux_2to1_12_oi,
       mux_2to1_13_oi, mux_2to1_14_oi, mux_2to1_15_oi, mux_2to1_16_oi, pull_resistor_1_node;

  Pull_Resistor pull_resistor_1 (.node(pull_resistor_1_node));
  // MUX_2to1 mux_2to1_1: pin names not known; wires that end beside it: in_1[0], in_1[1], in_2[0], mux_2to1_1_p4
  // MUX_2to1 mux_2to1_2: pin names not known; wires that end beside it: in_1[1], in_1[2], in_2[0], mux_2to1_2_p4
  // MUX_2to1 mux_2to1_3: pin names not known; wires that end beside it: in_1[2], in_1[3], in_2[0], mux_2to1_3_p4
  // MUX_2to1 mux_2to1_4: pin names not known; wires that end beside it: in_1[3], in_1[4], in_2[0], mux_2to1_4_p4
  // MUX_2to1 mux_2to1_5: pin names not known; wires that end beside it: in_1[4], in_1[5], in_2[0], mux_2to1_5_p4
  // MUX_2to1 mux_2to1_6: pin names not known; wires that end beside it: in_1[5], in_1[6], in_2[0], mux_2to1_6_p4
  // MUX_2to1 mux_2to1_7: pin names not known; wires that end beside it: in_1[6], in_1[7], in_2[0], mux_2to1_7_p4
  // MUX_2to1 mux_2to1_8: pin names not known; wires that end beside it: in_1[7], pull_resistor_1_node, in_2[0], mux_2to1_8_p4
  MUX_2to1 mux_2to1_9 (.Ai(mux_2to1_1_p4), .Bi(mux_2to1_3_p4), .CA(in_2[1]), .Oi(mux_2to1_9_oi));  // open: CB
  MUX_2to1 mux_2to1_10 (.Ai(mux_2to1_2_p4), .Bi(mux_2to1_4_p4), .CA(in_2[1]), .Oi(mux_2to1_10_oi));  // open: CB
  MUX_2to1 mux_2to1_11 (.Ai(mux_2to1_3_p4), .Bi(mux_2to1_5_p4), .CA(in_2[1]), .Oi(mux_2to1_11_oi));  // open: CB
  MUX_2to1 mux_2to1_12 (.Ai(mux_2to1_4_p4), .Bi(mux_2to1_6_p4), .CA(in_2[1]), .Oi(mux_2to1_12_oi));  // open: CB
  MUX_2to1 mux_2to1_13 (.Ai(mux_2to1_5_p4), .Bi(mux_2to1_7_p4), .CA(in_2[1]), .Oi(mux_2to1_13_oi));  // open: CB
  MUX_2to1 mux_2to1_14 (.Ai(mux_2to1_6_p4), .Bi(mux_2to1_8_p4), .CA(in_2[1]), .Oi(mux_2to1_14_oi));  // open: CB
  MUX_2to1 mux_2to1_15 (.Ai(mux_2to1_7_p4), .Bi(pull_resistor_1_node), .CA(in_2[1]), .Oi(mux_2to1_15_oi));  // open: CB
  MUX_2to1 mux_2to1_16 (.Ai(mux_2to1_8_p4), .Bi(pull_resistor_1_node), .CA(in_2[1]), .Oi(mux_2to1_16_oi));  // open: CB
  // MUX_2to1 mux_2to1_17: pin names not known; wires that end beside it: mux_2to1_9_oi, mux_2to1_13_oi, in_2[2], out_3[0]
  // MUX_2to1 mux_2to1_18: pin names not known; wires that end beside it: mux_2to1_10_oi, mux_2to1_14_oi, in_2[2], out_3[1]
  // MUX_2to1 mux_2to1_19: pin names not known; wires that end beside it: mux_2to1_11_oi, mux_2to1_15_oi, in_2[2], out_3[2]
  // MUX_2to1 mux_2to1_20: pin names not known; wires that end beside it: mux_2to1_12_oi, mux_2to1_16_oi, in_2[2], out_3[3]
  // MUX_2to1 mux_2to1_21: pin names not known; wires that end beside it: mux_2to1_13_oi, pull_resistor_1_node, in_2[2], out_3[4]
  // MUX_2to1 mux_2to1_22: pin names not known; wires that end beside it: mux_2to1_14_oi, pull_resistor_1_node, in_2[2], out_3[5]
  // MUX_2to1 mux_2to1_23: pin names not known; wires that end beside it: mux_2to1_15_oi, pull_resistor_1_node, in_2[2], out_3[6]
  // MUX_2to1 mux_2to1_24: pin names not known; wires that end beside it: mux_2to1_16_oi, pull_resistor_1_node, in_2[2], out_3[7]
endmodule

module Left_bitshifter (
  input  [7:0] in_1,
  input  [7:0] in_2,
  output [7:0] out_3
);

  wire [7:0] mux_2to1_1_p4, mux_2to1_2_p4, mux_2to1_3_p4, mux_2to1_4_p4, mux_2to1_5_p4, mux_2to1_6_p4,
       mux_2to1_7_p4, mux_2to1_8_p4, mux_2to1_9_oi, mux_2to1_10_oi, mux_2to1_11_oi, mux_2to1_12_oi,
       mux_2to1_13_oi, mux_2to1_14_oi, mux_2to1_15_oi, mux_2to1_16_oi, pull_resistor_1_node;

  Pull_Resistor pull_resistor_1 (.node(pull_resistor_1_node));
  // MUX_2to1 mux_2to1_1: pin names not known; wires that end beside it: in_1[0], pull_resistor_1_node, in_2[0], mux_2to1_1_p4
  // MUX_2to1 mux_2to1_2: pin names not known; wires that end beside it: in_1[1], in_1[0], in_2[0], mux_2to1_2_p4
  // MUX_2to1 mux_2to1_3: pin names not known; wires that end beside it: in_1[2], in_1[1], in_2[0], mux_2to1_3_p4
  // MUX_2to1 mux_2to1_4: pin names not known; wires that end beside it: in_1[3], in_1[2], in_2[0], mux_2to1_4_p4
  // MUX_2to1 mux_2to1_5: pin names not known; wires that end beside it: in_1[4], in_1[3], in_2[0], mux_2to1_5_p4
  // MUX_2to1 mux_2to1_6: pin names not known; wires that end beside it: in_1[5], in_1[4], in_2[0], mux_2to1_6_p4
  // MUX_2to1 mux_2to1_7: pin names not known; wires that end beside it: in_1[6], in_1[5], in_2[0], mux_2to1_7_p4
  // MUX_2to1 mux_2to1_8: pin names not known; wires that end beside it: in_1[7], in_1[6], in_2[0], mux_2to1_8_p4
  MUX_2to1 mux_2to1_9 (.Ai(mux_2to1_1_p4), .Bi(pull_resistor_1_node), .CA(in_2[1]), .Oi(mux_2to1_9_oi));  // open: CB
  MUX_2to1 mux_2to1_10 (.Ai(mux_2to1_2_p4), .Bi(pull_resistor_1_node), .CA(in_2[1]), .Oi(mux_2to1_10_oi));  // open: CB
  MUX_2to1 mux_2to1_11 (.Ai(mux_2to1_3_p4), .Bi(mux_2to1_1_p4), .CA(in_2[1]), .Oi(mux_2to1_11_oi));  // open: CB
  MUX_2to1 mux_2to1_12 (.Ai(mux_2to1_4_p4), .Bi(mux_2to1_2_p4), .CA(in_2[1]), .Oi(mux_2to1_12_oi));  // open: CB
  MUX_2to1 mux_2to1_13 (.Ai(mux_2to1_5_p4), .Bi(mux_2to1_3_p4), .CA(in_2[1]), .Oi(mux_2to1_13_oi));  // open: CB
  MUX_2to1 mux_2to1_14 (.Ai(mux_2to1_6_p4), .Bi(mux_2to1_4_p4), .CA(in_2[1]), .Oi(mux_2to1_14_oi));  // open: CB
  MUX_2to1 mux_2to1_15 (.Ai(mux_2to1_7_p4), .Bi(mux_2to1_5_p4), .CA(in_2[1]), .Oi(mux_2to1_15_oi));  // open: CB
  MUX_2to1 mux_2to1_16 (.Ai(mux_2to1_8_p4), .Bi(mux_2to1_6_p4), .CA(in_2[1]), .Oi(mux_2to1_16_oi));  // open: CB
  // MUX_2to1 mux_2to1_17: pin names not known; wires that end beside it: mux_2to1_9_oi, pull_resistor_1_node, in_2[2], out_3[0]
  // MUX_2to1 mux_2to1_18: pin names not known; wires that end beside it: mux_2to1_10_oi, pull_resistor_1_node, in_2[2], out_3[1]
  // MUX_2to1 mux_2to1_19: pin names not known; wires that end beside it: mux_2to1_11_oi, pull_resistor_1_node, in_2[2], out_3[2]
  // MUX_2to1 mux_2to1_20: pin names not known; wires that end beside it: mux_2to1_12_oi, pull_resistor_1_node, in_2[2], out_3[3]
  // MUX_2to1 mux_2to1_21: pin names not known; wires that end beside it: mux_2to1_13_oi, mux_2to1_9_oi, in_2[2], out_3[4]
  // MUX_2to1 mux_2to1_22: pin names not known; wires that end beside it: mux_2to1_14_oi, mux_2to1_10_oi, in_2[2], out_3[5]
  // MUX_2to1 mux_2to1_23: pin names not known; wires that end beside it: mux_2to1_15_oi, mux_2to1_11_oi, in_2[2], out_3[6]
  // MUX_2to1 mux_2to1_24: pin names not known; wires that end beside it: mux_2to1_16_oi, mux_2to1_12_oi, in_2[2], out_3[7]
endmodule

module NOT_Gate (
  input  in_1,
  output out_2
);

  Pull_Resistor pull_resistor_1 (.node(out_2));
  Transistor transistor_1 (.in(1'b1), .out(out_2), .gate(in_1));
endmodule

module NAND_Gate (
  input  in_1,
  input  in_2,
  output out_3
);

  wire transistor_2_out;

  Pull_Resistor #(.pull(1)) pull_resistor_1 (.node(out_3));
  Transistor #(.\type ("n")) transistor_1 (.in(transistor_2_out), .out(out_3), .gate(in_1));
  Transistor #(.\type ("n")) transistor_2 (.in(1'b0), .out(transistor_2_out), .gate(in_2));
endmodule

module AND_Gate_8bit (
  input  [7:0] in_1,
  input  [7:0] in_2,
  output [7:0] out_3
);

  wire nand_gate_1_out_3, nand_gate_2_out_3, nand_gate_3_out_3, nand_gate_4_out_3, nand_gate_5_out_3,
       nand_gate_6_out_3, nand_gate_7_out_3, nand_gate_8_out_3;

  NAND_Gate nand_gate_1 (.in_1(in_1[0]), .in_2(in_2[0]), .out_3(nand_gate_1_out_3));
  NAND_Gate nand_gate_2 (.in_1(in_1[1]), .in_2(in_2[1]), .out_3(nand_gate_2_out_3));
  NAND_Gate nand_gate_3 (.in_1(in_1[2]), .in_2(in_2[2]), .out_3(nand_gate_3_out_3));
  NAND_Gate nand_gate_4 (.in_1(in_1[3]), .in_2(in_2[3]), .out_3(nand_gate_4_out_3));
  NAND_Gate nand_gate_5 (.in_1(in_1[4]), .in_2(in_2[4]), .out_3(nand_gate_5_out_3));
  NAND_Gate nand_gate_6 (.in_1(in_1[5]), .in_2(in_2[5]), .out_3(nand_gate_6_out_3));
  NAND_Gate nand_gate_7 (.in_1(in_1[6]), .in_2(in_2[6]), .out_3(nand_gate_7_out_3));
  NAND_Gate nand_gate_8 (.in_1(in_1[7]), .in_2(in_2[7]), .out_3(nand_gate_8_out_3));
  NOT_Gate not_gate_1 (.in_1(nand_gate_1_out_3), .out_2(out_3[0]));
  NOT_Gate not_gate_2 (.in_1(nand_gate_2_out_3), .out_2(out_3[1]));
  NOT_Gate not_gate_3 (.in_1(nand_gate_3_out_3), .out_2(out_3[2]));
  NOT_Gate not_gate_4 (.in_1(nand_gate_4_out_3), .out_2(out_3[3]));
  NOT_Gate not_gate_5 (.in_1(nand_gate_5_out_3), .out_2(out_3[4]));
  NOT_Gate not_gate_6 (.in_1(nand_gate_6_out_3), .out_2(out_3[5]));
  NOT_Gate not_gate_7 (.in_1(nand_gate_7_out_3), .out_2(out_3[6]));
  NOT_Gate not_gate_8 (.in_1(nand_gate_8_out_3), .out_2(out_3[7]));
endmodule

module NOR_Gate (
  input  in_1,
  input  in_2,
  output out_3
);

  wire transistor_2_out;

  Pull_Resistor pull_resistor_1 (.node(out_3));
  Transistor transistor_1 (.in(transistor_2_out), .out(out_3), .gate(in_1));
  Transistor transistor_2 (.in(1'b1), .out(transistor_2_out), .gate(in_2));
endmodule

module XOR_Gate (
  input  in_1,
  input  in_2,
  output out_3
);

  wire nand_gate_1_out_3, nand_gate_2_out_3, nor_gate_1_out_3, not_gate_1_out_2, not_gate_2_out_2,
       not_gate_3_out_2, not_gate_4_out_2;

  NOT_Gate not_gate_1 (.in_1(in_2), .out_2(not_gate_1_out_2));
  NOT_Gate not_gate_2 (.in_1(in_1), .out_2(not_gate_2_out_2));
  NAND_Gate nand_gate_1 (.in_1(in_1), .in_2(not_gate_1_out_2), .out_3(nand_gate_1_out_3));
  NAND_Gate nand_gate_2 (.in_1(not_gate_2_out_2), .in_2(in_2), .out_3(nand_gate_2_out_3));
  NOT_Gate not_gate_3 (.in_1(nand_gate_1_out_3), .out_2(not_gate_3_out_2));
  NOT_Gate not_gate_4 (.in_1(nand_gate_2_out_3), .out_2(not_gate_4_out_2));
  NOR_Gate nor_gate_1 (.in_1(not_gate_3_out_2), .in_2(not_gate_4_out_2), .out_3(nor_gate_1_out_3));
  NOT_Gate not_gate_5 (.in_1(nor_gate_1_out_3), .out_2(out_3));
endmodule

module XOR_Gate_8bit (
  input  [7:0] in_1,
  input  [7:0] in_2,
  output [7:0] out_3
);

  XOR_Gate xor_gate_1 (.in_1(in_1[0]), .in_2(in_2[0]), .out_3(out_3[0]));
  XOR_Gate xor_gate_2 (.in_1(in_1[1]), .in_2(in_2[1]), .out_3(out_3[1]));
  XOR_Gate xor_gate_3 (.in_1(in_1[2]), .in_2(in_2[2]), .out_3(out_3[2]));
  XOR_Gate xor_gate_4 (.in_1(in_1[3]), .in_2(in_2[3]), .out_3(out_3[3]));
  XOR_Gate xor_gate_5 (.in_1(in_1[4]), .in_2(in_2[4]), .out_3(out_3[4]));
  XOR_Gate xor_gate_6 (.in_1(in_1[5]), .in_2(in_2[5]), .out_3(out_3[5]));
  XOR_Gate xor_gate_7 (.in_1(in_1[6]), .in_2(in_2[6]), .out_3(out_3[6]));
  XOR_Gate xor_gate_8 (.in_1(in_1[7]), .in_2(in_2[7]), .out_3(out_3[7]));
endmodule

module AND_Gate (
  input  in_1,
  input  in_2,
  output out_3
);

  wire nand_gate_1_out_3;

  NAND_Gate nand_gate_1 (.in_1(in_1), .in_2(in_2), .out_3(nand_gate_1_out_3));
  NOT_Gate not_gate_1 (.in_1(nand_gate_1_out_3), .out_2(out_3));
endmodule

module OR_Gate (
  input  in_1,
  input  in_2,
  output out_3
);

  wire nor_gate_1_out_3;

  NOR_Gate nor_gate_1 (.in_1(in_1), .in_2(in_2), .out_3(nor_gate_1_out_3));
  NOT_Gate not_gate_1 (.in_1(nor_gate_1_out_3), .out_2(out_3));
endmodule

module XNOR_Gate (
  input  in_1,
  input  in_2,
  output out_3
);

  wire xor_gate_1_out_3;

  XOR_Gate xor_gate_1 (.in_1(in_1), .in_2(in_2), .out_3(xor_gate_1_out_3));
  NOT_Gate not_gate_1 (.in_1(xor_gate_1_out_3), .out_2(out_3));
endmodule

module AND_Gate_3_input (
  input  in_1,
  input  in_2,
  input  in_3,
  input  in_4,
  input  in_5,
  input  in_6,
  output out_7,
  output out_8
);

  wire not_gate_1_out_2, pull_resistor_1_node, pull_resistor_2_node, pull_resistor_3_node, transistor_2_out,
       transistor_4_out, transistor_6_out, transistor_7_out;

  Pull_Resistor #(.pull(1)) pull_resistor_1 (.node(pull_resistor_1_node));
  Transistor #(.\type ("n")) transistor_1 (.in(transistor_2_out), .out(pull_resistor_1_node), .gate(in_2));
  Transistor #(.\type ("n")) transistor_2 (.in(1'b0), .out(transistor_2_out), .gate(in_3));
  NOT_Gate not_gate_1 (.in_1(pull_resistor_1_node), .out_2(not_gate_1_out_2));
  Pull_Resistor #(.pull(1)) pull_resistor_2 (.node(pull_resistor_2_node));
  Transistor #(.\type ("n")) transistor_3 (.in(transistor_4_out), .out(pull_resistor_2_node), .gate(in_1));
  Transistor #(.\type ("n")) transistor_4 (.in(1'b0), .out(transistor_4_out), .gate(not_gate_1_out_2));
  NOT_Gate not_gate_2 (.in_1(pull_resistor_2_node), .out_2(out_7));
  Pull_Resistor #(.pull(1)) pull_resistor_3 (.node(pull_resistor_3_node));
  Transistor #(.\type ("n")) transistor_5 (.in(transistor_6_out), .out(pull_resistor_3_node), .gate(in_4));
  Transistor #(.\type ("n")) transistor_6 (.in(transistor_7_out), .out(transistor_6_out), .gate(in_5));
  Transistor #(.\type ("n")) transistor_7 (.in(1'b0), .out(transistor_7_out), .gate(in_6));
  NOT_Gate not_gate_3 (.in_1(pull_resistor_3_node), .out_2(out_8));
endmodule

module Multi_input_OR_Gate (
  input  in_1,
  input  in_2,
  input  in_3,
  input  in_4,
  input  in_5,
  input  in_6,
  output out_7,
  output out_8
);

  wire not_gate_1_out_2, pull_resistor_1_node, pull_resistor_2_node, pull_resistor_3_node, transistor_2_out,
       transistor_4_out, transistor_6_out, transistor_7_out;

  Pull_Resistor pull_resistor_1 (.node(pull_resistor_1_node));
  Transistor transistor_1 (.in(transistor_2_out), .out(pull_resistor_1_node), .gate(in_2));
  Transistor transistor_2 (.in(1'b1), .out(transistor_2_out), .gate(in_3));
  NOT_Gate not_gate_1 (.in_1(pull_resistor_1_node), .out_2(not_gate_1_out_2));
  Pull_Resistor pull_resistor_2 (.node(pull_resistor_2_node));
  Transistor transistor_3 (.in(transistor_4_out), .out(pull_resistor_2_node), .gate(in_1));
  Transistor transistor_4 (.in(1'b1), .out(transistor_4_out), .gate(not_gate_1_out_2));
  NOT_Gate not_gate_2 (.in_1(pull_resistor_2_node), .out_2(out_7));
  Pull_Resistor pull_resistor_3 (.node(pull_resistor_3_node));
  Transistor transistor_5 (.in(transistor_6_out), .out(pull_resistor_3_node), .gate(in_4));
  Transistor transistor_6 (.in(transistor_7_out), .out(transistor_6_out), .gate(in_5));
  Transistor transistor_7 (.in(1'b1), .out(transistor_7_out), .gate(in_6));
  NOT_Gate not_gate_3 (.in_1(pull_resistor_3_node), .out_2(out_8));
endmodule

module Half_adder (
  input  in_1,
  input  in_2,
  output out_3
);

  XOR_Gate xor_gate_1 (.in_1(in_1), .in_2(in_2), .out_3(out_3));
endmodule

module ODD (
  input  in_1,
  input  in_2,
  input  CIN,
  output out_4
);

  wire and_gate_1_out_3, and_gate_2_out_3, not_gate_1_out_2, not_gate_2_out_2, xor_gate_1_out_3;

  XOR_Gate xor_gate_1 (.in_1(in_1), .in_2(in_2), .out_3(xor_gate_1_out_3));
  NOT_Gate not_gate_1 (.in_1(xor_gate_1_out_3), .out_2(not_gate_1_out_2));
  NOT_Gate not_gate_2 (.in_1(CIN), .out_2(not_gate_2_out_2));
  AND_Gate and_gate_1 (.in_1(not_gate_1_out_2), .in_2(CIN), .out_3(and_gate_1_out_3));
  AND_Gate and_gate_2 (.in_1(not_gate_2_out_2), .in_2(xor_gate_1_out_3), .out_3(and_gate_2_out_3));
  OR_Gate or_gate_1 (.in_1(and_gate_2_out_3), .in_2(and_gate_1_out_3), .out_3(out_4));
endmodule

module MAJ (
  input  in_1,
  input  in_2,
  input  CIN,
  output out_4
);

  wire and_gate_1_out_3, and_gate_2_out_3, or_gate_1_out_3;

  OR_Gate or_gate_1 (.in_1(in_1), .in_2(in_2), .out_3(or_gate_1_out_3));
  AND_Gate and_gate_1 (.in_1(in_1), .in_2(in_2), .out_3(and_gate_1_out_3));
  AND_Gate and_gate_2 (.in_1(or_gate_1_out_3), .in_2(CIN), .out_3(and_gate_2_out_3));
  OR_Gate or_gate_2 (.in_1(and_gate_2_out_3), .in_2(and_gate_1_out_3), .out_3(out_4));
endmodule

module Full_Adder_1bit (
  input  A,
  input  B,
  input  CIN,
  output SUM,
  output COUT
);

  MAJ maj_1 (.in_1(A), .in_2(B), .CIN(CIN), .out_4(COUT));
  ODD odd_1 (.in_1(A), .in_2(B), .CIN(CIN), .out_4(SUM));
  // Probe on {COUT, SUM}
endmodule

module Ripple_Carry_Adder_8bit (
  input  [7:0] A,
  input  [7:0] B,
  input  CIN,
  output [7:0] out_4,
  output out_5
);

  wire full_adder_1bit_1_cout, full_adder_1bit_2_cout, full_adder_1bit_3_cout, full_adder_1bit_4_cout,
       full_adder_1bit_5_cout, full_adder_1bit_6_cout, full_adder_1bit_7_cout;

  // Probe on B
  // Probe on A
  Full_Adder_1bit full_adder_1bit_1 (.A(A[0]), .B(B[0]), .CIN(CIN), .SUM(out_4[0]), .COUT(full_adder_1bit_1_cout));
  Full_Adder_1bit full_adder_1bit_2 (
    .A(A[1]), .B(B[1]), .CIN(full_adder_1bit_1_cout), .SUM(out_4[1]), .COUT(full_adder_1bit_2_cout));
  Full_Adder_1bit full_adder_1bit_3 (
    .A(A[2]), .B(B[2]), .CIN(full_adder_1bit_2_cout), .SUM(out_4[2]), .COUT(full_adder_1bit_3_cout));
  Full_Adder_1bit full_adder_1bit_4 (
    .A(A[3]), .B(B[3]), .CIN(full_adder_1bit_3_cout), .SUM(out_4[3]), .COUT(full_adder_1bit_4_cout));
  Full_Adder_1bit full_adder_1bit_5 (
    .A(A[4]), .B(B[4]), .CIN(full_adder_1bit_4_cout), .SUM(out_4[4]), .COUT(full_adder_1bit_5_cout));
  Full_Adder_1bit full_adder_1bit_6 (
    .A(A[5]), .B(B[5]), .CIN(full_adder_1bit_5_cout), .SUM(out_4[5]), .COUT(full_adder_1bit_6_cout));
  Full_Adder_1bit full_adder_1bit_7 (
    .A(A[6]), .B(B[6]), .CIN(full_adder_1bit_6_cout), .SUM(out_4[6]), .COUT(full_adder_1bit_7_cout));
  Full_Adder_1bit full_adder_1bit_8 (.A(A[7]), .B(B[7]), .CIN(full_adder_1bit_7_cout), .SUM(out_4[7]), .COUT(out_5));
  // Probe on {out_5, out_4}
endmodule

module ALU_8bit (
  input  [7:0] A,
  input  [7:0] B,
  input  S2,
  input  S1,
  input  S0,
  output [7:0] O
);

  wire de_coder_1__1, de_coder_1__2, de_coder_1__3, de_coder_1__4, de_coder_1__5, de_coder_1__6;
  wire [7:0] and_gate_8bit_1_out_3, left_bitshifter_1_out_3, right_bitshifter_1_out_3,
       ripple_carry_adder_8bit_1_out_4, substractor_8_bit_1_out_4, xor_gate_8bit_1_out_3;

  // Probe on A
  // Probe on B
  Ripple_Carry_Adder_8bit ripple_carry_adder_8bit_1 (
    .A(A), .B(B), .CIN(1'b0), .out_4(ripple_carry_adder_8bit_1_out_4));  // open: out_5
  XOR_Gate_8bit xor_gate_8bit_1 (.in_1(A), .in_2(B), .out_3(xor_gate_8bit_1_out_3));
  AND_Gate_8bit and_gate_8bit_1 (.in_1(A), .in_2(B), .out_3(and_gate_8bit_1_out_3));
  Substractor_8_bit substractor_8_bit_1 (.A(A), .B(B), .CIN(1'b0), .out_4(substractor_8_bit_1_out_4));  // open: out_5
  Right_bitshifter right_bitshifter_1 (.in_1(A), .in_2(B), .out_3(right_bitshifter_1_out_3));
  Left_bitshifter left_bitshifter_1 (.in_1(A), .in_2(B), .out_3(left_bitshifter_1_out_3));
  De_Coder de_coder_1 (
    .in_1(S2), .in_2(S1), .in_3(S0), ._1(de_coder_1__1), ._2(de_coder_1__2), ._3(de_coder_1__3),
    ._4(de_coder_1__4), ._5(de_coder_1__5), ._6(de_coder_1__6));  // open: _0, _7
  one_hot_mux_8bit one_hot_mux_8bit_1 (
    .ADD(ripple_carry_adder_8bit_1_out_4), .X(xor_gate_8bit_1_out_3), .AN(and_gate_8bit_1_out_3),
    .SUB(substractor_8_bit_1_out_4), .RS(right_bitshifter_1_out_3), .LS(left_bitshifter_1_out_3),
    .CADD(de_coder_1__1), .CX(de_coder_1__2), .CAN(de_coder_1__3), .CSUB(de_coder_1__4), .CRS(de_coder_1__5),
    .CLS(de_coder_1__6), .O(O));
  // Probe on O
endmodule

module one_hot_mux_1bit (
  input  A,
  input  B,
  input  C,
  input  C1,
  input  C2,
  input  C3,
  output O
);

  wire and_gate_1_out_3, and_gate_2_out_3, and_gate_3_out_3;

  AND_Gate and_gate_1 (.in_1(A), .in_2(C1), .out_3(and_gate_1_out_3));
  AND_Gate and_gate_2 (.in_1(B), .in_2(C2), .out_3(and_gate_2_out_3));
  AND_Gate and_gate_3 (.in_1(C), .in_2(C3), .out_3(and_gate_3_out_3));
  or or_1 (O, and_gate_1_out_3, and_gate_2_out_3, and_gate_3_out_3);
endmodule

module one_hot_mux_8bit (
  input  [7:0] ADD,
  input  [7:0] X,
  input  [7:0] AN,
  input  [7:0] SUB,
  input  [7:0] RS,
  input  [7:0] LS,
  input  CADD,
  input  CX,
  input  CAN,
  input  CSUB,
  input  CRS,
  input  CLS,
  output [7:0] O
);

  wire [7:0] and_gate_8bit_1_out_3, and_gate_8bit_2_out_3, and_gate_8bit_3_out_3, and_gate_8bit_4_out_3,
       and_gate_8bit_5_out_3, and_gate_8bit_6_out_3, or_1_out, or_2_out;

  AND_Gate_8bit and_gate_8bit_1 (.in_1(ADD), .in_2({8{CADD}}), .out_3(and_gate_8bit_1_out_3));
  AND_Gate_8bit and_gate_8bit_2 (.in_1(X), .in_2({8{CX}}), .out_3(and_gate_8bit_2_out_3));
  AND_Gate_8bit and_gate_8bit_3 (.in_1(AN), .in_2({8{CAN}}), .out_3(and_gate_8bit_3_out_3));
  AND_Gate_8bit and_gate_8bit_4 (.in_1(SUB), .in_2({8{CSUB}}), .out_3(and_gate_8bit_4_out_3));
  AND_Gate_8bit and_gate_8bit_5 (.in_1(RS), .in_2({8{CRS}}), .out_3(and_gate_8bit_5_out_3));
  AND_Gate_8bit and_gate_8bit_6 (.in_1(LS), .in_2({8{CLS}}), .out_3(and_gate_8bit_6_out_3));
  assign or_1_out = and_gate_8bit_1_out_3 | and_gate_8bit_2_out_3 | and_gate_8bit_3_out_3;  // OR_Gate_part or_1, 8 bits wide
  assign or_2_out = and_gate_8bit_4_out_3 | and_gate_8bit_5_out_3 | and_gate_8bit_6_out_3;  // OR_Gate_part or_2, 8 bits wide
  assign O = or_1_out | or_2_out;  // OR_Gate_part or_3, 8 bits wide
endmodule

module Full_Substractor (
  input  A,
  input  B,
  input  CIN,
  output SUM,
  output COUT
);

  wire and_1_out, and_2_out, not_1_out, not_2_out, xor_1_out;

  not not_1 (not_1_out, A);
  xor xor_1 (xor_1_out, A, B);
  not not_2 (not_2_out, xor_1_out);
  and and_1 (and_1_out, not_1_out, B);
  xor xor_2 (SUM, xor_1_out, CIN);
  and and_2 (and_2_out, not_2_out, CIN);
  or or_1 (COUT, and_1_out, and_2_out);
  // Probe on {COUT, SUM}
endmodule

module Substractor_8_bit (
  input  [7:0] A,
  input  [7:0] B,
  input  CIN,
  output [7:0] out_4,
  output out_5
);

  wire full_substractor_1_cout, full_substractor_2_cout, full_substractor_3_cout, full_substractor_4_cout,
       full_substractor_5_cout, full_substractor_6_cout, full_substractor_7_cout;

  // Probe on B
  // Probe on A
  Full_Substractor full_substractor_1 (.A(A[0]), .B(B[0]), .CIN(CIN), .SUM(out_4[0]), .COUT(full_substractor_1_cout));
  Full_Substractor full_substractor_2 (
    .A(A[1]), .B(B[1]), .CIN(full_substractor_1_cout), .SUM(out_4[1]), .COUT(full_substractor_2_cout));
  Full_Substractor full_substractor_3 (
    .A(A[2]), .B(B[2]), .CIN(full_substractor_2_cout), .SUM(out_4[2]), .COUT(full_substractor_3_cout));
  Full_Substractor full_substractor_4 (
    .A(A[3]), .B(B[3]), .CIN(full_substractor_3_cout), .SUM(out_4[3]), .COUT(full_substractor_4_cout));
  Full_Substractor full_substractor_5 (
    .A(A[4]), .B(B[4]), .CIN(full_substractor_4_cout), .SUM(out_4[4]), .COUT(full_substractor_5_cout));
  Full_Substractor full_substractor_6 (
    .A(A[5]), .B(B[5]), .CIN(full_substractor_5_cout), .SUM(out_4[5]), .COUT(full_substractor_6_cout));
  Full_Substractor full_substractor_7 (
    .A(A[6]), .B(B[6]), .CIN(full_substractor_6_cout), .SUM(out_4[6]), .COUT(full_substractor_7_cout));
  Full_Substractor full_substractor_8 (.A(A[7]), .B(B[7]), .CIN(full_substractor_7_cout), .SUM(out_4[7]), .COUT(out_5));
  // Probe on {out_5, out_4}
  // Probe on out_4
endmodule

module ALU_8bit_WOD (
  input  [7:0] A,
  input  [7:0] B,
  input  CADD,
  input  CX,
  input  CAN,
  input  CSUB,
  input  CRS,
  input  CLS,
  output [7:0] O
);

  wire [7:0] and_gate_8bit_1_out_3, left_bitshifter_1_out_3, right_bitshifter_1_out_3,
       ripple_carry_adder_8bit_1_out_4, substractor_8_bit_1_out_4, xor_gate_8bit_1_out_3;

  // Probe on A
  // Probe on B
  Ripple_Carry_Adder_8bit ripple_carry_adder_8bit_1 (
    .A(A), .B(B), .CIN(1'b0), .out_4(ripple_carry_adder_8bit_1_out_4));  // open: out_5
  XOR_Gate_8bit xor_gate_8bit_1 (.in_1(A), .in_2(B), .out_3(xor_gate_8bit_1_out_3));
  AND_Gate_8bit and_gate_8bit_1 (.in_1(A), .in_2(B), .out_3(and_gate_8bit_1_out_3));
  Substractor_8_bit substractor_8_bit_1 (.A(A), .B(B), .CIN(1'b0), .out_4(substractor_8_bit_1_out_4));  // open: out_5
  Right_bitshifter right_bitshifter_1 (.in_1(A), .in_2(B), .out_3(right_bitshifter_1_out_3));
  Left_bitshifter left_bitshifter_1 (.in_1(A), .in_2(B), .out_3(left_bitshifter_1_out_3));
  one_hot_mux_8bit one_hot_mux_8bit_1 (
    .ADD(ripple_carry_adder_8bit_1_out_4), .X(xor_gate_8bit_1_out_3), .AN(and_gate_8bit_1_out_3),
    .SUB(substractor_8_bit_1_out_4), .RS(right_bitshifter_1_out_3), .LS(left_bitshifter_1_out_3),
    .CADD(CADD), .CX(CX), .CAN(CAN), .CSUB(CSUB), .CRS(CRS), .CLS(CLS), .O(O));
  // Probe on O
endmodule

module MUX_2to1 (
  input  [7:0] Ai,
  input  [7:0] Bi,
  input  CA,
  input  CB,
  output [7:0] Oi
);

  wire [7:0] and_1_out, and_2_out;

  assign and_1_out = Ai & {8{CA}};  // AND_Gate_part and_1, 8 bits wide
  assign and_2_out = {8{CB}} & Bi;  // AND_Gate_part and_2, 8 bits wide
  assign Oi = and_1_out | and_2_out;  // OR_Gate_part or_1, 8 bits wide
endmodule

module Flip_Flop (
  input  in_1,
  input  in_2,
  output out_3,
  output out_4
);

  wire clock_1_out, nand_1_out, nand_2_out;

  Clock clock_1 (.out(clock_1_out));
  nand nand_1 (nand_1_out, in_1, clock_1_out);
  nand nand_2 (nand_2_out, clock_1_out, in_2);
  nand nand_3 (out_3, nand_1_out, out_4);
  nand nand_4 (out_4, out_3, nand_2_out);
endmodule

module D_flip_flop (
  input  in_1,
  input  in_2,
  output out_3,
  output out_4
);

  wire nand_1_out, nand_2_out, not_1_out;

  not not_1 (not_1_out, in_1);
  nand nand_1 (nand_1_out, in_1, in_2);
  nand nand_2 (nand_2_out, in_2, not_1_out);
  nand nand_3 (out_3, nand_1_out, out_4);
  nand nand_4 (out_4, out_3, nand_2_out);
endmodule

module Control_Unit_Sequencer (
  input  RUN,
  input  HALT,
  output fetch,
  output fetchwrite,
  output execute,
  output Executewrite
);

  wire and_1_out, and_2_out, and_3_out, and_5_out, clock_1_out, d_ff_1_q, d_ff_1_qn, d_ff_2_q, d_ff_3_q,
       not_1_out, pull_resistor_1_node;

  Clock clock_1 (.out(clock_1_out));
  not not_1 (not_1_out, HALT);
  Pull_Resistor pull_resistor_1 (.node(pull_resistor_1_node));
  assign pull_resistor_1_node = not_1_out ? RUN : 1'bz;  // Controlled_Buffer controlled_buffer_1
  and and_1 (and_1_out, pull_resistor_1_node, clock_1_out);
  and and_2 (and_2_out, and_1_out, not_1_out);
  D_Flip_Flop d_ff_1 (.D(d_ff_1_qn), .clk(and_2_out), .Q(d_ff_1_q), .Qn(d_ff_1_qn));  // open: preset, reset
  D_Flip_Flop d_ff_2 (.D(d_ff_1_qn), .clk(and_2_out), .Q(d_ff_2_q));  // open: Qn, preset, reset
  D_Flip_Flop d_ff_3 (.D(d_ff_1_q), .clk(and_2_out), .Q(d_ff_3_q));  // open: Qn, preset, reset
  and and_3 (and_3_out, ~Executewrite, d_ff_1_qn);  // AND_Gate_part
  and and_4 (fetchwrite, d_ff_2_q, and_2_out);
  and and_5 (and_5_out, ~fetchwrite, d_ff_1_q);  // AND_Gate_part
  and and_6 (Executewrite, d_ff_3_q, and_2_out);
  or or_1 (fetch, and_3_out, fetchwrite);
  or or_2 (execute, and_5_out, Executewrite);
endmodule

module memory_cell (
  input  Din,
  input  WE,
  input  clock,
  input  Reset,
  output Dout
);

  wire and_1_out, and_2_out, not_1_out, or_1_out;

  not not_1 (not_1_out, WE);
  and and_1 (and_1_out, Din, WE);
  and and_2 (and_2_out, Dout, not_1_out);
  or or_1 (or_1_out, and_1_out, and_2_out);
  D_Flip_Flop d_ff_1 (.D(or_1_out), .clk(clock), .Q(Dout), .reset(Reset));  // open: Qn, preset
endmodule

module Controled_Buffer (
  input  in_1,
  input  in_2,
  output out_3
);

  wire not_1_out;

  not not_1 (not_1_out, in_1);
  Transistor #(.\type ("n")) transistor_1 (.in(in_2), .out(out_3), .gate(in_1));
  Transistor transistor_2 (.in(in_2), .out(out_3), .gate(not_1_out));
endmodule

module register_8bit (
  input  [7:0] D,
  input  WE,
  input  in_3,
  input  R,
  output [7:0] Q
);

  memory_cell memory_cell_1 (.Din(D[0]), .WE(WE), .clock(in_3), .Reset(R), .Dout(Q[0]));
  memory_cell memory_cell_2 (.Din(D[1]), .WE(WE), .clock(in_3), .Reset(R), .Dout(Q[1]));
  memory_cell memory_cell_3 (.Din(D[2]), .WE(WE), .clock(in_3), .Reset(R), .Dout(Q[2]));
  memory_cell memory_cell_4 (.Din(D[3]), .WE(WE), .clock(in_3), .Reset(R), .Dout(Q[3]));
  memory_cell memory_cell_5 (.Din(D[4]), .WE(WE), .clock(in_3), .Reset(R), .Dout(Q[4]));
  memory_cell memory_cell_6 (.Din(D[5]), .WE(WE), .clock(in_3), .Reset(R), .Dout(Q[5]));
  memory_cell memory_cell_7 (.Din(D[6]), .WE(WE), .clock(in_3), .Reset(R), .Dout(Q[6]));
  memory_cell memory_cell_8 (.Din(D[7]), .WE(WE), .clock(in_3), .Reset(R), .Dout(Q[7]));
endmodule

module register_4bit (
  input  [3:0] D,
  input  WE,
  input  R,
  output [3:0] Q
);

  wire clock_1_out;

  Clock clock_1 (.out(clock_1_out));
  memory_cell memory_cell_1 (.Din(D[0]), .WE(WE), .clock(clock_1_out), .Reset(R), .Dout(Q[0]));
  memory_cell memory_cell_2 (.Din(D[1]), .WE(WE), .clock(clock_1_out), .Reset(R), .Dout(Q[1]));
  memory_cell memory_cell_3 (.Din(D[2]), .WE(WE), .clock(clock_1_out), .Reset(R), .Dout(Q[2]));
  memory_cell memory_cell_4 (.Din(D[3]), .WE(WE), .clock(clock_1_out), .Reset(R), .Dout(Q[3]));
endmodule

module register_16bits (
  input  [15:0] D,
  input  WE,
  input  CLK,
  input  R,
  output [15:0] Q
);

  register_8bit register_8bit_1 (.D(D[7:0]), .WE(WE), .in_3(CLK), .R(R), .Q(Q[7:0]));
  register_8bit register_8bit_2 (.D(D[15:8]), .WE(WE), .in_3(CLK), .R(R), .Q(Q[15:8]));
endmodule

module Memory_bank_16x16_bits (
  input  [15:0] D,
  input  [3:0] A,
  input  WE,
  input  OE,
  input  CLK,
  input  R,
  output [15:0] out_7
);

  wire and_1_out, and_2_out, and_3_out, and_4_out, and_5_out, and_6_out, and_7_out, and_8_out, and_9_out,
       and_10_out, and_11_out, and_12_out, and_13_out, and_14_out, and_15_out, and_16_out,
       de_coder_de_mux_16bits_1_c1, de_coder_de_mux_16bits_1_c2, de_coder_de_mux_16bits_1_c3,
       de_coder_de_mux_16bits_1_c4, de_coder_de_mux_16bits_1_c5, de_coder_de_mux_16bits_1_c6,
       de_coder_de_mux_16bits_1_c7, de_coder_de_mux_16bits_1_c8, de_coder_de_mux_16bits_1_c9,
       de_coder_de_mux_16bits_1_c10, de_coder_de_mux_16bits_1_c11, de_coder_de_mux_16bits_1_c12,
       de_coder_de_mux_16bits_1_c13, de_coder_de_mux_16bits_1_c14, de_coder_de_mux_16bits_1_c15,
       de_coder_de_mux_16bits_1_c16;
  wire [15:0] de_coder_de_mux_16bits_1__2, de_coder_de_mux_16bits_1__3, de_coder_de_mux_16bits_1__4,
       de_coder_de_mux_16bits_1__5, de_coder_de_mux_16bits_1__6, de_coder_de_mux_16bits_1__7,
       de_coder_de_mux_16bits_1_a_2, de_coder_de_mux_16bits_1_b, de_coder_de_mux_16bits_1_c,
       de_coder_de_mux_16bits_1_d_2, de_coder_de_mux_16bits_1_e, de_coder_de_mux_16bits_1_f,
       de_coder_de_mux_16bits_1_out_3, de_coder_de_mux_16bits_1_out_5, de_coder_de_mux_16bits_1_out_19,
       de_coder_de_mux_16bits_1_out_21, mux_4_bits_1_out_18, register_16bits_1_q, register_16bits_2_q,
       register_16bits_3_q, register_16bits_4_q, register_16bits_5_q, register_16bits_6_q,
       register_16bits_7_q, register_16bits_8_q, register_16bits_9_q, register_16bits_10_q,
       register_16bits_11_q, register_16bits_12_q, register_16bits_13_q, register_16bits_14_q,
       register_16bits_15_q, register_16bits_16_q;

  DE_coder_De_mux_16bits de_coder_de_mux_16bits_1 (
    .D(D), .A(A), .out_3(de_coder_de_mux_16bits_1_out_3), .C1(de_coder_de_mux_16bits_1_c1),
    .out_5(de_coder_de_mux_16bits_1_out_5), .C2(de_coder_de_mux_16bits_1_c2),
    ._2(de_coder_de_mux_16bits_1__2), .C3(de_coder_de_mux_16bits_1_c3), ._3(de_coder_de_mux_16bits_1__3),
    .C4(de_coder_de_mux_16bits_1_c4), ._4(de_coder_de_mux_16bits_1__4), .C5(de_coder_de_mux_16bits_1_c5),
    ._5(de_coder_de_mux_16bits_1__5), .C6(de_coder_de_mux_16bits_1_c6), ._6(de_coder_de_mux_16bits_1__6),
    .C7(de_coder_de_mux_16bits_1_c7), ._7(de_coder_de_mux_16bits_1__7), .C8(de_coder_de_mux_16bits_1_c8),
    .out_19(de_coder_de_mux_16bits_1_out_19), .C9(de_coder_de_mux_16bits_1_c9),
    .out_21(de_coder_de_mux_16bits_1_out_21), .C10(de_coder_de_mux_16bits_1_c10),
    .a_2(de_coder_de_mux_16bits_1_a_2), .C11(de_coder_de_mux_16bits_1_c11), .b(de_coder_de_mux_16bits_1_b),
    .C12(de_coder_de_mux_16bits_1_c12), .c(de_coder_de_mux_16bits_1_c), .C13(de_coder_de_mux_16bits_1_c13),
    .d_2(de_coder_de_mux_16bits_1_d_2), .C14(de_coder_de_mux_16bits_1_c14), .e(de_coder_de_mux_16bits_1_e),
    .C15(de_coder_de_mux_16bits_1_c15), .f(de_coder_de_mux_16bits_1_f), .C16(de_coder_de_mux_16bits_1_c16));
  and and_1 (and_1_out, de_coder_de_mux_16bits_1_c1, WE);
  buf and_2 (and_2_out, de_coder_de_mux_16bits_1_c5);  // AND_Gate_part
  and and_3 (and_3_out, de_coder_de_mux_16bits_1_c9, WE);
  and and_4 (and_4_out, de_coder_de_mux_16bits_1_c13, WE);
  register_16bits register_16bits_1 (
    .D(de_coder_de_mux_16bits_1_out_3), .WE(and_1_out), .CLK(CLK), .R(R), .Q(register_16bits_1_q));
  register_16bits register_16bits_2 (
    .D(de_coder_de_mux_16bits_1__4), .WE(and_2_out), .CLK(CLK), .R(R), .Q(register_16bits_2_q));
  register_16bits register_16bits_3 (
    .D(de_coder_de_mux_16bits_1_out_19), .WE(and_3_out), .CLK(CLK), .R(R), .Q(register_16bits_3_q));
  register_16bits register_16bits_4 (
    .D(de_coder_de_mux_16bits_1_c), .WE(and_4_out), .CLK(CLK), .R(R), .Q(register_16bits_4_q));
  and and_5 (and_5_out, de_coder_de_mux_16bits_1_c2, WE);
  and and_6 (and_6_out, de_coder_de_mux_16bits_1_c6, WE);
  and and_7 (and_7_out, de_coder_de_mux_16bits_1_c10, WE);
  and and_8 (and_8_out, de_coder_de_mux_16bits_1_c14, WE);
  register_16bits register_16bits_5 (
    .D(de_coder_de_mux_16bits_1_out_5), .WE(and_5_out), .CLK(CLK), .R(R), .Q(register_16bits_5_q));
  register_16bits register_16bits_6 (
    .D(de_coder_de_mux_16bits_1__5), .WE(and_6_out), .CLK(CLK), .R(R), .Q(register_16bits_6_q));
  register_16bits register_16bits_7 (
    .D(de_coder_de_mux_16bits_1_out_21), .WE(and_7_out), .CLK(CLK), .R(R), .Q(register_16bits_7_q));
  register_16bits register_16bits_8 (
    .D(de_coder_de_mux_16bits_1_d_2), .WE(and_8_out), .CLK(CLK), .R(R), .Q(register_16bits_8_q));
  and and_9 (and_9_out, de_coder_de_mux_16bits_1_c3, WE);
  and and_10 (and_10_out, de_coder_de_mux_16bits_1_c7, WE);
  and and_11 (and_11_out, de_coder_de_mux_16bits_1_c11, WE);
  and and_12 (and_12_out, de_coder_de_mux_16bits_1_c15, WE);
  register_16bits register_16bits_9 (
    .D(de_coder_de_mux_16bits_1__2), .WE(and_9_out), .CLK(CLK), .R(R), .Q(register_16bits_9_q));
  register_16bits register_16bits_10 (
    .D(de_coder_de_mux_16bits_1__6), .WE(and_10_out), .CLK(CLK), .R(R), .Q(register_16bits_10_q));
  register_16bits register_16bits_11 (
    .D(de_coder_de_mux_16bits_1_a_2), .WE(and_11_out), .CLK(CLK), .R(R), .Q(register_16bits_11_q));
  register_16bits register_16bits_12 (
    .D(de_coder_de_mux_16bits_1_e), .WE(and_12_out), .CLK(CLK), .R(R), .Q(register_16bits_12_q));
  and and_13 (and_13_out, de_coder_de_mux_16bits_1_c4, WE);
  and and_14 (and_14_out, de_coder_de_mux_16bits_1_c8, WE);
  and and_15 (and_15_out, de_coder_de_mux_16bits_1_c12, WE);
  and and_16 (and_16_out, de_coder_de_mux_16bits_1_c16, WE);
  register_16bits register_16bits_13 (
    .D(de_coder_de_mux_16bits_1__3), .WE(and_13_out), .CLK(CLK), .R(R), .Q(register_16bits_13_q));
  register_16bits register_16bits_14 (
    .D(de_coder_de_mux_16bits_1__7), .WE(and_14_out), .CLK(CLK), .R(R), .Q(register_16bits_14_q));
  register_16bits register_16bits_15 (
    .D(de_coder_de_mux_16bits_1_b), .WE(and_15_out), .CLK(CLK), .R(R), .Q(register_16bits_15_q));
  register_16bits register_16bits_16 (
    .D(de_coder_de_mux_16bits_1_f), .WE(and_16_out), .CLK(CLK), .R(R), .Q(register_16bits_16_q));
  mux_4_bits mux_4_bits_1 (
    .A(A), .in_2(register_16bits_1_q), .in_3(register_16bits_5_q), .in_4(register_16bits_9_q),
    .in_5(register_16bits_13_q), .in_6(register_16bits_2_q), .in_7(register_16bits_6_q),
    .in_8(register_16bits_10_q), .in_9(register_16bits_14_q), .in_10(register_16bits_3_q),
    .in_11(register_16bits_7_q), .in_12(register_16bits_11_q), .in_13(register_16bits_15_q),
    .in_14(register_16bits_4_q), .in_15(register_16bits_8_q), .in_16(register_16bits_12_q),
    .in_17(register_16bits_16_q), .out_18(mux_4_bits_1_out_18));
  assign out_7 = OE ? mux_4_bits_1_out_18 : 16'bz;  // Controlled_Buffer controlled_buffer_1
  Pull_Resistor pull_resistor_1 (.node(out_7));
endmodule

module DE_coder_De_mux_16bits (
  input  [15:0] D,
  input  [3:0] A,
  output [15:0] out_3,
  output C1,
  output [15:0] out_5,
  output C2,
  output [15:0] _2,
  output C3,
  output [15:0] _3,
  output C4,
  output [15:0] _4,
  output C5,
  output [15:0] _5,
  output C6,
  output [15:0] _6,
  output C7,
  output [15:0] _7,
  output C8,
  output [15:0] out_19,
  output C9,
  output [15:0] out_21,
  output C10,
  output [15:0] a_2,
  output C11,
  output [15:0] b,
  output C12,
  output [15:0] c,
  output C13,
  output [15:0] d_2,
  output C14,
  output [15:0] e,
  output C15,
  output [15:0] f,
  output C16
);

  // Probe on A
  and and_1 (C2, A[0], ~A[1], ~A[2], ~A[3]);  // AND_Gate_part
  and and_2 (C3, ~A[0], A[1], ~A[2], ~A[3]);  // AND_Gate_part
  and and_3 (C4, A[0], A[1], ~A[2], ~A[3]);  // AND_Gate_part
  and and_4 (C5, ~A[0], ~A[1], A[2], ~A[3]);  // AND_Gate_part
  and and_5 (C6, A[0], ~A[1], A[2], ~A[3]);  // AND_Gate_part
  and and_6 (C7, ~A[0], A[1], A[2], ~A[3]);  // AND_Gate_part
  and and_7 (C8, A[0], A[1], A[2], ~A[3]);  // AND_Gate_part
  and and_8 (C9, ~A[0], ~A[1], ~A[2], A[3]);  // AND_Gate_part
  and and_9 (C10, A[0], ~A[1], ~A[2], A[3]);  // AND_Gate_part
  and and_10 (C11, ~A[0], A[1], ~A[2], A[3]);  // AND_Gate_part
  and and_11 (C12, A[0], A[1], ~A[2], A[3]);  // AND_Gate_part
  and and_12 (C13, ~A[0], ~A[1], A[2], A[3]);  // AND_Gate_part
  and and_13 (C14, A[0], ~A[1], A[2], A[3]);  // AND_Gate_part
  and and_14 (C15, ~A[0], A[1], A[2], A[3]);  // AND_Gate_part
  and and_15 (C16, A[0], A[1], A[2], A[3]);
  Pull_Resistor pull_resistor_1 (.node(out_3));
  assign out_3 = C1 ? D : 16'bz;  // Controlled_Buffer controlled_buffer_1
  nor nor_1 (C1, A[0], A[1], A[2], A[3]);
  Pull_Resistor pull_resistor_2 (.node(out_5));
  assign out_5 = C2 ? D : 16'bz;  // Controlled_Buffer controlled_buffer_2
  Pull_Resistor pull_resistor_3 (.node(_2));
  assign _2 = C3 ? D : 16'bz;  // Controlled_Buffer controlled_buffer_3
  Pull_Resistor pull_resistor_4 (.node(_3));
  assign _3 = C4 ? D : 16'bz;  // Controlled_Buffer controlled_buffer_4
  Pull_Resistor pull_resistor_5 (.node(_4));
  assign _4 = C5 ? D : 16'bz;  // Controlled_Buffer controlled_buffer_5
  Pull_Resistor pull_resistor_6 (.node(_5));
  assign _5 = C6 ? D : 16'bz;  // Controlled_Buffer controlled_buffer_6
  Pull_Resistor pull_resistor_7 (.node(_6));
  assign _6 = C7 ? D : 16'bz;  // Controlled_Buffer controlled_buffer_7
  Pull_Resistor pull_resistor_8 (.node(_7));
  assign _7 = C8 ? D : 16'bz;  // Controlled_Buffer controlled_buffer_8
  Pull_Resistor pull_resistor_9 (.node(out_19));
  assign out_19 = C9 ? D : 16'bz;  // Controlled_Buffer controlled_buffer_9
  Pull_Resistor pull_resistor_10 (.node(out_21));
  assign out_21 = C10 ? D : 16'bz;  // Controlled_Buffer controlled_buffer_10
  Pull_Resistor pull_resistor_11 (.node(a_2));
  assign a_2 = C11 ? D : 16'bz;  // Controlled_Buffer controlled_buffer_11
  Pull_Resistor pull_resistor_12 (.node(b));
  assign b = C12 ? D : 16'bz;  // Controlled_Buffer controlled_buffer_12
  Pull_Resistor pull_resistor_13 (.node(c));
  assign c = C13 ? D : 16'bz;  // Controlled_Buffer controlled_buffer_13
  Pull_Resistor pull_resistor_14 (.node(d_2));
  assign d_2 = C14 ? D : 16'bz;  // Controlled_Buffer controlled_buffer_14
  Pull_Resistor pull_resistor_15 (.node(e));
  assign e = C15 ? D : 16'bz;  // Controlled_Buffer controlled_buffer_15
  Pull_Resistor pull_resistor_16 (.node(f));
  assign f = C16 ? D : 16'bz;  // Controlled_Buffer controlled_buffer_16

  // Notes on the sheet:
  //   0
  //   1
  //   8
  //   9
endmodule

module PC (
  input  [7:0] D,
  input  Increment,
  input  Load,
  input  CLK,
  input  R,
  output [7:0] Q
);

  wire or_1_out;
  wire [7:0] incrementer_1_out_2, mux_2to1_1_oi;

  or or_1 (or_1_out, Increment, Load);
  INCREMENTER incrementer_1 (.in_1(Q), .out_2(incrementer_1_out_2));
  MUX_2to1 mux_2to1_1 (.Ai(incrementer_1_out_2), .Bi(D), .CA(Increment), .CB(Load), .Oi(mux_2to1_1_oi));
  register_8bit register_8bit_1 (.D(mux_2to1_1_oi), .WE(or_1_out), .in_3(CLK), .R(R), .Q(Q));
endmodule

module INCREMENTER (
  input  [7:0] in_1,
  output [7:0] out_2
);

  Ripple_Carry_Adder_8bit ripple_carry_adder_8bit_1 (.A(in_1), .B(8'h1), .CIN(1'b0), .out_4(out_2));  // open: out_5
endmodule

module mux_4_bits (
  input  [3:0] A,
  input  [15:0] in_2,
  input  [15:0] in_3,
  input  [15:0] in_4,
  input  [15:0] in_5,
  input  [15:0] in_6,
  input  [15:0] in_7,
  input  [15:0] in_8,
  input  [15:0] in_9,
  input  [15:0] in_10,
  input  [15:0] in_11,
  input  [15:0] in_12,
  input  [15:0] in_13,
  input  [15:0] in_14,
  input  [15:0] in_15,
  input  [15:0] in_16,
  input  [15:0] in_17,
  output [15:0] out_18
);

  wire and_1_out, and_2_out, and_3_out, and_4_out, and_5_out, and_6_out, and_7_out, and_8_out, and_9_out,
       and_10_out, and_11_out, and_12_out, and_13_out, and_14_out, and_15_out, nor_1_out;

  // Probe on A
  and and_1 (and_1_out, A[0], ~A[1], ~A[2], ~A[3]);  // AND_Gate_part
  and and_2 (and_2_out, ~A[0], A[1], ~A[2], ~A[3]);  // AND_Gate_part
  and and_3 (and_3_out, A[0], A[1], ~A[2], ~A[3]);  // AND_Gate_part
  and and_4 (and_4_out, ~A[0], ~A[1], A[2], ~A[3]);  // AND_Gate_part
  and and_5 (and_5_out, A[0], ~A[1], A[2], ~A[3]);  // AND_Gate_part
  and and_6 (and_6_out, ~A[0], A[1], A[2], ~A[3]);  // AND_Gate_part
  and and_7 (and_7_out, A[0], A[1], A[2], ~A[3]);  // AND_Gate_part
  and and_8 (and_8_out, ~A[0], ~A[1], ~A[2], A[3]);  // AND_Gate_part
  and and_9 (and_9_out, A[0], ~A[1], ~A[2], A[3]);  // AND_Gate_part
  and and_10 (and_10_out, ~A[0], A[1], ~A[2], A[3]);  // AND_Gate_part
  and and_11 (and_11_out, A[0], A[1], ~A[2], A[3]);  // AND_Gate_part
  and and_12 (and_12_out, ~A[0], ~A[1], A[2], A[3]);  // AND_Gate_part
  and and_13 (and_13_out, A[0], ~A[1], A[2], A[3]);  // AND_Gate_part
  and and_14 (and_14_out, ~A[0], A[1], A[2], A[3]);  // AND_Gate_part
  and and_15 (and_15_out, A[0], A[1], A[2], A[3]);
  nor nor_1 (nor_1_out, A[0], A[1], A[2], A[3]);
  assign out_18 = nor_1_out ? in_2 : 16'bz;  // Controlled_Buffer controlled_buffer_1
  assign out_18 = and_1_out ? in_3 : 16'bz;  // Controlled_Buffer controlled_buffer_2
  assign out_18 = and_2_out ? in_4 : 16'bz;  // Controlled_Buffer controlled_buffer_3
  assign out_18 = and_3_out ? in_5 : 16'bz;  // Controlled_Buffer controlled_buffer_4
  assign out_18 = and_4_out ? in_6 : 16'bz;  // Controlled_Buffer controlled_buffer_5
  assign out_18 = and_5_out ? in_7 : 16'bz;  // Controlled_Buffer controlled_buffer_6
  assign out_18 = and_6_out ? in_8 : 16'bz;  // Controlled_Buffer controlled_buffer_7
  assign out_18 = and_7_out ? in_9 : 16'bz;  // Controlled_Buffer controlled_buffer_8
  assign out_18 = and_8_out ? in_10 : 16'bz;  // Controlled_Buffer controlled_buffer_9
  assign out_18 = and_9_out ? in_11 : 16'bz;  // Controlled_Buffer controlled_buffer_10
  assign out_18 = and_10_out ? in_12 : 16'bz;  // Controlled_Buffer controlled_buffer_11
  assign out_18 = and_11_out ? in_13 : 16'bz;  // Controlled_Buffer controlled_buffer_12
  assign out_18 = and_12_out ? in_14 : 16'bz;  // Controlled_Buffer controlled_buffer_13
  assign out_18 = and_13_out ? in_15 : 16'bz;  // Controlled_Buffer controlled_buffer_14
  assign out_18 = and_14_out ? in_16 : 16'bz;  // Controlled_Buffer controlled_buffer_15
  assign out_18 = and_15_out ? in_17 : 16'bz;  // Controlled_Buffer controlled_buffer_16
endmodule

module main (
);

  ALU_8bit_WOD alu_8bit_wod_1 ();  // open: A, B, CADD, CX, CAN, CSUB, CRS, CLS, O
  R_mux r_mux_1 ();  // open: Ai, Bi, Ci, CA, CB, CC, Oi
  register_8bit register_8bit_1 ();  // open: D, WE, in_3, R, Q
  register_8bit register_8bit_2 ();  // open: D, WE, in_3, R, Q
  PC pc_1 ();  // open: D, Increment, Load, CLK, R, Q
  MUX_2to1 mux_2to1_1 ();  // open: Ai, Bi, CA, CB, Oi
  Memory_bank_16x16_bits memory_bank_16x16_bits_1 ();  // open: D, A, WE, OE, CLK, R, out_7
endmodule

module R_mux (
  input  [7:0] Ai,
  input  [7:0] Bi,
  input  [7:0] Ci,
  input  CA,
  input  CB,
  input  CC,
  output [7:0] Oi
);

  wire [7:0] and_1_out, and_2_out, and_3_out;

  assign and_1_out = Ai & {8{CA}};  // AND_Gate_part and_1, 8 bits wide
  assign and_2_out = {8{CB}} & Bi;  // AND_Gate_part and_2, 8 bits wide
  assign and_3_out = {8{CC}} & Ci;  // AND_Gate_part and_3, 8 bits wide
  assign Oi = and_1_out | and_3_out | and_2_out;  // OR_Gate_part or_1, 8 bits wide
endmodule

module CPU_16bits (
  input  Stepback,
  input  START,
  input  [7:0] ADDR_in,
  input  [15:0] Data_in,
  input  load,
  input  Step,
  input  look,
  output A0,
  output A1,
  output D0,
  output A2,
  output D1,
  output A3,
  output D2,
  output A4,
  output D3,
  output A5,
  output D4,
  output A6,
  output D5,
  output A7,
  output D6,
  output D7,
  output D8,
  output D9,
  output Da,
  output Db,
  output Dc,
  output Dd,
  output De,
  output Df,
  output [3:0] STD_out1,
  output [3:0] STD_out2,
  output [3:0] STD_out3,
  output [3:0] STD_out4
);

  wire and_1_out, and_2_out, and_3_out, comparator_1_eq, comparator_2_eq, comparator_3_eq, control_1_a_mux_c,
       control_1_bank_clk, control_1_bank_we, control_1_cadd, control_1_can, control_1_cct, control_1_cls,
       control_1_crs, control_1_csub, control_1_cx, control_1_halt, control_1_load, control_1_oe_s,
       control_1_oe_t, control_1_r_we, control_1_ram_oe, control_1_ram_we, control_1_run,
       control_unit_sequencer_1_execute, control_unit_sequencer_1_executewrite,
       control_unit_sequencer_1_fetch, control_unit_sequencer_1_fetchwrite, not_1_out, not_2_out, not_3_out,
       not_4_out, not_5_out, or_1_out, or_2_out, or_3_out, or_4_out, or_5_out, or_6_out;
  wire [3:0] control_1_aoutput_s, control_1_aoutput_t, control_1_awrite;
  wire [7:0] control_1_a_mux, control_1_cd, controlled_buffer_2_out, counter_1_q, multiplexer_1_out;
  wire [15:0] alu_16bits_1_o, bank_16registers_1_output_s, bank_16registers_1_output_t, control_1_a,
       control_1_b, control_1_ram_input, control_1_write, controlled_buffer_1_out, ram_1_dout, register_1_q,
       register_2_q;

  bank_16Registers bank_16registers_1 (
    .WRITE(control_1_write), .AWRITE(control_1_awrite), .WE(control_1_bank_we),
    .AOUTPUT_S(control_1_aoutput_s), .OE_S(control_1_oe_s), .AOUTPUT_t(control_1_aoutput_t),
    .OE_t(control_1_oe_t), .CLK(control_1_bank_clk), .OUTPUT_S(bank_16registers_1_output_s),
    .OUTPUT_t(bank_16registers_1_output_t));  // open: R
  ALU_16bits alu_16bits_1 (
    .A(control_1_a), .B(control_1_b), .CADD(control_1_cadd), .CX(control_1_cx), .CAN(control_1_can),
    .CSUB(control_1_csub), .CRS(control_1_crs), .CLS(control_1_cls), .O(alu_16bits_1_o));
  Register #(.trigger("falling"), .width(16)) register_1 (
    .D(ram_1_dout), .en(control_1_r_we), .clk(control_1_bank_clk), .Q(register_1_q));  // open: clr
  Control_Unit_Sequencer control_unit_sequencer_1 (
    .RUN(control_1_run), .HALT(control_1_halt), .fetch(control_unit_sequencer_1_fetch),
    .fetchwrite(control_unit_sequencer_1_fetchwrite), .execute(control_unit_sequencer_1_execute),
    .Executewrite(control_unit_sequencer_1_executewrite));
  CONTROL control_1 (
    .START(START), .fetch(control_unit_sequencer_1_fetch), .fetchwrite(control_unit_sequencer_1_fetchwrite),
    .execute(control_unit_sequencer_1_execute), .executewrite(control_unit_sequencer_1_executewrite),
    .OUTPUT_S(bank_16registers_1_output_s), .O(alu_16bits_1_o), .OUTPUT_t(bank_16registers_1_output_t),
    .CQ(counter_1_q), .Ram_OUTPUT(ram_1_dout), .R_Q(register_1_q), .RUN(control_1_run),
    .HALT(control_1_halt), .WRITE(control_1_write), .A(control_1_a), .AWRITE(control_1_awrite),
    .B(control_1_b), .bank_WE(control_1_bank_we), .CADD(control_1_cadd), .AOUTPUT_S(control_1_aoutput_s),
    .CX(control_1_cx), .OE_S(control_1_oe_s), .CAN(control_1_can), .AOUTPUT_t(control_1_aoutput_t),
    .CSUB(control_1_csub), .LOAD(control_1_load), .OE_t(control_1_oe_t), .CRS(control_1_crs),
    .CD(control_1_cd), .CCT(control_1_cct), .bank_clk(control_1_bank_clk), .CLS(control_1_cls),
    .RAM_WE(control_1_ram_we), .RAM_OE(control_1_ram_oe), .RAM_INPUT(control_1_ram_input),
    .A_MUX_C(control_1_a_mux_c), .A_MUX(control_1_a_mux), .R_WE(control_1_r_we));
  assign controlled_buffer_1_out = not_2_out ? control_1_ram_input : 16'bz;  // Controlled_Buffer controlled_buffer_1
  assign controlled_buffer_2_out = not_1_out ? control_1_a_mux : 8'bz;  // Controlled_Buffer controlled_buffer_2
  or or_1 (or_1_out, control_1_cct, Step);
  Counter #(.trigger("falling")) counter_1 (
    .load(control_1_load), .D(control_1_cd), .count(or_1_out), .Q(counter_1_q), .up(not_3_out),
    .clk(control_1_bank_clk));  // open: carry, clr
  or or_2 (or_2_out, control_1_ram_we, load);
  not not_1 (not_1_out, or_3_out);
  RAM #(.asyncread("true"), .dataWidth(16), .\type ("nonvolatile")) ram_1 (
    .addr(multiplexer_1_out), .we(or_2_out), .oe(control_1_ram_oe), .clk(control_1_bank_clk),
    .din(controlled_buffer_1_out), .dout(ram_1_dout));
  Multiplexer #(.width(8)) multiplexer_1 (
    .in0(counter_1_q), .in1(controlled_buffer_2_out), .out(multiplexer_1_out), .sel(or_4_out));
  assign controlled_buffer_1_out = load ? Data_in : 16'bz;  // Controlled_Buffer controlled_buffer_3
  or or_3 (or_3_out, load, look);
  not not_2 (not_2_out, load);
  assign controlled_buffer_2_out = or_3_out ? ADDR_in : 8'bz;  // Controlled_Buffer controlled_buffer_4
  or or_4 (or_4_out, load, look, control_1_a_mux_c);
  not not_3 (not_3_out, Stepback);
  Comparator #(.width(16)) comparator_1 (.a(register_1_q), .b({16{1'b0}}), .eq(comparator_1_eq));  // open: gt, lt
  Comparator comparator_2 (.a(register_1_q[7:0]), .b({8{1'b1}}), .eq(comparator_2_eq));  // open: gt, lt
  Comparator #(.width(4)) comparator_3 (.a(register_1_q[15:12]), .b(4'b1001), .eq(comparator_3_eq));  // open: gt, lt
  assign {A7, A6, A5, A4, A3, A2, A1, A0} = not_4_out ? multiplexer_1_out : 8'bz;  // Controlled_Buffer controlled_buffer_5
  not not_4 (not_4_out, or_6_out);
  assign {A7, A6, A5, A4, A3, A2, A1, A0} = or_6_out ? ADDR_in : 8'bz;  // Controlled_Buffer controlled_buffer_6
  or or_5 (or_5_out, START, and_2_out);
  or or_6 (or_6_out, load, look);
  Register #(.trigger("falling"), .width(16)) register_2 (
    .D(control_1_ram_input), .en(and_1_out), .clk(control_1_bank_clk), .Q(register_2_q));  // open: clr
  and and_1 (and_1_out, comparator_2_eq, control_1_ram_we, comparator_3_eq);
  and and_2 (and_2_out, not_5_out, look);
  and and_3 (and_3_out, control_1_halt, comparator_1_eq);
  assign {STD_out4, STD_out3, STD_out2, STD_out1} = and_3_out ? register_2_q : 16'bz;  // Controlled_Buffer controlled_buffer_7
  assign {Df, De, Dd, Dc, Db, Da, D9, D8, D7, D6, D5, D4, D3, D2, D1, D0} = or_5_out ? ram_1_dout : 16'bz;  // Controlled_Buffer controlled_buffer_8
  not not_5 (not_5_out, load);
  assign {Df, De, Dd, Dc, Db, Da, D9, D8, D7, D6, D5, D4, D3, D2, D1, D0} = load ? Data_in : 16'bz;  // Controlled_Buffer controlled_buffer_9
endmodule

module ALU_16bits (
  input  [15:0] A,
  input  [15:0] B,
  input  CADD,
  input  CX,
  input  CAN,
  input  CSUB,
  input  CRS,
  input  CLS,
  output [15:0] O
);

  wire [15:0] adder_1_out, and_1_out, shifter_1_out, shifter_2_out, subtractor_1_out, xor_1_out;

  // Probe on A
  // Probe on B
  Adder #(.width(16)) adder_1 (.a(A), .b(B), .out(adder_1_out), .cin(1'b0));  // open: cout
  Subtractor #(.width(16)) subtractor_1 (.a(A), .b(B), .out(subtractor_1_out), .bin(1'b0));  // open: bout
  Shifter #(.shift("lr"), .width(16)) shifter_1 (.in(A), .\dist (B[3:0]), .out(shifter_1_out));
  Shifter #(.width(16)) shifter_2 (.in(A), .\dist (B[3:0]), .out(shifter_2_out));
  assign xor_1_out = A ^ B;  // XOR_Gate_part xor_1, 16 bits wide
  assign and_1_out = A & B;  // AND_Gate_part and_1, 16 bits wide
  one_hot_mux_6ways_16bits one_hot_mux_6ways_16bits_1 (
    .ADD(adder_1_out), .X(xor_1_out), .AN(and_1_out), .SUB(subtractor_1_out), .RS(shifter_1_out),
    .LS(shifter_2_out), .CADD(CADD), .CX(CX), .CAN(CAN), .CSUB(CSUB), .CRS(CRS), .CLS(CLS), .O(O));
  // Probe on O
endmodule

module one_hot_mux_6ways_16bits (
  input  [15:0] ADD,
  input  [15:0] X,
  input  [15:0] AN,
  input  [15:0] SUB,
  input  [15:0] RS,
  input  [15:0] LS,
  input  CADD,
  input  CX,
  input  CAN,
  input  CSUB,
  input  CRS,
  input  CLS,
  output [15:0] O
);

  wire [15:0] and_1_out, and_2_out, and_3_out, and_4_out, and_5_out, and_6_out, or_1_out, or_2_out;

  assign and_1_out = ADD & {16{CADD}};  // AND_Gate_part and_1, 16 bits wide
  assign and_2_out = X & {16{CX}};  // AND_Gate_part and_2, 16 bits wide
  assign and_3_out = AN & {16{CAN}};  // AND_Gate_part and_3, 16 bits wide
  assign and_4_out = SUB & {16{CSUB}};  // AND_Gate_part and_4, 16 bits wide
  assign and_5_out = RS & {16{CRS}};  // AND_Gate_part and_5, 16 bits wide
  assign and_6_out = LS & {16{CLS}};  // AND_Gate_part and_6, 16 bits wide
  assign or_1_out = and_1_out | and_2_out | and_3_out;  // OR_Gate_part or_1, 16 bits wide
  assign or_2_out = and_4_out | and_5_out | and_6_out;  // OR_Gate_part or_2, 16 bits wide
  assign O = or_1_out | or_2_out;  // OR_Gate_part or_3, 16 bits wide
endmodule

module bank_16Registers (
  input  [15:0] WRITE,
  input  [3:0] AWRITE,
  input  WE,
  input  [3:0] AOUTPUT_S,
  input  OE_S,
  input  [3:0] AOUTPUT_t,
  input  OE_t,
  input  CLK,
  input  R,
  output [15:0] OUTPUT_S,
  output [15:0] OUTPUT_t
);

  wire decoder_1_out0, decoder_1_out1, decoder_1_out2, decoder_1_out3, decoder_1_out4, decoder_1_out5,
       decoder_1_out6, decoder_1_out7, decoder_1_out8, decoder_1_out9, decoder_1_out10, decoder_1_out11,
       decoder_1_out12, decoder_1_out13, decoder_1_out14, decoder_1_out15;
  wire [15:0] demultiplexer_1_out0, demultiplexer_1_out1, demultiplexer_1_out2, demultiplexer_1_out3,
       demultiplexer_1_out4, demultiplexer_1_out5, demultiplexer_1_out6, demultiplexer_1_out7,
       demultiplexer_1_out8, demultiplexer_1_out9, demultiplexer_1_out10, demultiplexer_1_out11,
       demultiplexer_1_out12, demultiplexer_1_out13, demultiplexer_1_out14, demultiplexer_1_out15,
       register_1_q, register_2_q, register_3_q, register_4_q, register_5_q, register_6_q, register_7_q,
       register_8_q, register_9_q, register_10_q, register_11_q, register_12_q, register_13_q, register_14_q,
       register_15_q, register_16_q;

  Demultiplexer #(.select(4), .width(16)) demultiplexer_1 (
    .out0(demultiplexer_1_out0), .out1(demultiplexer_1_out1), .out2(demultiplexer_1_out2),
    .out3(demultiplexer_1_out3), .out4(demultiplexer_1_out4), .out5(demultiplexer_1_out5),
    .out6(demultiplexer_1_out6), .out7(demultiplexer_1_out7), .out8(demultiplexer_1_out8),
    .out9(demultiplexer_1_out9), .out10(demultiplexer_1_out10), .out11(demultiplexer_1_out11),
    .out12(demultiplexer_1_out12), .out13(demultiplexer_1_out13), .out14(demultiplexer_1_out14),
    .out15(demultiplexer_1_out15), .in(WRITE), .sel(AWRITE));
  Decoder #(.select(4)) decoder_1 (
    .out0(decoder_1_out0), .out1(decoder_1_out1), .out2(decoder_1_out2), .out3(decoder_1_out3),
    .out4(decoder_1_out4), .out5(decoder_1_out5), .out6(decoder_1_out6), .out7(decoder_1_out7),
    .out8(decoder_1_out8), .out9(decoder_1_out9), .out10(decoder_1_out10), .out11(decoder_1_out11),
    .out12(decoder_1_out12), .out13(decoder_1_out13), .out14(decoder_1_out14), .out15(decoder_1_out15),
    .sel(AWRITE), .en(WE));
  Register #(.trigger("falling"), .width(16)) register_1 (
    .D({16{1'b0}}), .clk(CLK), .Q(register_1_q), .clr(R));  // open: en
  Register #(.trigger("falling"), .width(16)) register_2 (
    .D(demultiplexer_1_out4), .en(decoder_1_out4), .clk(CLK), .Q(register_2_q), .clr(R));
  Register #(.trigger("falling"), .width(16)) register_3 (
    .D(demultiplexer_1_out8), .en(decoder_1_out8), .clk(CLK), .Q(register_3_q), .clr(R));
  Register #(.trigger("falling"), .width(16)) register_4 (
    .D(demultiplexer_1_out12), .en(decoder_1_out12), .clk(CLK), .Q(register_4_q), .clr(R));
  Register #(.trigger("falling"), .width(16)) register_5 (
    .D(demultiplexer_1_out1), .en(decoder_1_out1), .clk(CLK), .Q(register_5_q), .clr(R));
  Register #(.trigger("falling"), .width(16)) register_6 (
    .D(demultiplexer_1_out5), .en(decoder_1_out5), .clk(CLK), .Q(register_6_q), .clr(R));
  Register #(.trigger("falling"), .width(16)) register_7 (
    .D(demultiplexer_1_out9), .en(decoder_1_out9), .clk(CLK), .Q(register_7_q), .clr(R));
  Register #(.trigger("falling"), .width(16)) register_8 (
    .D(demultiplexer_1_out13), .en(decoder_1_out13), .clk(CLK), .Q(register_8_q), .clr(R));
  Register #(.trigger("falling"), .width(16)) register_9 (
    .D(demultiplexer_1_out2), .en(decoder_1_out2), .clk(CLK), .Q(register_9_q), .clr(R));
  Register #(.trigger("falling"), .width(16)) register_10 (
    .D(demultiplexer_1_out6), .en(decoder_1_out6), .clk(CLK), .Q(register_10_q), .clr(R));
  Register #(.trigger("falling"), .width(16)) register_11 (
    .D(demultiplexer_1_out10), .en(decoder_1_out10), .clk(CLK), .Q(register_11_q), .clr(R));
  Register #(.trigger("falling"), .width(16)) register_12 (
    .D(demultiplexer_1_out14), .en(decoder_1_out14), .clk(CLK), .Q(register_12_q), .clr(R));
  Register #(.trigger("falling"), .width(16)) register_13 (
    .D(demultiplexer_1_out3), .en(decoder_1_out3), .clk(CLK), .Q(register_13_q), .clr(R));
  Register #(.trigger("falling"), .width(16)) register_14 (
    .D(demultiplexer_1_out7), .en(decoder_1_out7), .clk(CLK), .Q(register_14_q), .clr(R));
  Register #(.trigger("falling"), .width(16)) register_15 (
    .D(demultiplexer_1_out11), .en(decoder_1_out11), .clk(CLK), .Q(register_15_q), .clr(R));
  Register #(.trigger("falling"), .width(16)) register_16 (
    .D(demultiplexer_1_out15), .en(decoder_1_out15), .clk(CLK), .Q(register_16_q), .clr(R));
  Multiplexer #(.enable("true"), .select(4), .width(16)) multiplexer_1 (
    .in0(register_1_q), .in1(register_5_q), .in2(register_9_q), .in3(register_13_q), .in4(register_2_q),
    .in5(register_6_q), .in6(register_10_q), .in7(register_14_q), .in8(register_3_q), .in9(register_7_q),
    .in10(register_11_q), .in11(register_15_q), .in12(register_4_q), .in13(register_8_q),
    .in14(register_12_q), .in15(register_16_q), .out(OUTPUT_S), .sel(AOUTPUT_S), .en(OE_S));
  Multiplexer #(.enable("true"), .select(4), .width(16)) multiplexer_2 (
    .in0(register_1_q), .in1(register_5_q), .in2(register_9_q), .in3(register_13_q), .in4(register_2_q),
    .in5(register_6_q), .in6(register_10_q), .in7(register_14_q), .in8(register_3_q), .in9(register_7_q),
    .in10(register_11_q), .in11(register_15_q), .in12(register_4_q), .in13(register_8_q),
    .in14(register_12_q), .in15(register_16_q), .out(OUTPUT_t), .sel(AOUTPUT_t), .en(OE_t));

  // Notes on the sheet:
  //   0
  //   4
  //   8
  //   c
  //   1
  //   5
  //   9
  //   d
  //   2
  //   6
  //   a
  //   e
  //   3
  //   7
  //   b
  //   f
endmodule

module CONTROL (
  input  START,
  input  fetch,
  input  fetchwrite,
  input  execute,
  input  executewrite,
  input  [15:0] OUTPUT_S,
  input  [15:0] O,
  input  [15:0] OUTPUT_t,
  input  [7:0] CQ,
  input  [15:0] Ram_OUTPUT,
  input  [15:0] R_Q,
  output RUN,
  output HALT,
  output [15:0] WRITE,
  output [15:0] A,
  output [3:0] AWRITE,
  output [15:0] B,
  output bank_WE,
  output CADD,
  output [3:0] AOUTPUT_S,
  output CX,
  output OE_S,
  output CAN,
  output [3:0] AOUTPUT_t,
  output CSUB,
  output LOAD,
  output OE_t,
  output CRS,
  output [7:0] CD,
  output CCT,
  output bank_clk,
  output CLS,
  output RAM_WE,
  output RAM_OE,
  output [15:0] RAM_INPUT,
  output A_MUX_C,
  output [7:0] A_MUX,
  output R_WE
);

  wire and_2_out, and_3_out, and_4_out, and_5_out, and_6_out, and_9_out, and_10_out, clock_2_out,
       decoder_1_out0, decoder_1_out7, decoder_1_out8, decoder_1_out9, decoder_1_out10, decoder_1_out11,
       decoder_1_out12, decoder_1_out13, decoder_1_out14, decoder_1_out15, or_1_out, or_2_out, or_3_out,
       or_4_out, or_5_out, or_6_out, or_7_out, or_8_out, or_9_out, or_10_out;
  wire [7:0] controlled_buffer_8_out;

  or or_1 (or_1_out, decoder_1_out8, decoder_1_out10);
  assign WRITE = decoder_1_out15 ? {{8{1'b0}}, CQ} : 16'bz;  // Controlled_Buffer controlled_buffer_1
  Multiplexer #(.width(4)) multiplexer_1 (.in0(R_Q[7:4]), .in1(R_Q[11:8]), .out(AOUTPUT_S), .sel(or_2_out));
  assign WRITE = decoder_1_out7 ? {{8{1'b0}}, R_Q[7:0]} : 16'bz;  // Controlled_Buffer controlled_buffer_2
  assign WRITE = or_1_out ? Ram_OUTPUT : 16'bz;  // Controlled_Buffer controlled_buffer_3
  Pull_Resistor pull_resistor_1 (.node(WRITE));
  or or_2 (or_2_out, decoder_1_out9, decoder_1_out12, decoder_1_out13, decoder_1_out14, decoder_1_out11);
  Clock clock_1 (.out(bank_clk));
  and and_1 (bank_WE, ~or_2_out, executewrite);  // AND_Gate_part
  Decoder #(.select(4)) decoder_1 (
    .out0(decoder_1_out0), .out1(CADD), .out2(CSUB), .out3(CAN), .out4(CX), .out5(CLS), .out6(CRS),
    .out7(decoder_1_out7), .out8(decoder_1_out8), .out9(decoder_1_out9), .out10(decoder_1_out10),
    .out11(decoder_1_out11), .out12(decoder_1_out12), .out13(decoder_1_out13), .out14(decoder_1_out14),
    .out15(decoder_1_out15), .sel(R_Q[15:12]));  // open: en
  assign WRITE = or_3_out ? O : 16'bz;  // Controlled_Buffer controlled_buffer_4
  or or_3 (or_3_out, CADD, CSUB, CAN, CX, CLS, CRS);
  and and_2 (and_2_out, ~OUTPUT_S[0], ~OUTPUT_S[1], ~OUTPUT_S[2], ~OUTPUT_S[3], ~OUTPUT_S[4], ~OUTPUT_S[5], ~OUTPUT_S[6], ~OUTPUT_S[7], ~OUTPUT_S[9], ~OUTPUT_S[10], ~OUTPUT_S[11], ~OUTPUT_S[12], ~OUTPUT_S[13], ~OUTPUT_S[14], ~OUTPUT_S[15], ~OUTPUT_S[8]);  // AND_Gate_part
  Register #(.width(1)) register_1 (.D(and_3_out), .en(and_3_out), .clk(bank_clk), .Q(HALT));  // open: clr
  and and_3 (and_3_out, decoder_1_out0, execute);
  or or_4 (or_4_out, decoder_1_out8, decoder_1_out9);
  and and_4 (and_4_out, decoder_1_out14, or_9_out);
  or or_5 (or_5_out, decoder_1_out13, decoder_1_out12, decoder_1_out14);
  assign CD = decoder_1_out14 ? OUTPUT_S[7:0] : 8'bz;  // Controlled_Buffer controlled_buffer_5
  assign CD = or_8_out ? R_Q[7:0] : 8'bz;  // Controlled_Buffer controlled_buffer_6
  or or_6 (or_6_out, decoder_1_out10, decoder_1_out11);
  assign A_MUX = or_4_out ? R_Q[7:0] : 8'bz;  // Controlled_Buffer controlled_buffer_7
  Pull_Resistor pull_resistor_2 (.node(CD));
  assign {controlled_buffer_8_out, A_MUX} = or_6_out ? OUTPUT_t : 16'bz;  // Controlled_Buffer controlled_buffer_8
  and and_5 (and_5_out, ~OUTPUT_S[0], ~OUTPUT_S[1], ~OUTPUT_S[2], ~OUTPUT_S[3], ~OUTPUT_S[4], ~OUTPUT_S[5], ~OUTPUT_S[6], ~OUTPUT_S[7], ~OUTPUT_S[8], ~OUTPUT_S[9], ~OUTPUT_S[10], ~OUTPUT_S[11], ~OUTPUT_S[12], ~OUTPUT_S[13], ~OUTPUT_S[14], ~OUTPUT_S[15], decoder_1_out12);  // AND_Gate_part
  or or_7 (or_7_out, execute, executewrite);
  or or_8 (or_8_out, and_5_out, and_6_out, decoder_1_out15);
  and and_6 (and_6_out, decoder_1_out13, ~and_2_out, ~OUTPUT_S[15]);  // AND_Gate_part
  and and_7 (RAM_WE, or_7_out, ~or_5_out, or_2_out);  // AND_Gate_part
  and and_8 (LOAD, ~fetch, or_10_out);  // AND_Gate_part
  or or_9 (or_9_out, execute, executewrite);
  or or_10 (or_10_out, and_5_out, and_6_out, and_4_out, decoder_1_out15);
  or or_11 (RAM_OE, fetch, A_MUX_C);
  Clock clock_2 (.out(clock_2_out));
  or or_12 (A_MUX_C, and_9_out, and_10_out);
  and and_9 (and_9_out, executewrite, or_1_out);
  and and_10 (and_10_out, or_9_out, ~or_5_out, or_2_out);  // AND_Gate_part

  assign A = OUTPUT_S;
  assign AOUTPUT_t = R_Q[3:0];
  assign AWRITE = R_Q[11:8];
  assign B = OUTPUT_t;
  assign CCT = fetchwrite;
  assign OE_S = execute;
  assign OE_t = execute;
  assign R_WE = fetchwrite;
  assign RAM_INPUT = OUTPUT_S;
  assign RUN = START;
endmodule

module CLOCKK (
  input  RUN,
  input  HALT,
  output FETCH,
  output FETCH_WRITE,
  output EXECUTE,
  output EXECUTE_WRITE
);

  wire and_1_out, and_2_out, clock_1_out, d_ff_1_q, d_ff_1_qn, not_1_out;

  Clock clock_1 (.out(clock_1_out));
  not not_1 (not_1_out, HALT);
  and and_1 (and_1_out, RUN, clock_1_out);
  and and_2 (and_2_out, and_1_out, not_1_out);
  D_Flip_Flop #(.trigger("falling")) d_ff_1 (
    .D(d_ff_1_qn), .clk(and_2_out), .Q(d_ff_1_q), .Qn(d_ff_1_qn));  // open: preset, reset
  and and_3 (FETCH, d_ff_1_qn, RUN);
  and and_4 (EXECUTE, d_ff_1_q, RUN);
  and and_5 (FETCH_WRITE, FETCH, and_2_out);
  and and_6 (EXECUTE_WRITE, EXECUTE, and_2_out);
endmodule

module HARD_WORK (
  input  START,
  input  fetch,
  input  fetchwrite,
  input  execute,
  input  executewrite,
  input  [15:0] O,
  input  [15:0] OUTPUT_S,
  input  [15:0] OUTPUT_t,
  input  [7:0] CQ,
  input  [15:0] Ram_OUTPUT,
  input  [15:0] R_Q,
  output RUN,
  output HALT,
  output [15:0] WRITE,
  output [15:0] A,
  output [3:0] AWRITE,
  output [15:0] B,
  output bank_WE,
  output CADD,
  output [3:0] AOUTPUT_S,
  output CX,
  output OE_S,
  output CAN,
  output [3:0] AOUTPUT_t,
  output CSUB,
  output LOAD,
  output OE_t,
  output CRS,
  output [7:0] CD,
  output CCT,
  output bank_clk,
  output CLS,
  output RAM_WE,
  output RAM_OE,
  output [15:0] RAM_INPUT,
  output A_MUX_C,
  output [7:0] A_MUX,
  output R_WE
);

  wire and_2_out, and_4_out, and_5_out, and_6_out, and_8_out, and_9_out, clock_2_out, decoder_1_out0,
       decoder_1_out7, decoder_1_out8, decoder_1_out9, decoder_1_out10, decoder_1_out11, decoder_1_out12,
       decoder_1_out13, decoder_1_out14, decoder_1_out15, or_1_out, or_2_out, or_3_out, or_4_out, or_5_out,
       or_6_out, or_7_out, or_8_out, or_9_out;
  wire [7:0] controlled_buffer_8_out, multiplexer_2_out;

  or or_1 (or_1_out, decoder_1_out8, decoder_1_out10);
  assign WRITE = decoder_1_out15 ? {{8{1'b0}}, CQ} : 16'bz;  // Controlled_Buffer controlled_buffer_1
  Multiplexer #(.width(4)) multiplexer_1 (.in0(R_Q[7:4]), .in1(R_Q[11:8]), .out(AOUTPUT_S), .sel(or_2_out));
  assign WRITE = decoder_1_out7 ? {{8{1'b0}}, R_Q[7:0]} : 16'bz;  // Controlled_Buffer controlled_buffer_2
  assign WRITE = or_1_out ? Ram_OUTPUT : 16'bz;  // Controlled_Buffer controlled_buffer_3
  Pull_Resistor pull_resistor_1 (.node(WRITE));
  or or_2 (or_2_out, decoder_1_out9, decoder_1_out12, decoder_1_out13, decoder_1_out14, decoder_1_out11);
  Clock clock_1 (.out(bank_clk));
  and and_1 (bank_WE, ~or_2_out, executewrite);  // AND_Gate_part
  Decoder #(.select(4)) decoder_1 (
    .out0(decoder_1_out0), .out1(CADD), .out2(CSUB), .out3(CAN), .out4(CX), .out5(CLS), .out6(CRS),
    .out7(decoder_1_out7), .out8(decoder_1_out8), .out9(decoder_1_out9), .out10(decoder_1_out10),
    .out11(decoder_1_out11), .out12(decoder_1_out12), .out13(decoder_1_out13), .out14(decoder_1_out14),
    .out15(decoder_1_out15), .sel(R_Q[15:12]));  // open: en
  assign WRITE = or_3_out ? O : 16'bz;  // Controlled_Buffer controlled_buffer_4
  or or_3 (or_3_out, CADD, CSUB, CAN, CX, CLS, CRS);
  bank_16Registers bank_16registers_1 (
    .WRITE(WRITE), .AWRITE(R_Q[11:8]), .WE(bank_WE), .AOUTPUT_S(AOUTPUT_S), .OE_S(execute),
    .AOUTPUT_t(R_Q[3:0]), .OE_t(execute), .CLK(bank_clk), .OUTPUT_S(OUTPUT_S), .OUTPUT_t(OUTPUT_t));  // open: R
  and and_2 (and_2_out, ~OUTPUT_S[0], ~OUTPUT_S[1], ~OUTPUT_S[2], ~OUTPUT_S[3], ~OUTPUT_S[4], ~OUTPUT_S[5], ~OUTPUT_S[6], ~OUTPUT_S[7], ~OUTPUT_S[9], ~OUTPUT_S[10], ~OUTPUT_S[11], ~OUTPUT_S[12], ~OUTPUT_S[13], ~OUTPUT_S[14], ~OUTPUT_S[15], ~OUTPUT_S[8]);  // AND_Gate_part
  and and_3 (HALT, decoder_1_out0, executewrite);
  or or_4 (or_4_out, decoder_1_out8, decoder_1_out9);
  Register #(.trigger("falling"), .width(16)) register_1 (
    .D(Ram_OUTPUT), .en(fetchwrite), .clk(clock_2_out), .Q(R_Q));  // open: clr
  and and_4 (and_4_out, decoder_1_out14, or_9_out);
  ALU_16bits alu_16bits_1 (
    .A(OUTPUT_S), .B(OUTPUT_t), .CADD(CADD), .CX(CX), .CAN(CAN), .CSUB(CSUB), .CRS(CRS), .CLS(CLS), .O(O));
  or or_5 (or_5_out, decoder_1_out13, decoder_1_out12, decoder_1_out14);
  Control_Unit_Sequencer control_unit_sequencer_1 (
    .RUN(START), .HALT(HALT), .fetch(fetch), .fetchwrite(fetchwrite), .execute(execute),
    .Executewrite(executewrite));
  assign CD = decoder_1_out14 ? OUTPUT_S[7:0] : 8'bz;  // Controlled_Buffer controlled_buffer_5
  assign CD = or_8_out ? R_Q[7:0] : 8'bz;  // Controlled_Buffer controlled_buffer_6
  or or_6 (or_6_out, decoder_1_out10, decoder_1_out11);
  assign A_MUX = or_4_out ? R_Q[7:0] : 8'bz;  // Controlled_Buffer controlled_buffer_7
  Pull_Resistor pull_resistor_2 (.node(CD));
  assign {controlled_buffer_8_out, A_MUX} = or_6_out ? OUTPUT_t : 16'bz;  // Controlled_Buffer controlled_buffer_8
  and and_5 (and_5_out, ~OUTPUT_S[0], ~OUTPUT_S[1], ~OUTPUT_S[2], ~OUTPUT_S[3], ~OUTPUT_S[4], ~OUTPUT_S[5], ~OUTPUT_S[6], ~OUTPUT_S[7], ~OUTPUT_S[8], ~OUTPUT_S[9], ~OUTPUT_S[10], ~OUTPUT_S[11], ~OUTPUT_S[12], ~OUTPUT_S[13], ~OUTPUT_S[14], ~OUTPUT_S[15], decoder_1_out12);  // AND_Gate_part
  or or_7 (or_7_out, execute, executewrite);
  or or_8 (or_8_out, and_5_out, and_6_out, decoder_1_out15);
  and and_6 (and_6_out, decoder_1_out13, ~and_2_out, ~OUTPUT_S[15]);  // AND_Gate_part
  and and_7 (RAM_WE, or_7_out, ~or_5_out, or_2_out);  // AND_Gate_part
  or or_9 (or_9_out, execute, executewrite);
  or or_10 (LOAD, and_5_out, and_6_out, and_4_out, decoder_1_out15);
  Counter #(.trigger("falling")) counter_1 (
    .load(LOAD), .D(CD), .count(fetchwrite), .Q(CQ), .clk(clock_2_out));  // open: carry, up, clr
  or or_11 (RAM_OE, fetch, A_MUX_C);
  Clock clock_2 (.out(clock_2_out));
  Multiplexer #(.width(8)) multiplexer_2 (.in0(CQ), .in1(A_MUX), .out(multiplexer_2_out), .sel(A_MUX_C));
  or or_12 (A_MUX_C, and_8_out, and_9_out);
  and and_8 (and_8_out, executewrite, or_1_out);
  and and_9 (and_9_out, or_9_out, ~or_5_out, or_2_out);  // AND_Gate_part
  RAM #(.asyncread("true"), .dataWidth(16), .\type ("nonvolatile")) ram_1 (
    .addr(multiplexer_2_out), .we(RAM_WE), .oe(RAM_OE), .clk(clock_2_out), .din(OUTPUT_S), .dout(Ram_OUTPUT));

  assign A = OUTPUT_S;
  assign AOUTPUT_t = R_Q[3:0];
  assign AWRITE = R_Q[11:8];
  assign B = OUTPUT_t;
  assign CCT = fetchwrite;
  assign OE_S = execute;
  assign OE_t = execute;
  assign R_WE = fetchwrite;
  assign RAM_INPUT = OUTPUT_S;
  assign RUN = START;
endmodule

module CPU_16bits_WOIBC (
  input  START
);

  wire control_1_a_mux_c, control_1_bank_clk, control_1_bank_we, control_1_cadd, control_1_can,
       control_1_cct, control_1_cls, control_1_crs, control_1_csub, control_1_cx, control_1_halt,
       control_1_load, control_1_oe_s, control_1_oe_t, control_1_ram_oe, control_1_ram_we, control_1_run,
       control_unit_sequencer_1_execute, control_unit_sequencer_1_executewrite,
       control_unit_sequencer_1_fetch, control_unit_sequencer_1_fetchwrite, register_1_p2;
  wire [3:0] control_1_aoutput_s, control_1_aoutput_t, control_1_awrite;
  wire [7:0] control_1_a_mux, control_1_cd, counter_1_q, multiplexer_1_out;
  wire [15:0] alu_16bits_woibc_1_o, bank_16registers_1_output_s, bank_16registers_1_output_t, control_1_a,
       control_1_b, control_1_ram_input, control_1_write, register_1_p1, register_1_p3;

  register_16bits register_16bits_1 ();  // open: D, WE, CLK, R, Q
  bank_16Registers bank_16registers_1 (
    .WRITE(control_1_write), .AWRITE(control_1_awrite), .WE(control_1_bank_we),
    .AOUTPUT_S(control_1_aoutput_s), .OE_S(control_1_oe_s), .AOUTPUT_t(control_1_aoutput_t),
    .OE_t(control_1_oe_t), .CLK(control_1_bank_clk), .OUTPUT_S(bank_16registers_1_output_s),
    .OUTPUT_t(bank_16registers_1_output_t));  // open: R
  ALU_16bits_WOIBC alu_16bits_woibc_1 (
    .A(control_1_a), .B(control_1_b), .CADD(control_1_cadd), .CX(control_1_cx), .CAN(control_1_can),
    .CSUB(control_1_csub), .CRS(control_1_crs), .CLS(control_1_cls), .O(alu_16bits_woibc_1_o));
  // Register #(.trigger("falling"), .width(16)) register_1: pin names not known; wires that end beside it: register_1_p1, register_1_p2, register_1_p3
  register_16bits register_16bits_2 (
    .D(register_1_p1), .WE(register_1_p2), .CLK(control_1_bank_clk), .Q(register_1_p3));  // open: R
  Control_Unit_Sequencer control_unit_sequencer_1 (
    .RUN(control_1_run), .HALT(control_1_halt), .fetch(control_unit_sequencer_1_fetch),
    .fetchwrite(control_unit_sequencer_1_fetchwrite), .execute(control_unit_sequencer_1_execute),
    .Executewrite(control_unit_sequencer_1_executewrite));
  CONTROL control_1 (
    .START(START), .fetch(control_unit_sequencer_1_fetch), .fetchwrite(control_unit_sequencer_1_fetchwrite),
    .execute(control_unit_sequencer_1_execute), .executewrite(control_unit_sequencer_1_executewrite),
    .OUTPUT_S(bank_16registers_1_output_s), .O(alu_16bits_woibc_1_o), .OUTPUT_t(bank_16registers_1_output_t),
    .CQ(counter_1_q), .Ram_OUTPUT(register_1_p1), .R_Q(register_1_p3), .RUN(control_1_run),
    .HALT(control_1_halt), .WRITE(control_1_write), .A(control_1_a), .AWRITE(control_1_awrite),
    .B(control_1_b), .bank_WE(control_1_bank_we), .CADD(control_1_cadd), .AOUTPUT_S(control_1_aoutput_s),
    .CX(control_1_cx), .OE_S(control_1_oe_s), .CAN(control_1_can), .AOUTPUT_t(control_1_aoutput_t),
    .CSUB(control_1_csub), .LOAD(control_1_load), .OE_t(control_1_oe_t), .CRS(control_1_crs),
    .CD(control_1_cd), .CCT(control_1_cct), .bank_clk(control_1_bank_clk), .CLS(control_1_cls),
    .RAM_WE(control_1_ram_we), .RAM_OE(control_1_ram_oe), .RAM_INPUT(control_1_ram_input),
    .A_MUX_C(control_1_a_mux_c), .A_MUX(control_1_a_mux), .R_WE(register_1_p2));
  Counter #(.trigger("falling")) counter_1 (
    .load(control_1_load), .D(control_1_cd), .count(control_1_cct), .Q(counter_1_q), .clk(control_1_bank_clk));  // open: carry, up, clr
  RAM #(.asyncread("true"), .dataWidth(16), .\type ("nonvolatile")) ram_1 (
    .addr(multiplexer_1_out), .we(control_1_ram_we), .oe(control_1_ram_oe), .clk(control_1_bank_clk),
    .din(control_1_ram_input), .dout(register_1_p1));
  Multiplexer #(.width(8)) multiplexer_1 (
    .in0(counter_1_q), .in1(control_1_a_mux), .out(multiplexer_1_out), .sel(control_1_a_mux_c));
  PC pc_1 ();  // open: D, Increment, Load, CLK, R, Q
endmodule

module Copy_past (
  input  in_1,
  input  in_2
);

  CLOCKK clockk_1 (.RUN(in_1), .HALT(in_2));  // open: FETCH, FETCH_WRITE, EXECUTE, EXECUTE_WRITE
  Control_Unit_Sequencer control_unit_sequencer_1 (
    .RUN(in_1), .HALT(in_2));  // open: fetch, fetchwrite, execute, Executewrite
endmodule

module ALU_16bits_WOIBC (
  input  [15:0] A,
  input  [15:0] B,
  input  CADD,
  input  CX,
  input  CAN,
  input  CSUB,
  input  CRS,
  input  CLS,
  output [15:0] O
);

  wire [15:0] and_gate_16bits_1_out_3, left_bitshifter_16bits_1_out_3, right_bitshifter_16bits_1_out_3,
       ripple_carry_adder_16bits_1_out_3, subtractor_16bits_1_out_3, xor_gate_16bits_1_out_3;

  // Probe on A
  // Probe on B
  Ripple_Carry_Adder_16bits ripple_carry_adder_16bits_1 (.A(A), .B(B), .out_3(ripple_carry_adder_16bits_1_out_3));
  XOR_Gate_16bits xor_gate_16bits_1 (.in_1(A), .in_2(B), .out_3(xor_gate_16bits_1_out_3));
  AND_Gate_16bits and_gate_16bits_1 (.in_1(A), .in_2(B), .out_3(and_gate_16bits_1_out_3));
  Subtractor_16bits subtractor_16bits_1 (.A(A), .B(B), .out_3(subtractor_16bits_1_out_3));
  Right_bitShifter_16bits right_bitshifter_16bits_1 (.in_1(A), .in_2(B), .out_3(right_bitshifter_16bits_1_out_3));
  Left_bitShifter_16bits left_bitshifter_16bits_1 (.in_1(A), .in_2(B), .out_3(left_bitshifter_16bits_1_out_3));
  one_hot_mux_6ways_16bits one_hot_mux_6ways_16bits_1 (
    .ADD(ripple_carry_adder_16bits_1_out_3), .X(xor_gate_16bits_1_out_3), .AN(and_gate_16bits_1_out_3),
    .SUB(subtractor_16bits_1_out_3), .RS(right_bitshifter_16bits_1_out_3),
    .LS(left_bitshifter_16bits_1_out_3), .CADD(CADD), .CX(CX), .CAN(CAN), .CSUB(CSUB), .CRS(CRS), .CLS(CLS),
    .O(O));
  // Probe on O
endmodule

module Ripple_Carry_Adder_16bits (
  input  [15:0] A,
  input  [15:0] B,
  output [15:0] out_3
);

  wire full_adder_1bit_1_cout, full_adder_1bit_2_cout, full_adder_1bit_3_cout, full_adder_1bit_4_cout,
       full_adder_1bit_5_cout, full_adder_1bit_6_cout, full_adder_1bit_7_cout, full_adder_1bit_8_cout,
       full_adder_1bit_9_cout, full_adder_1bit_10_cout, full_adder_1bit_11_cout, full_adder_1bit_12_cout,
       full_adder_1bit_13_cout, full_adder_1bit_14_cout, full_adder_1bit_15_cout;

  Full_Adder_1bit full_adder_1bit_1 (.A(A[0]), .B(B[0]), .SUM(out_3[0]), .COUT(full_adder_1bit_1_cout));  // open: CIN
  Full_Adder_1bit full_adder_1bit_2 (
    .A(A[1]), .B(B[1]), .CIN(full_adder_1bit_1_cout), .SUM(out_3[1]), .COUT(full_adder_1bit_2_cout));
  Full_Adder_1bit full_adder_1bit_3 (
    .A(A[2]), .B(B[2]), .CIN(full_adder_1bit_2_cout), .SUM(out_3[2]), .COUT(full_adder_1bit_3_cout));
  Full_Adder_1bit full_adder_1bit_4 (
    .A(A[3]), .B(B[3]), .CIN(full_adder_1bit_3_cout), .SUM(out_3[3]), .COUT(full_adder_1bit_4_cout));
  Full_Adder_1bit full_adder_1bit_5 (
    .A(A[4]), .B(B[4]), .CIN(full_adder_1bit_4_cout), .SUM(out_3[4]), .COUT(full_adder_1bit_5_cout));
  Full_Adder_1bit full_adder_1bit_6 (
    .A(A[5]), .B(B[5]), .CIN(full_adder_1bit_5_cout), .SUM(out_3[5]), .COUT(full_adder_1bit_6_cout));
  Full_Adder_1bit full_adder_1bit_7 (
    .A(A[6]), .B(B[6]), .CIN(full_adder_1bit_6_cout), .SUM(out_3[6]), .COUT(full_adder_1bit_7_cout));
  Full_Adder_1bit full_adder_1bit_8 (
    .A(A[7]), .B(B[7]), .CIN(full_adder_1bit_7_cout), .SUM(out_3[7]), .COUT(full_adder_1bit_8_cout));
  Full_Adder_1bit full_adder_1bit_9 (
    .A(A[8]), .B(B[8]), .CIN(full_adder_1bit_8_cout), .SUM(out_3[8]), .COUT(full_adder_1bit_9_cout));
  Full_Adder_1bit full_adder_1bit_10 (
    .A(A[9]), .B(B[9]), .CIN(full_adder_1bit_9_cout), .SUM(out_3[9]), .COUT(full_adder_1bit_10_cout));
  Full_Adder_1bit full_adder_1bit_11 (
    .A(A[10]), .B(B[10]), .CIN(full_adder_1bit_10_cout), .SUM(out_3[10]), .COUT(full_adder_1bit_11_cout));
  Full_Adder_1bit full_adder_1bit_12 (
    .A(A[11]), .B(B[11]), .CIN(full_adder_1bit_11_cout), .SUM(out_3[11]), .COUT(full_adder_1bit_12_cout));
  Full_Adder_1bit full_adder_1bit_13 (
    .A(A[12]), .B(B[12]), .CIN(full_adder_1bit_12_cout), .SUM(out_3[12]), .COUT(full_adder_1bit_13_cout));
  Full_Adder_1bit full_adder_1bit_14 (
    .A(A[13]), .B(B[13]), .CIN(full_adder_1bit_13_cout), .SUM(out_3[13]), .COUT(full_adder_1bit_14_cout));
  Full_Adder_1bit full_adder_1bit_15 (
    .A(A[14]), .B(B[14]), .CIN(full_adder_1bit_14_cout), .SUM(out_3[14]), .COUT(full_adder_1bit_15_cout));
  Full_Adder_1bit full_adder_1bit_16 (
    .A(A[15]), .B(B[15]), .CIN(full_adder_1bit_15_cout), .SUM(out_3[15]));  // open: COUT
endmodule

module XOR_Gate_16bits (
  input  [15:0] in_1,
  input  [15:0] in_2,
  output [15:0] out_3
);

  XOR_Gate xor_gate_1 (.in_1(in_1[0]), .in_2(in_2[0]), .out_3(out_3[0]));
  XOR_Gate xor_gate_2 (.in_1(in_1[1]), .in_2(in_2[1]), .out_3(out_3[1]));
  XOR_Gate xor_gate_3 (.in_1(in_1[2]), .in_2(in_2[2]), .out_3(out_3[2]));
  XOR_Gate xor_gate_4 (.in_1(in_1[3]), .in_2(in_2[3]), .out_3(out_3[3]));
  XOR_Gate xor_gate_5 (.in_1(in_1[4]), .in_2(in_2[4]), .out_3(out_3[4]));
  XOR_Gate xor_gate_6 (.in_1(in_1[5]), .in_2(in_2[5]), .out_3(out_3[5]));
  XOR_Gate xor_gate_7 (.in_1(in_1[6]), .in_2(in_2[6]), .out_3(out_3[6]));
  XOR_Gate xor_gate_8 (.in_1(in_1[7]), .in_2(in_2[7]), .out_3(out_3[7]));
  XOR_Gate xor_gate_9 (.in_1(in_1[8]), .in_2(in_2[8]), .out_3(out_3[8]));
  XOR_Gate xor_gate_10 (.in_1(in_1[9]), .in_2(in_2[9]), .out_3(out_3[9]));
  XOR_Gate xor_gate_11 (.in_1(in_1[10]), .in_2(in_2[10]), .out_3(out_3[10]));
  XOR_Gate xor_gate_12 (.in_1(in_1[11]), .in_2(in_2[11]), .out_3(out_3[11]));
  XOR_Gate xor_gate_13 (.in_1(in_1[12]), .in_2(in_2[12]), .out_3(out_3[12]));
  XOR_Gate xor_gate_14 (.in_1(in_1[13]), .in_2(in_2[13]), .out_3(out_3[13]));
  XOR_Gate xor_gate_15 (.in_1(in_1[14]), .in_2(in_2[14]), .out_3(out_3[14]));
  XOR_Gate xor_gate_16 (.in_1(in_1[15]), .in_2(in_2[15]), .out_3(out_3[15]));
endmodule

module AND_Gate_16bits (
  input  [15:0] in_1,
  input  [15:0] in_2,
  output [15:0] out_3
);

  AND_Gate and_gate_1 (.in_1(in_1[0]), .in_2(in_2[0]), .out_3(out_3[0]));
  AND_Gate and_gate_2 (.in_1(in_1[1]), .in_2(in_2[1]), .out_3(out_3[1]));
  AND_Gate and_gate_3 (.in_1(in_1[2]), .in_2(in_2[2]), .out_3(out_3[2]));
  AND_Gate and_gate_4 (.in_1(in_1[3]), .in_2(in_2[3]), .out_3(out_3[3]));
  AND_Gate and_gate_5 (.in_1(in_1[4]), .in_2(in_2[4]), .out_3(out_3[4]));
  AND_Gate and_gate_6 (.in_1(in_1[5]), .in_2(in_2[5]), .out_3(out_3[5]));
  AND_Gate and_gate_7 (.in_1(in_1[6]), .in_2(in_2[6]), .out_3(out_3[6]));
  AND_Gate and_gate_8 (.in_1(in_1[7]), .in_2(in_2[7]), .out_3(out_3[7]));
  AND_Gate and_gate_9 (.in_1(in_1[8]), .in_2(in_2[8]), .out_3(out_3[8]));
  AND_Gate and_gate_10 (.in_1(in_1[9]), .in_2(in_2[9]), .out_3(out_3[9]));
  AND_Gate and_gate_11 (.in_1(in_1[10]), .in_2(in_2[10]), .out_3(out_3[10]));
  AND_Gate and_gate_12 (.in_1(in_1[11]), .in_2(in_2[11]), .out_3(out_3[11]));
  AND_Gate and_gate_13 (.in_1(in_1[12]), .in_2(in_2[12]), .out_3(out_3[12]));
  AND_Gate and_gate_14 (.in_1(in_1[13]), .in_2(in_2[13]), .out_3(out_3[13]));
  AND_Gate and_gate_15 (.in_1(in_1[14]), .in_2(in_2[14]), .out_3(out_3[14]));
  AND_Gate and_gate_16 (.in_1(in_1[15]), .in_2(in_2[15]), .out_3(out_3[15]));
endmodule

module Subtractor_16bits (
  input  [15:0] A,
  input  [15:0] B,
  output [15:0] out_3
);

  wire sub_1_out_5, sub_2_out_5, sub_3_out_5, sub_4_out_5, sub_5_out_5, sub_6_out_5, sub_7_out_5,
       sub_8_out_5, sub_9_out_5, sub_10_out_5, sub_11_out_5, sub_12_out_5, sub_13_out_5, sub_14_out_5,
       sub_15_out_5;

  Sub sub_1 (.in_1(A[0]), .in_2(B[0]), .out_4(out_3[0]), .out_5(sub_1_out_5));  // open: in_3
  Sub sub_2 (.in_1(A[1]), .in_2(B[1]), .in_3(sub_1_out_5), .out_4(out_3[1]), .out_5(sub_2_out_5));
  Sub sub_3 (.in_1(A[2]), .in_2(B[2]), .in_3(sub_2_out_5), .out_4(out_3[2]), .out_5(sub_3_out_5));
  Sub sub_4 (.in_1(A[3]), .in_2(B[3]), .in_3(sub_3_out_5), .out_4(out_3[3]), .out_5(sub_4_out_5));
  Sub sub_5 (.in_1(A[4]), .in_2(B[4]), .in_3(sub_4_out_5), .out_4(out_3[4]), .out_5(sub_5_out_5));
  Sub sub_6 (.in_1(A[5]), .in_2(B[5]), .in_3(sub_5_out_5), .out_4(out_3[5]), .out_5(sub_6_out_5));
  Sub sub_7 (.in_1(A[6]), .in_2(B[6]), .in_3(sub_6_out_5), .out_4(out_3[6]), .out_5(sub_7_out_5));
  Sub sub_8 (.in_1(A[7]), .in_2(B[7]), .in_3(sub_7_out_5), .out_4(out_3[7]), .out_5(sub_8_out_5));
  Sub sub_9 (.in_1(A[8]), .in_2(B[8]), .in_3(sub_8_out_5), .out_4(out_3[8]), .out_5(sub_9_out_5));
  Sub sub_10 (.in_1(A[9]), .in_2(B[9]), .in_3(sub_9_out_5), .out_4(out_3[9]), .out_5(sub_10_out_5));
  Sub sub_11 (.in_1(A[10]), .in_2(B[10]), .in_3(sub_10_out_5), .out_4(out_3[10]), .out_5(sub_11_out_5));
  Sub sub_12 (.in_1(A[11]), .in_2(B[11]), .in_3(sub_11_out_5), .out_4(out_3[11]), .out_5(sub_12_out_5));
  Sub sub_13 (.in_1(A[12]), .in_2(B[12]), .in_3(sub_12_out_5), .out_4(out_3[12]), .out_5(sub_13_out_5));
  Sub sub_14 (.in_1(A[13]), .in_2(B[13]), .in_3(sub_13_out_5), .out_4(out_3[13]), .out_5(sub_14_out_5));
  Sub sub_15 (.in_1(A[14]), .in_2(B[14]), .in_3(sub_14_out_5), .out_4(out_3[14]), .out_5(sub_15_out_5));
  Sub sub_16 (.in_1(A[15]), .in_2(B[15]), .in_3(sub_15_out_5), .out_4(out_3[15]));  // open: out_5
endmodule
module Right_bitShifter_16bits (
  input  [15:0] in_1,
  input  [15:0] in_2,
  output [15:0] out_3
);

  wire mux_2to1_1bit_1_out_4, mux_2to1_1bit_2_out_4, mux_2to1_1bit_3_out_4, mux_2to1_1bit_4_out_4,
       mux_2to1_1bit_5_out_4, mux_2to1_1bit_6_out_4, mux_2to1_1bit_7_out_4, mux_2to1_1bit_8_out_4,
       mux_2to1_1bit_9_out_4, mux_2to1_1bit_10_out_4, mux_2to1_1bit_11_out_4, mux_2to1_1bit_12_out_4,
       mux_2to1_1bit_13_out_4, mux_2to1_1bit_14_out_4, mux_2to1_1bit_15_out_4, mux_2to1_1bit_16_out_4,
       mux_2to1_1bit_17_out_4, mux_2to1_1bit_18_out_4, mux_2to1_1bit_19_out_4, mux_2to1_1bit_20_out_4,
       mux_2to1_1bit_21_out_4, mux_2to1_1bit_22_out_4, mux_2to1_1bit_23_out_4, mux_2to1_1bit_24_out_4,
       mux_2to1_1bit_25_out_4, mux_2to1_1bit_26_out_4, mux_2to1_1bit_27_out_4, mux_2to1_1bit_28_out_4,
       mux_2to1_1bit_29_out_4, mux_2to1_1bit_30_out_4, mux_2to1_1bit_31_out_4, mux_2to1_1bit_32_out_4,
       mux_2to1_1bit_33_out_4, mux_2to1_1bit_34_out_4, mux_2to1_1bit_35_out_4, mux_2to1_1bit_36_out_4,
       mux_2to1_1bit_37_out_4, mux_2to1_1bit_38_out_4, mux_2to1_1bit_39_out_4, mux_2to1_1bit_40_out_4,
       mux_2to1_1bit_41_out_4, mux_2to1_1bit_42_out_4, mux_2to1_1bit_43_out_4, mux_2to1_1bit_44_out_4,
       mux_2to1_1bit_45_out_4, mux_2to1_1bit_46_out_4, mux_2to1_1bit_47_out_4, mux_2to1_1bit_48_out_4,
       not_gate_1_out_2, or_gate_1_out_3, or_gate_2_out_3, or_gate_3_out_3, or_gate_4_out_3, or_gate_5_out_3,
       or_gate_6_out_3, or_gate_7_out_3, or_gate_8_out_3, or_gate_9_out_3, or_gate_10_out_3,
       or_gate_11_out_3, pull_resistor_1_node;
  wire [15:0] mux_2to1_1bit_49_out_4;

  Pull_Resistor pull_resistor_1 (.node(pull_resistor_1_node));
  Mux_2to1_1bit mux_2to1_1bit_1 (.in_1(in_1[0]), .in_2(in_1[1]), .in_3(in_2[0]), .out_4(mux_2to1_1bit_1_out_4));
  Mux_2to1_1bit mux_2to1_1bit_2 (.in_1(in_1[1]), .in_2(in_1[2]), .in_3(in_2[0]), .out_4(mux_2to1_1bit_2_out_4));
  Mux_2to1_1bit mux_2to1_1bit_3 (.in_1(in_1[2]), .in_2(in_1[3]), .in_3(in_2[0]), .out_4(mux_2to1_1bit_3_out_4));
  Mux_2to1_1bit mux_2to1_1bit_4 (.in_1(in_1[3]), .in_2(in_1[4]), .in_3(in_2[0]), .out_4(mux_2to1_1bit_4_out_4));
  Mux_2to1_1bit mux_2to1_1bit_5 (.in_1(in_1[4]), .in_2(in_1[5]), .in_3(in_2[0]), .out_4(mux_2to1_1bit_5_out_4));
  Mux_2to1_1bit mux_2to1_1bit_6 (.in_1(in_1[5]), .in_2(in_1[6]), .in_3(in_2[0]), .out_4(mux_2to1_1bit_6_out_4));
  Mux_2to1_1bit mux_2to1_1bit_7 (.in_1(in_1[6]), .in_2(in_1[7]), .in_3(in_2[0]), .out_4(mux_2to1_1bit_7_out_4));
  Mux_2to1_1bit mux_2to1_1bit_8 (.in_1(in_1[7]), .in_2(in_1[8]), .in_3(in_2[0]), .out_4(mux_2to1_1bit_8_out_4));
  Mux_2to1_1bit mux_2to1_1bit_9 (.in_1(in_1[8]), .in_2(in_1[9]), .in_3(in_2[0]), .out_4(mux_2to1_1bit_9_out_4));
  Mux_2to1_1bit mux_2to1_1bit_10 (.in_1(in_1[9]), .in_2(in_1[10]), .in_3(in_2[0]), .out_4(mux_2to1_1bit_10_out_4));
  Mux_2to1_1bit mux_2to1_1bit_11 (.in_1(in_1[10]), .in_2(in_1[11]), .in_3(in_2[0]), .out_4(mux_2to1_1bit_11_out_4));
  Mux_2to1_1bit mux_2to1_1bit_12 (.in_1(in_1[11]), .in_2(in_1[12]), .in_3(in_2[0]), .out_4(mux_2to1_1bit_12_out_4));
  Mux_2to1_1bit mux_2to1_1bit_13 (.in_1(in_1[12]), .in_2(in_1[13]), .in_3(in_2[0]), .out_4(mux_2to1_1bit_13_out_4));
  Mux_2to1_1bit mux_2to1_1bit_14 (.in_1(in_1[13]), .in_2(in_1[14]), .in_3(in_2[0]), .out_4(mux_2to1_1bit_14_out_4));
  Mux_2to1_1bit mux_2to1_1bit_15 (.in_1(in_1[14]), .in_2(in_1[15]), .in_3(in_2[0]), .out_4(mux_2to1_1bit_15_out_4));
  Mux_2to1_1bit mux_2to1_1bit_16 (
    .in_1(in_1[15]), .in_2(pull_resistor_1_node), .in_3(in_2[0]), .out_4(mux_2to1_1bit_16_out_4));
  OR_Gate or_gate_1 (.in_1(in_2[4]), .in_2(in_2[5]), .out_3(or_gate_1_out_3));
  OR_Gate or_gate_2 (.in_1(in_2[6]), .in_2(in_2[7]), .out_3(or_gate_2_out_3));
  OR_Gate or_gate_3 (.in_1(in_2[8]), .in_2(in_2[9]), .out_3(or_gate_3_out_3));
  OR_Gate or_gate_4 (.in_1(in_2[10]), .in_2(in_2[11]), .out_3(or_gate_4_out_3));
  OR_Gate or_gate_5 (.in_1(in_2[12]), .in_2(in_2[13]), .out_3(or_gate_5_out_3));
  OR_Gate or_gate_6 (.in_1(in_2[14]), .in_2(in_2[15]), .out_3(or_gate_6_out_3));
  OR_Gate or_gate_7 (.in_1(or_gate_1_out_3), .in_2(or_gate_2_out_3), .out_3(or_gate_7_out_3));
  OR_Gate or_gate_8 (.in_1(or_gate_3_out_3), .in_2(or_gate_4_out_3), .out_3(or_gate_8_out_3));
  OR_Gate or_gate_9 (.in_1(or_gate_5_out_3), .in_2(or_gate_6_out_3), .out_3(or_gate_9_out_3));
  Mux_2to1_1bit mux_2to1_1bit_17 (
    .in_1(mux_2to1_1bit_1_out_4), .in_2(mux_2to1_1bit_3_out_4), .in_3(in_2[1]), .out_4(mux_2to1_1bit_17_out_4));
  Mux_2to1_1bit mux_2to1_1bit_18 (
    .in_1(mux_2to1_1bit_2_out_4), .in_2(mux_2to1_1bit_4_out_4), .in_3(in_2[1]), .out_4(mux_2to1_1bit_18_out_4));
  Mux_2to1_1bit mux_2to1_1bit_19 (
    .in_1(mux_2to1_1bit_3_out_4), .in_2(mux_2to1_1bit_5_out_4), .in_3(in_2[1]), .out_4(mux_2to1_1bit_19_out_4));
  Mux_2to1_1bit mux_2to1_1bit_20 (
    .in_1(mux_2to1_1bit_4_out_4), .in_2(mux_2to1_1bit_6_out_4), .in_3(in_2[1]), .out_4(mux_2to1_1bit_20_out_4));
  Mux_2to1_1bit mux_2to1_1bit_21 (
    .in_1(mux_2to1_1bit_5_out_4), .in_2(mux_2to1_1bit_7_out_4), .in_3(in_2[1]), .out_4(mux_2to1_1bit_21_out_4));
  Mux_2to1_1bit mux_2to1_1bit_22 (
    .in_1(mux_2to1_1bit_6_out_4), .in_2(mux_2to1_1bit_8_out_4), .in_3(in_2[1]), .out_4(mux_2to1_1bit_22_out_4));
  Mux_2to1_1bit mux_2to1_1bit_23 (
    .in_1(mux_2to1_1bit_7_out_4), .in_2(mux_2to1_1bit_9_out_4), .in_3(in_2[1]), .out_4(mux_2to1_1bit_23_out_4));
  Mux_2to1_1bit mux_2to1_1bit_24 (
    .in_1(mux_2to1_1bit_8_out_4), .in_2(mux_2to1_1bit_10_out_4), .in_3(in_2[1]),
    .out_4(mux_2to1_1bit_24_out_4));
  Mux_2to1_1bit mux_2to1_1bit_25 (
    .in_1(mux_2to1_1bit_9_out_4), .in_2(mux_2to1_1bit_11_out_4), .in_3(in_2[1]),
    .out_4(mux_2to1_1bit_25_out_4));
  Mux_2to1_1bit mux_2to1_1bit_26 (
    .in_1(mux_2to1_1bit_10_out_4), .in_2(mux_2to1_1bit_12_out_4), .in_3(in_2[1]),
    .out_4(mux_2to1_1bit_26_out_4));
  Mux_2to1_1bit mux_2to1_1bit_27 (
    .in_1(mux_2to1_1bit_11_out_4), .in_2(mux_2to1_1bit_13_out_4), .in_3(in_2[1]),
    .out_4(mux_2to1_1bit_27_out_4));
  Mux_2to1_1bit mux_2to1_1bit_28 (
    .in_1(mux_2to1_1bit_12_out_4), .in_2(mux_2to1_1bit_14_out_4), .in_3(in_2[1]),
    .out_4(mux_2to1_1bit_28_out_4));
  Mux_2to1_1bit mux_2to1_1bit_29 (
    .in_1(mux_2to1_1bit_13_out_4), .in_2(mux_2to1_1bit_15_out_4), .in_3(in_2[1]),
    .out_4(mux_2to1_1bit_29_out_4));
  Mux_2to1_1bit mux_2to1_1bit_30 (
    .in_1(mux_2to1_1bit_14_out_4), .in_2(mux_2to1_1bit_16_out_4), .in_3(in_2[1]),
    .out_4(mux_2to1_1bit_30_out_4));
  Mux_2to1_1bit mux_2to1_1bit_31 (
    .in_1(mux_2to1_1bit_15_out_4), .in_2(pull_resistor_1_node), .in_3(in_2[1]), .out_4(mux_2to1_1bit_31_out_4));
  Mux_2to1_1bit mux_2to1_1bit_32 (
    .in_1(mux_2to1_1bit_16_out_4), .in_2(pull_resistor_1_node), .in_3(in_2[1]), .out_4(mux_2to1_1bit_32_out_4));
  OR_Gate or_gate_10 (.in_1(or_gate_7_out_3), .in_2(or_gate_8_out_3), .out_3(or_gate_10_out_3));
  Mux_2to1_1bit mux_2to1_1bit_33 (
    .in_1(mux_2to1_1bit_17_out_4), .in_2(mux_2to1_1bit_21_out_4), .in_3(in_2[2]),
    .out_4(mux_2to1_1bit_33_out_4));
  Mux_2to1_1bit mux_2to1_1bit_34 (
    .in_1(mux_2to1_1bit_18_out_4), .in_2(mux_2to1_1bit_22_out_4), .in_3(in_2[2]),
    .out_4(mux_2to1_1bit_34_out_4));
  Mux_2to1_1bit mux_2to1_1bit_35 (
    .in_1(mux_2to1_1bit_19_out_4), .in_2(mux_2to1_1bit_23_out_4), .in_3(in_2[2]),
    .out_4(mux_2to1_1bit_35_out_4));
  Mux_2to1_1bit mux_2to1_1bit_36 (
    .in_1(mux_2to1_1bit_20_out_4), .in_2(mux_2to1_1bit_24_out_4), .in_3(in_2[2]),
    .out_4(mux_2to1_1bit_36_out_4));
  Mux_2to1_1bit mux_2to1_1bit_37 (
    .in_1(mux_2to1_1bit_21_out_4), .in_2(mux_2to1_1bit_25_out_4), .in_3(in_2[2]),
    .out_4(mux_2to1_1bit_37_out_4));
  Mux_2to1_1bit mux_2to1_1bit_38 (
    .in_1(mux_2to1_1bit_22_out_4), .in_2(mux_2to1_1bit_26_out_4), .in_3(in_2[2]),
    .out_4(mux_2to1_1bit_38_out_4));
  Mux_2to1_1bit mux_2to1_1bit_39 (
    .in_1(mux_2to1_1bit_23_out_4), .in_2(mux_2to1_1bit_27_out_4), .in_3(in_2[2]),
    .out_4(mux_2to1_1bit_39_out_4));
  Mux_2to1_1bit mux_2to1_1bit_40 (
    .in_1(mux_2to1_1bit_24_out_4), .in_2(mux_2to1_1bit_28_out_4), .in_3(in_2[2]),
    .out_4(mux_2to1_1bit_40_out_4));
  Mux_2to1_1bit mux_2to1_1bit_41 (
    .in_1(mux_2to1_1bit_25_out_4), .in_2(mux_2to1_1bit_29_out_4), .in_3(in_2[2]),
    .out_4(mux_2to1_1bit_41_out_4));
  Mux_2to1_1bit mux_2to1_1bit_42 (
    .in_1(mux_2to1_1bit_26_out_4), .in_2(mux_2to1_1bit_30_out_4), .in_3(in_2[2]),
    .out_4(mux_2to1_1bit_42_out_4));
  Mux_2to1_1bit mux_2to1_1bit_43 (
    .in_1(mux_2to1_1bit_27_out_4), .in_2(mux_2to1_1bit_31_out_4), .in_3(in_2[2]),
    .out_4(mux_2to1_1bit_43_out_4));
  Mux_2to1_1bit mux_2to1_1bit_44 (
    .in_1(mux_2to1_1bit_28_out_4), .in_2(mux_2to1_1bit_32_out_4), .in_3(in_2[2]),
    .out_4(mux_2to1_1bit_44_out_4));
  Mux_2to1_1bit mux_2to1_1bit_45 (
    .in_1(mux_2to1_1bit_29_out_4), .in_2(pull_resistor_1_node), .in_3(in_2[2]), .out_4(mux_2to1_1bit_45_out_4));
  Mux_2to1_1bit mux_2to1_1bit_46 (
    .in_1(mux_2to1_1bit_30_out_4), .in_2(pull_resistor_1_node), .in_3(in_2[2]), .out_4(mux_2to1_1bit_46_out_4));
  Mux_2to1_1bit mux_2to1_1bit_47 (
    .in_1(mux_2to1_1bit_31_out_4), .in_2(pull_resistor_1_node), .in_3(in_2[2]), .out_4(mux_2to1_1bit_47_out_4));
  Mux_2to1_1bit mux_2to1_1bit_48 (
    .in_1(mux_2to1_1bit_32_out_4), .in_2(pull_resistor_1_node), .in_3(in_2[2]), .out_4(mux_2to1_1bit_48_out_4));
  OR_Gate or_gate_11 (.in_1(or_gate_10_out_3), .in_2(or_gate_9_out_3), .out_3(or_gate_11_out_3));
  Mux_2to1_1bit mux_2to1_1bit_49 (
    .in_1(mux_2to1_1bit_33_out_4), .in_2(mux_2to1_1bit_41_out_4), .in_3(in_2[3]),
    .out_4(mux_2to1_1bit_49_out_4[0]));
  Mux_2to1_1bit mux_2to1_1bit_50 (
    .in_1(mux_2to1_1bit_34_out_4), .in_2(mux_2to1_1bit_42_out_4), .in_3(in_2[3]),
    .out_4(mux_2to1_1bit_49_out_4[1]));
  Mux_2to1_1bit mux_2to1_1bit_51 (
    .in_1(mux_2to1_1bit_35_out_4), .in_2(mux_2to1_1bit_43_out_4), .in_3(in_2[3]),
    .out_4(mux_2to1_1bit_49_out_4[2]));
  Mux_2to1_1bit mux_2to1_1bit_52 (
    .in_1(mux_2to1_1bit_36_out_4), .in_2(mux_2to1_1bit_44_out_4), .in_3(in_2[3]),
    .out_4(mux_2to1_1bit_49_out_4[3]));
  Mux_2to1_1bit mux_2to1_1bit_53 (
    .in_1(mux_2to1_1bit_37_out_4), .in_2(mux_2to1_1bit_45_out_4), .in_3(in_2[3]),
    .out_4(mux_2to1_1bit_49_out_4[4]));
  Mux_2to1_1bit mux_2to1_1bit_54 (
    .in_1(mux_2to1_1bit_38_out_4), .in_2(mux_2to1_1bit_46_out_4), .in_3(in_2[3]),
    .out_4(mux_2to1_1bit_49_out_4[5]));
  Mux_2to1_1bit mux_2to1_1bit_55 (
    .in_1(mux_2to1_1bit_39_out_4), .in_2(mux_2to1_1bit_47_out_4), .in_3(in_2[3]),
    .out_4(mux_2to1_1bit_49_out_4[6]));
  Mux_2to1_1bit mux_2to1_1bit_56 (
    .in_1(mux_2to1_1bit_40_out_4), .in_2(mux_2to1_1bit_48_out_4), .in_3(in_2[3]),
    .out_4(mux_2to1_1bit_49_out_4[7]));
  Mux_2to1_1bit mux_2to1_1bit_57 (
    .in_1(mux_2to1_1bit_41_out_4), .in_2(pull_resistor_1_node), .in_3(in_2[3]),
    .out_4(mux_2to1_1bit_49_out_4[8]));
  Mux_2to1_1bit mux_2to1_1bit_58 (
    .in_1(mux_2to1_1bit_42_out_4), .in_2(pull_resistor_1_node), .in_3(in_2[3]),
    .out_4(mux_2to1_1bit_49_out_4[9]));
  Mux_2to1_1bit mux_2to1_1bit_59 (
    .in_1(mux_2to1_1bit_43_out_4), .in_2(pull_resistor_1_node), .in_3(in_2[3]),
    .out_4(mux_2to1_1bit_49_out_4[10]));
  Mux_2to1_1bit mux_2to1_1bit_60 (
    .in_1(mux_2to1_1bit_44_out_4), .in_2(pull_resistor_1_node), .in_3(in_2[3]),
    .out_4(mux_2to1_1bit_49_out_4[11]));
  Mux_2to1_1bit mux_2to1_1bit_61 (
    .in_1(mux_2to1_1bit_45_out_4), .in_2(pull_resistor_1_node), .in_3(in_2[3]),
    .out_4(mux_2to1_1bit_49_out_4[12]));
  Mux_2to1_1bit mux_2to1_1bit_62 (
    .in_1(mux_2to1_1bit_46_out_4), .in_2(pull_resistor_1_node), .in_3(in_2[3]),
    .out_4(mux_2to1_1bit_49_out_4[13]));
  Mux_2to1_1bit mux_2to1_1bit_63 (
    .in_1(mux_2to1_1bit_47_out_4), .in_2(pull_resistor_1_node), .in_3(in_2[3]),
    .out_4(mux_2to1_1bit_49_out_4[14]));
  Mux_2to1_1bit mux_2to1_1bit_64 (
    .in_1(mux_2to1_1bit_48_out_4), .in_2(pull_resistor_1_node), .in_3(in_2[3]),
    .out_4(mux_2to1_1bit_49_out_4[15]));
  NOT_Gate not_gate_1 (.in_1(or_gate_11_out_3), .out_2(not_gate_1_out_2));
  Controled_Buffer_16bits controled_buffer_16bits_1 (
    .in_1(not_gate_1_out_2), .in_2(mux_2to1_1bit_49_out_4), .out_3(out_3));
  Pull_Resistor pull_resistor_2 (.node(out_3));
endmodule

module Left_bitShifter_16bits (
  input  [15:0] in_1,
  input  [15:0] in_2,
  output [15:0] out_3
);

  wire mux_2to1_1bit_1_out_4, mux_2to1_1bit_2_out_4, mux_2to1_1bit_3_out_4, mux_2to1_1bit_4_out_4,
       mux_2to1_1bit_5_out_4, mux_2to1_1bit_6_out_4, mux_2to1_1bit_7_out_4, mux_2to1_1bit_8_out_4,
       mux_2to1_1bit_9_out_4, mux_2to1_1bit_10_out_4, mux_2to1_1bit_11_out_4, mux_2to1_1bit_12_out_4,
       mux_2to1_1bit_13_out_4, mux_2to1_1bit_14_out_4, mux_2to1_1bit_15_out_4, mux_2to1_1bit_16_out_4,
       mux_2to1_1bit_17_out_4, mux_2to1_1bit_18_out_4, mux_2to1_1bit_19_out_4, mux_2to1_1bit_20_out_4,
       mux_2to1_1bit_21_out_4, mux_2to1_1bit_22_out_4, mux_2to1_1bit_23_out_4, mux_2to1_1bit_24_out_4,
       mux_2to1_1bit_25_out_4, mux_2to1_1bit_26_out_4, mux_2to1_1bit_27_out_4, mux_2to1_1bit_28_out_4,
       mux_2to1_1bit_29_out_4, mux_2to1_1bit_30_out_4, mux_2to1_1bit_31_out_4, mux_2to1_1bit_32_out_4,
       mux_2to1_1bit_33_out_4, mux_2to1_1bit_34_out_4, mux_2to1_1bit_35_out_4, mux_2to1_1bit_36_out_4,
       mux_2to1_1bit_37_out_4, mux_2to1_1bit_38_out_4, mux_2to1_1bit_39_out_4, mux_2to1_1bit_40_out_4,
       mux_2to1_1bit_41_out_4, mux_2to1_1bit_42_out_4, mux_2to1_1bit_43_out_4, mux_2to1_1bit_44_out_4,
       mux_2to1_1bit_45_out_4, mux_2to1_1bit_46_out_4, mux_2to1_1bit_47_out_4, mux_2to1_1bit_48_out_4,
       not_gate_1_out_2, or_gate_1_out_3, or_gate_2_out_3, or_gate_3_out_3, or_gate_4_out_3, or_gate_5_out_3,
       or_gate_6_out_3, or_gate_7_out_3, or_gate_8_out_3, or_gate_9_out_3, or_gate_10_out_3,
       or_gate_11_out_3, pull_resistor_1_node;
  wire [15:0] mux_2to1_1bit_49_out_4;

  Pull_Resistor pull_resistor_1 (.node(pull_resistor_1_node));
  Mux_2to1_1bit mux_2to1_1bit_1 (
    .in_1(in_1[0]), .in_2(pull_resistor_1_node), .in_3(in_2[0]), .out_4(mux_2to1_1bit_1_out_4));
  Mux_2to1_1bit mux_2to1_1bit_2 (.in_1(in_1[1]), .in_2(in_1[0]), .in_3(in_2[0]), .out_4(mux_2to1_1bit_2_out_4));
  Mux_2to1_1bit mux_2to1_1bit_3 (.in_1(in_1[2]), .in_2(in_1[1]), .in_3(in_2[0]), .out_4(mux_2to1_1bit_3_out_4));
  Mux_2to1_1bit mux_2to1_1bit_4 (.in_1(in_1[3]), .in_2(in_1[2]), .in_3(in_2[0]), .out_4(mux_2to1_1bit_4_out_4));
  Mux_2to1_1bit mux_2to1_1bit_5 (.in_1(in_1[4]), .in_2(in_1[3]), .in_3(in_2[0]), .out_4(mux_2to1_1bit_5_out_4));
  Mux_2to1_1bit mux_2to1_1bit_6 (.in_1(in_1[5]), .in_2(in_1[4]), .in_3(in_2[0]), .out_4(mux_2to1_1bit_6_out_4));
  Mux_2to1_1bit mux_2to1_1bit_7 (.in_1(in_1[6]), .in_2(in_1[5]), .in_3(in_2[0]), .out_4(mux_2to1_1bit_7_out_4));
  Mux_2to1_1bit mux_2to1_1bit_8 (.in_1(in_1[7]), .in_2(in_1[6]), .in_3(in_2[0]), .out_4(mux_2to1_1bit_8_out_4));
  Mux_2to1_1bit mux_2to1_1bit_9 (.in_1(in_1[8]), .in_2(in_1[7]), .in_3(in_2[0]), .out_4(mux_2to1_1bit_9_out_4));
  Mux_2to1_1bit mux_2to1_1bit_10 (.in_1(in_1[9]), .in_2(in_1[8]), .in_3(in_2[0]), .out_4(mux_2to1_1bit_10_out_4));
  Mux_2to1_1bit mux_2to1_1bit_11 (.in_1(in_1[10]), .in_2(in_1[9]), .in_3(in_2[0]), .out_4(mux_2to1_1bit_11_out_4));
  Mux_2to1_1bit mux_2to1_1bit_12 (.in_1(in_1[11]), .in_2(in_1[10]), .in_3(in_2[0]), .out_4(mux_2to1_1bit_12_out_4));
  Mux_2to1_1bit mux_2to1_1bit_13 (.in_1(in_1[12]), .in_2(in_1[11]), .in_3(in_2[0]), .out_4(mux_2to1_1bit_13_out_4));
  Mux_2to1_1bit mux_2to1_1bit_14 (.in_1(in_1[13]), .in_2(in_1[12]), .in_3(in_2[0]), .out_4(mux_2to1_1bit_14_out_4));
  Mux_2to1_1bit mux_2to1_1bit_15 (.in_1(in_1[14]), .in_2(in_1[13]), .in_3(in_2[0]), .out_4(mux_2to1_1bit_15_out_4));
  Mux_2to1_1bit mux_2to1_1bit_16 (.in_1(in_1[15]), .in_2(in_1[14]), .in_3(in_2[0]), .out_4(mux_2to1_1bit_16_out_4));
  OR_Gate or_gate_1 (.in_1(in_2[4]), .in_2(in_2[5]), .out_3(or_gate_1_out_3));
  OR_Gate or_gate_2 (.in_1(in_2[6]), .in_2(in_2[7]), .out_3(or_gate_2_out_3));
  OR_Gate or_gate_3 (.in_1(in_2[8]), .in_2(in_2[9]), .out_3(or_gate_3_out_3));
  OR_Gate or_gate_4 (.in_1(in_2[10]), .in_2(in_2[11]), .out_3(or_gate_4_out_3));
  OR_Gate or_gate_5 (.in_1(in_2[12]), .in_2(in_2[13]), .out_3(or_gate_5_out_3));
  OR_Gate or_gate_6 (.in_1(in_2[14]), .in_2(in_2[15]), .out_3(or_gate_6_out_3));
  OR_Gate or_gate_7 (.in_1(or_gate_1_out_3), .in_2(or_gate_2_out_3), .out_3(or_gate_7_out_3));
  OR_Gate or_gate_8 (.in_1(or_gate_3_out_3), .in_2(or_gate_4_out_3), .out_3(or_gate_8_out_3));
  OR_Gate or_gate_9 (.in_1(or_gate_5_out_3), .in_2(or_gate_6_out_3), .out_3(or_gate_9_out_3));
  Mux_2to1_1bit mux_2to1_1bit_17 (
    .in_1(mux_2to1_1bit_1_out_4), .in_2(pull_resistor_1_node), .in_3(in_2[1]), .out_4(mux_2to1_1bit_17_out_4));
  Mux_2to1_1bit mux_2to1_1bit_18 (
    .in_1(mux_2to1_1bit_2_out_4), .in_2(pull_resistor_1_node), .in_3(in_2[1]), .out_4(mux_2to1_1bit_18_out_4));
  Mux_2to1_1bit mux_2to1_1bit_19 (
    .in_1(mux_2to1_1bit_3_out_4), .in_2(mux_2to1_1bit_1_out_4), .in_3(in_2[1]), .out_4(mux_2to1_1bit_19_out_4));
  Mux_2to1_1bit mux_2to1_1bit_20 (
    .in_1(mux_2to1_1bit_4_out_4), .in_2(mux_2to1_1bit_2_out_4), .in_3(in_2[1]), .out_4(mux_2to1_1bit_20_out_4));
  Mux_2to1_1bit mux_2to1_1bit_21 (
    .in_1(mux_2to1_1bit_5_out_4), .in_2(mux_2to1_1bit_3_out_4), .in_3(in_2[1]), .out_4(mux_2to1_1bit_21_out_4));
  Mux_2to1_1bit mux_2to1_1bit_22 (
    .in_1(mux_2to1_1bit_6_out_4), .in_2(mux_2to1_1bit_4_out_4), .in_3(in_2[1]), .out_4(mux_2to1_1bit_22_out_4));
  Mux_2to1_1bit mux_2to1_1bit_23 (
    .in_1(mux_2to1_1bit_7_out_4), .in_2(mux_2to1_1bit_5_out_4), .in_3(in_2[1]), .out_4(mux_2to1_1bit_23_out_4));
  Mux_2to1_1bit mux_2to1_1bit_24 (
    .in_1(mux_2to1_1bit_8_out_4), .in_2(mux_2to1_1bit_6_out_4), .in_3(in_2[1]), .out_4(mux_2to1_1bit_24_out_4));
  Mux_2to1_1bit mux_2to1_1bit_25 (
    .in_1(mux_2to1_1bit_9_out_4), .in_2(mux_2to1_1bit_7_out_4), .in_3(in_2[1]), .out_4(mux_2to1_1bit_25_out_4));
  Mux_2to1_1bit mux_2to1_1bit_26 (
    .in_1(mux_2to1_1bit_10_out_4), .in_2(mux_2to1_1bit_8_out_4), .in_3(in_2[1]),
    .out_4(mux_2to1_1bit_26_out_4));
  Mux_2to1_1bit mux_2to1_1bit_27 (
    .in_1(mux_2to1_1bit_11_out_4), .in_2(mux_2to1_1bit_9_out_4), .in_3(in_2[1]),
    .out_4(mux_2to1_1bit_27_out_4));
  Mux_2to1_1bit mux_2to1_1bit_28 (
    .in_1(mux_2to1_1bit_12_out_4), .in_2(mux_2to1_1bit_10_out_4), .in_3(in_2[1]),
    .out_4(mux_2to1_1bit_28_out_4));
  Mux_2to1_1bit mux_2to1_1bit_29 (
    .in_1(mux_2to1_1bit_13_out_4), .in_2(mux_2to1_1bit_11_out_4), .in_3(in_2[1]),
    .out_4(mux_2to1_1bit_29_out_4));
  Mux_2to1_1bit mux_2to1_1bit_30 (
    .in_1(mux_2to1_1bit_14_out_4), .in_2(mux_2to1_1bit_12_out_4), .in_3(in_2[1]),
    .out_4(mux_2to1_1bit_30_out_4));
  Mux_2to1_1bit mux_2to1_1bit_31 (
    .in_1(mux_2to1_1bit_15_out_4), .in_2(mux_2to1_1bit_13_out_4), .in_3(in_2[1]),
    .out_4(mux_2to1_1bit_31_out_4));
  Mux_2to1_1bit mux_2to1_1bit_32 (
    .in_1(mux_2to1_1bit_16_out_4), .in_2(mux_2to1_1bit_14_out_4), .in_3(in_2[1]),
    .out_4(mux_2to1_1bit_32_out_4));
  OR_Gate or_gate_10 (.in_1(or_gate_7_out_3), .in_2(or_gate_8_out_3), .out_3(or_gate_10_out_3));
  Mux_2to1_1bit mux_2to1_1bit_33 (
    .in_1(mux_2to1_1bit_17_out_4), .in_2(pull_resistor_1_node), .in_3(in_2[2]), .out_4(mux_2to1_1bit_33_out_4));
  Mux_2to1_1bit mux_2to1_1bit_34 (
    .in_1(mux_2to1_1bit_18_out_4), .in_2(pull_resistor_1_node), .in_3(in_2[2]), .out_4(mux_2to1_1bit_34_out_4));
  Mux_2to1_1bit mux_2to1_1bit_35 (
    .in_1(mux_2to1_1bit_19_out_4), .in_2(pull_resistor_1_node), .in_3(in_2[2]), .out_4(mux_2to1_1bit_35_out_4));
  Mux_2to1_1bit mux_2to1_1bit_36 (
    .in_1(mux_2to1_1bit_20_out_4), .in_2(pull_resistor_1_node), .in_3(in_2[2]), .out_4(mux_2to1_1bit_36_out_4));
  Mux_2to1_1bit mux_2to1_1bit_37 (
    .in_1(mux_2to1_1bit_21_out_4), .in_2(mux_2to1_1bit_17_out_4), .in_3(in_2[2]),
    .out_4(mux_2to1_1bit_37_out_4));
  Mux_2to1_1bit mux_2to1_1bit_38 (
    .in_1(mux_2to1_1bit_22_out_4), .in_2(mux_2to1_1bit_18_out_4), .in_3(in_2[2]),
    .out_4(mux_2to1_1bit_38_out_4));
  Mux_2to1_1bit mux_2to1_1bit_39 (
    .in_1(mux_2to1_1bit_23_out_4), .in_2(mux_2to1_1bit_19_out_4), .in_3(in_2[2]),
    .out_4(mux_2to1_1bit_39_out_4));
  Mux_2to1_1bit mux_2to1_1bit_40 (
    .in_1(mux_2to1_1bit_24_out_4), .in_2(mux_2to1_1bit_20_out_4), .in_3(in_2[2]),
    .out_4(mux_2to1_1bit_40_out_4));
  Mux_2to1_1bit mux_2to1_1bit_41 (
    .in_1(mux_2to1_1bit_25_out_4), .in_2(mux_2to1_1bit_21_out_4), .in_3(in_2[2]),
    .out_4(mux_2to1_1bit_41_out_4));
  Mux_2to1_1bit mux_2to1_1bit_42 (
    .in_1(mux_2to1_1bit_26_out_4), .in_2(mux_2to1_1bit_22_out_4), .in_3(in_2[2]),
    .out_4(mux_2to1_1bit_42_out_4));
  Mux_2to1_1bit mux_2to1_1bit_43 (
    .in_1(mux_2to1_1bit_27_out_4), .in_2(mux_2to1_1bit_23_out_4), .in_3(in_2[2]),
    .out_4(mux_2to1_1bit_43_out_4));
  Mux_2to1_1bit mux_2to1_1bit_44 (
    .in_1(mux_2to1_1bit_28_out_4), .in_2(mux_2to1_1bit_24_out_4), .in_3(in_2[2]),
    .out_4(mux_2to1_1bit_44_out_4));
  Mux_2to1_1bit mux_2to1_1bit_45 (
    .in_1(mux_2to1_1bit_29_out_4), .in_2(mux_2to1_1bit_25_out_4), .in_3(in_2[2]),
    .out_4(mux_2to1_1bit_45_out_4));
  Mux_2to1_1bit mux_2to1_1bit_46 (
    .in_1(mux_2to1_1bit_30_out_4), .in_2(mux_2to1_1bit_26_out_4), .in_3(in_2[2]),
    .out_4(mux_2to1_1bit_46_out_4));
  Mux_2to1_1bit mux_2to1_1bit_47 (
    .in_1(mux_2to1_1bit_31_out_4), .in_2(mux_2to1_1bit_27_out_4), .in_3(in_2[2]),
    .out_4(mux_2to1_1bit_47_out_4));
  Mux_2to1_1bit mux_2to1_1bit_48 (
    .in_1(mux_2to1_1bit_32_out_4), .in_2(mux_2to1_1bit_29_out_4), .in_3(in_2[2]),
    .out_4(mux_2to1_1bit_48_out_4));
  OR_Gate or_gate_11 (.in_1(or_gate_10_out_3), .in_2(or_gate_9_out_3), .out_3(or_gate_11_out_3));
  Mux_2to1_1bit mux_2to1_1bit_49 (
    .in_1(mux_2to1_1bit_33_out_4), .in_2(pull_resistor_1_node), .in_3(in_2[3]),
    .out_4(mux_2to1_1bit_49_out_4[0]));
  Mux_2to1_1bit mux_2to1_1bit_50 (
    .in_1(mux_2to1_1bit_34_out_4), .in_2(pull_resistor_1_node), .in_3(in_2[3]),
    .out_4(mux_2to1_1bit_49_out_4[1]));
  Mux_2to1_1bit mux_2to1_1bit_51 (
    .in_1(mux_2to1_1bit_35_out_4), .in_2(pull_resistor_1_node), .in_3(in_2[3]),
    .out_4(mux_2to1_1bit_49_out_4[2]));
  Mux_2to1_1bit mux_2to1_1bit_52 (
    .in_1(mux_2to1_1bit_36_out_4), .in_2(pull_resistor_1_node), .in_3(in_2[3]),
    .out_4(mux_2to1_1bit_49_out_4[3]));
  Mux_2to1_1bit mux_2to1_1bit_53 (
    .in_1(mux_2to1_1bit_37_out_4), .in_2(pull_resistor_1_node), .in_3(in_2[3]),
    .out_4(mux_2to1_1bit_49_out_4[4]));
  Mux_2to1_1bit mux_2to1_1bit_54 (
    .in_1(mux_2to1_1bit_38_out_4), .in_2(pull_resistor_1_node), .in_3(in_2[3]),
    .out_4(mux_2to1_1bit_49_out_4[5]));
  Mux_2to1_1bit mux_2to1_1bit_55 (
    .in_1(mux_2to1_1bit_39_out_4), .in_2(pull_resistor_1_node), .in_3(in_2[3]),
    .out_4(mux_2to1_1bit_49_out_4[6]));
  Mux_2to1_1bit mux_2to1_1bit_56 (
    .in_1(mux_2to1_1bit_40_out_4), .in_2(pull_resistor_1_node), .in_3(in_2[3]),
    .out_4(mux_2to1_1bit_49_out_4[7]));
  Mux_2to1_1bit mux_2to1_1bit_57 (
    .in_1(mux_2to1_1bit_41_out_4), .in_2(mux_2to1_1bit_33_out_4), .in_3(in_2[3]),
    .out_4(mux_2to1_1bit_49_out_4[8]));
  Mux_2to1_1bit mux_2to1_1bit_58 (
    .in_1(mux_2to1_1bit_42_out_4), .in_2(mux_2to1_1bit_34_out_4), .in_3(in_2[3]),
    .out_4(mux_2to1_1bit_49_out_4[9]));
  Mux_2to1_1bit mux_2to1_1bit_59 (
    .in_1(mux_2to1_1bit_43_out_4), .in_2(mux_2to1_1bit_35_out_4), .in_3(in_2[3]),
    .out_4(mux_2to1_1bit_49_out_4[10]));
  Mux_2to1_1bit mux_2to1_1bit_60 (
    .in_1(mux_2to1_1bit_44_out_4), .in_2(mux_2to1_1bit_36_out_4), .in_3(in_2[3]),
    .out_4(mux_2to1_1bit_49_out_4[11]));
  Mux_2to1_1bit mux_2to1_1bit_61 (
    .in_1(mux_2to1_1bit_45_out_4), .in_2(mux_2to1_1bit_37_out_4), .in_3(in_2[3]),
    .out_4(mux_2to1_1bit_49_out_4[12]));
  Mux_2to1_1bit mux_2to1_1bit_62 (
    .in_1(mux_2to1_1bit_46_out_4), .in_2(mux_2to1_1bit_38_out_4), .in_3(in_2[3]),
    .out_4(mux_2to1_1bit_49_out_4[13]));
  Mux_2to1_1bit mux_2to1_1bit_63 (
    .in_1(mux_2to1_1bit_47_out_4), .in_2(mux_2to1_1bit_39_out_4), .in_3(in_2[3]),
    .out_4(mux_2to1_1bit_49_out_4[14]));
  Mux_2to1_1bit mux_2to1_1bit_64 (
    .in_1(mux_2to1_1bit_48_out_4), .in_2(mux_2to1_1bit_40_out_4), .in_3(in_2[3]),
    .out_4(mux_2to1_1bit_49_out_4[15]));
  NOT_Gate not_gate_1 (.in_1(or_gate_11_out_3), .out_2(not_gate_1_out_2));
  Controled_Buffer_16bits controled_buffer_16bits_1 (
    .in_1(not_gate_1_out_2), .in_2(mux_2to1_1bit_49_out_4), .out_3(out_3));
  Pull_Resistor pull_resistor_2 (.node(out_3));
endmodule

module Mux_2to1_1bit (
  input  in_1,
  input  in_2,
  input  in_3,
  output out_4
);

  wire and_gate_1_out_3, and_gate_2_out_3, not_gate_1_out_2;

  NOT_Gate not_gate_1 (.in_1(in_3), .out_2(not_gate_1_out_2));
  AND_Gate and_gate_1 (.in_1(in_1), .in_2(not_gate_1_out_2), .out_3(and_gate_1_out_3));
  AND_Gate and_gate_2 (.in_1(in_2), .in_2(in_3), .out_3(and_gate_2_out_3));
  OR_Gate or_gate_1 (.in_1(and_gate_1_out_3), .in_2(and_gate_2_out_3), .out_3(out_4));
endmodule

module Controled_Buffer_16bits (
  input  in_1,
  input  [15:0] in_2,
  output [15:0] out_3
);

  Controled_Buffer controled_buffer_1 (.in_1(in_1), .in_2(in_2[0]), .out_3(out_3[0]));
  Controled_Buffer controled_buffer_2 (.in_1(in_1), .in_2(in_2[1]), .out_3(out_3[1]));
  Controled_Buffer controled_buffer_3 (.in_1(in_1), .in_2(in_2[2]), .out_3(out_3[2]));
  Controled_Buffer controled_buffer_4 (.in_1(in_1), .in_2(in_2[3]), .out_3(out_3[3]));
  Controled_Buffer controled_buffer_5 (.in_1(in_1), .in_2(in_2[4]), .out_3(out_3[4]));
  Controled_Buffer controled_buffer_6 (.in_1(in_1), .in_2(in_2[5]), .out_3(out_3[5]));
  Controled_Buffer controled_buffer_7 (.in_1(in_1), .in_2(in_2[6]), .out_3(out_3[6]));
  Controled_Buffer controled_buffer_8 (.in_1(in_1), .in_2(in_2[7]), .out_3(out_3[7]));
  Controled_Buffer controled_buffer_9 (.in_1(in_1), .in_2(in_2[8]), .out_3(out_3[8]));
  Controled_Buffer controled_buffer_10 (.in_1(in_1), .in_2(in_2[9]), .out_3(out_3[9]));
  Controled_Buffer controled_buffer_11 (.in_1(in_1), .in_2(in_2[10]), .out_3(out_3[10]));
  Controled_Buffer controled_buffer_12 (.in_1(in_1), .in_2(in_2[11]), .out_3(out_3[11]));
  Controled_Buffer controled_buffer_13 (.in_1(in_1), .in_2(in_2[12]), .out_3(out_3[12]));
  Controled_Buffer controled_buffer_14 (.in_1(in_1), .in_2(in_2[13]), .out_3(out_3[13]));
  Controled_Buffer controled_buffer_15 (.in_1(in_1), .in_2(in_2[14]), .out_3(out_3[14]));
  Controled_Buffer controled_buffer_16 (.in_1(in_1), .in_2(in_2[15]), .out_3(out_3[15]));
endmodule

module onehotmux_6ways_16bits_WOIBC (
  input  [15:0] ADD,
  input  [15:0] X,
  input  [15:0] AN,
  input  [15:0] SUB,
  input  [15:0] RS,
  input  [15:0] LS,
  input  CADD,
  input  CX,
  input  CAN,
  input  CSUB,
  input  CRS,
  input  CLS,
  output [15:0] O
);

  wire [15:0] and_gate_16bits_1_out_3, and_gate_16bits_2_out_3, and_gate_16bits_3_out_3,
       and_gate_16bits_4_out_3, and_gate_16bits_5_out_3, and_gate_16bits_6_out_3, or_gate_16bits_1_out_3,
       or_gate_16bits_2_out_3, or_gate_16bits_3_out_3, or_gate_16bits_4_out_3;

  AND_Gate_16bits and_gate_16bits_1 (.in_1(ADD), .in_2({16{CADD}}), .out_3(and_gate_16bits_1_out_3));
  AND_Gate_16bits and_gate_16bits_2 (.in_1(X), .in_2({16{CX}}), .out_3(and_gate_16bits_2_out_3));
  AND_Gate_16bits and_gate_16bits_3 (.in_1(AN), .in_2({16{CAN}}), .out_3(and_gate_16bits_3_out_3));
  AND_Gate_16bits and_gate_16bits_4 (.in_1(SUB), .in_2({16{CSUB}}), .out_3(and_gate_16bits_4_out_3));
  AND_Gate_16bits and_gate_16bits_5 (.in_1(RS), .in_2({16{CRS}}), .out_3(and_gate_16bits_5_out_3));
  AND_Gate_16bits and_gate_16bits_6 (.in_1(LS), .in_2({16{CLS}}), .out_3(and_gate_16bits_6_out_3));
  OR_Gate_16bits or_gate_16bits_1 (
    .in_1(and_gate_16bits_1_out_3), .in_2(and_gate_16bits_2_out_3), .out_3(or_gate_16bits_1_out_3));
  OR_Gate_16bits or_gate_16bits_2 (
    .in_1(and_gate_16bits_3_out_3), .in_2(and_gate_16bits_4_out_3), .out_3(or_gate_16bits_2_out_3));
  OR_Gate_16bits or_gate_16bits_3 (
    .in_1(and_gate_16bits_5_out_3), .in_2(and_gate_16bits_6_out_3), .out_3(or_gate_16bits_3_out_3));
  OR_Gate_16bits or_gate_16bits_4 (
    .in_1(or_gate_16bits_1_out_3), .in_2(or_gate_16bits_2_out_3), .out_3(or_gate_16bits_4_out_3));
  OR_Gate_16bits or_gate_16bits_5 (.in_1(or_gate_16bits_4_out_3), .in_2(or_gate_16bits_3_out_3), .out_3(O));
endmodule

module OR_Gate_16bits (
  input  [15:0] in_1,
  input  [15:0] in_2,
  output [15:0] out_3
);

  OR_Gate or_gate_1 (.in_1(in_1[0]), .in_2(in_2[0]), .out_3(out_3[0]));
  OR_Gate or_gate_2 (.in_1(in_1[1]), .in_2(in_2[1]), .out_3(out_3[1]));
  OR_Gate or_gate_3 (.in_1(in_1[2]), .in_2(in_2[2]), .out_3(out_3[2]));
  OR_Gate or_gate_4 (.in_1(in_1[3]), .in_2(in_2[3]), .out_3(out_3[3]));
  OR_Gate or_gate_5 (.in_1(in_1[4]), .in_2(in_2[4]), .out_3(out_3[4]));
  OR_Gate or_gate_6 (.in_1(in_1[5]), .in_2(in_2[5]), .out_3(out_3[5]));
  OR_Gate or_gate_7 (.in_1(in_1[6]), .in_2(in_2[6]), .out_3(out_3[6]));
  OR_Gate or_gate_8 (.in_1(in_1[7]), .in_2(in_2[7]), .out_3(out_3[7]));
  OR_Gate or_gate_9 (.in_1(in_1[8]), .in_2(in_2[8]), .out_3(out_3[8]));
  OR_Gate or_gate_10 (.in_1(in_1[9]), .in_2(in_2[9]), .out_3(out_3[9]));
  OR_Gate or_gate_11 (.in_1(in_1[10]), .in_2(in_2[10]), .out_3(out_3[10]));
  OR_Gate or_gate_12 (.in_1(in_1[11]), .in_2(in_2[11]), .out_3(out_3[11]));
  OR_Gate or_gate_13 (.in_1(in_1[12]), .in_2(in_2[12]), .out_3(out_3[12]));
  OR_Gate or_gate_14 (.in_1(in_1[13]), .in_2(in_2[13]), .out_3(out_3[13]));
  OR_Gate or_gate_15 (.in_1(in_1[14]), .in_2(in_2[14]), .out_3(out_3[14]));
  OR_Gate or_gate_16 (.in_1(in_1[15]), .in_2(in_2[15]), .out_3(out_3[15]));
endmodule

module Sub_ODD (
  input  in_1,
  input  in_2,
  input  CIN,
  output out_4
);

  wire xor_gate_1_out_3;

  XOR_Gate xor_gate_1 (.in_1(in_1), .in_2(in_2), .out_3(xor_gate_1_out_3));
  XOR_Gate xor_gate_2 (.in_1(xor_gate_1_out_3), .in_2(CIN), .out_3(out_4));
endmodule

module Sub_MAJ (
  input  in_1,
  input  in_2,
  input  CIN,
  output out_4
);

  wire and_gate_1_out_3, and_gate_2_out_3, not_gate_1_out_2, not_gate_2_out_2, xor_gate_1_out_3;

  XOR_Gate xor_gate_1 (.in_1(in_1), .in_2(in_2), .out_3(xor_gate_1_out_3));
  NOT_Gate not_gate_1 (.in_1(in_1), .out_2(not_gate_1_out_2));
  NOT_Gate not_gate_2 (.in_1(xor_gate_1_out_3), .out_2(not_gate_2_out_2));
  AND_Gate and_gate_1 (.in_1(not_gate_2_out_2), .in_2(CIN), .out_3(and_gate_1_out_3));
  AND_Gate and_gate_2 (.in_1(not_gate_1_out_2), .in_2(in_2), .out_3(and_gate_2_out_3));
  OR_Gate or_gate_1 (.in_1(and_gate_1_out_3), .in_2(and_gate_2_out_3), .out_3(out_4));
endmodule

module Sub (
  input  in_1,
  input  in_2,
  input  in_3,
  output out_4,
  output out_5
);

  Sub_ODD sub_odd_1 (.in_1(in_1), .in_2(in_2), .CIN(in_3), .out_4(out_4));
  Sub_MAJ sub_maj_1 (.in_1(in_1), .in_2(in_2), .CIN(in_3), .out_4(out_5));
endmodule

module bank_16Registers_WOIBC (
  input  [15:0] WRITE,
  input  [3:0] AWRITE,
  input  WE,
  input  [3:0] AOUTPUT_S,
  input  OE_S,
  input  [3:0] AOUTPUT_t,
  input  OE_t,
  input  CLK,
  input  R,
  output [15:0] OUTPUT_S,
  output [15:0] OUTPUT_t
);

  wire decoder_1_out0, decoder_1_out1, decoder_1_out2, decoder_1_out3, decoder_1_out4, decoder_1_out5,
       decoder_1_out6, decoder_1_out7, decoder_1_out8, decoder_1_out9, decoder_1_out10, decoder_1_out11,
       decoder_1_out12, decoder_1_out13, decoder_1_out14, decoder_1_out15;
  wire [15:0] demultiplexer_1_out0, demultiplexer_1_out1, demultiplexer_1_out2, demultiplexer_1_out3,
       demultiplexer_1_out4, demultiplexer_1_out5, demultiplexer_1_out6, demultiplexer_1_out7,
       demultiplexer_1_out8, demultiplexer_1_out9, demultiplexer_1_out10, demultiplexer_1_out11,
       demultiplexer_1_out12, demultiplexer_1_out13, demultiplexer_1_out14, demultiplexer_1_out15,
       register_1_q, register_2_q, register_3_q, register_4_q, register_5_q, register_6_q, register_7_q,
       register_8_q, register_9_q, register_10_q, register_11_q, register_12_q, register_13_q, register_14_q,
       register_15_q, register_16_q;

  Demultiplexer #(.select(4), .width(16)) demultiplexer_1 (
    .out0(demultiplexer_1_out0), .out1(demultiplexer_1_out1), .out2(demultiplexer_1_out2),
    .out3(demultiplexer_1_out3), .out4(demultiplexer_1_out4), .out5(demultiplexer_1_out5),
    .out6(demultiplexer_1_out6), .out7(demultiplexer_1_out7), .out8(demultiplexer_1_out8),
    .out9(demultiplexer_1_out9), .out10(demultiplexer_1_out10), .out11(demultiplexer_1_out11),
    .out12(demultiplexer_1_out12), .out13(demultiplexer_1_out13), .out14(demultiplexer_1_out14),
    .out15(demultiplexer_1_out15), .in(WRITE), .sel(AWRITE));
  Decoder #(.select(4)) decoder_1 (
    .out0(decoder_1_out0), .out1(decoder_1_out1), .out2(decoder_1_out2), .out3(decoder_1_out3),
    .out4(decoder_1_out4), .out5(decoder_1_out5), .out6(decoder_1_out6), .out7(decoder_1_out7),
    .out8(decoder_1_out8), .out9(decoder_1_out9), .out10(decoder_1_out10), .out11(decoder_1_out11),
    .out12(decoder_1_out12), .out13(decoder_1_out13), .out14(decoder_1_out14), .out15(decoder_1_out15),
    .sel(AWRITE), .en(WE));
  Register #(.trigger("falling"), .width(16)) register_1 (
    .D(demultiplexer_1_out0), .en(decoder_1_out0), .clk(CLK), .Q(register_1_q), .clr(R));
  Register #(.trigger("falling"), .width(16)) register_2 (
    .D(demultiplexer_1_out4), .en(decoder_1_out4), .clk(CLK), .Q(register_2_q), .clr(R));
  Register #(.trigger("falling"), .width(16)) register_3 (
    .D(demultiplexer_1_out8), .en(decoder_1_out8), .clk(CLK), .Q(register_3_q), .clr(R));
  Register #(.trigger("falling"), .width(16)) register_4 (
    .D(demultiplexer_1_out12), .en(decoder_1_out12), .clk(CLK), .Q(register_4_q), .clr(R));
  Register #(.trigger("falling"), .width(16)) register_5 (
    .D(demultiplexer_1_out1), .en(decoder_1_out1), .clk(CLK), .Q(register_5_q), .clr(R));
  Register #(.trigger("falling"), .width(16)) register_6 (
    .D(demultiplexer_1_out5), .en(decoder_1_out5), .clk(CLK), .Q(register_6_q), .clr(R));
  Register #(.trigger("falling"), .width(16)) register_7 (
    .D(demultiplexer_1_out9), .en(decoder_1_out9), .clk(CLK), .Q(register_7_q), .clr(R));
  Register #(.trigger("falling"), .width(16)) register_8 (
    .D(demultiplexer_1_out13), .en(decoder_1_out13), .clk(CLK), .Q(register_8_q), .clr(R));
  Register #(.trigger("falling"), .width(16)) register_9 (
    .D(demultiplexer_1_out2), .en(decoder_1_out2), .clk(CLK), .Q(register_9_q), .clr(R));
  Register #(.trigger("falling"), .width(16)) register_10 (
    .D(demultiplexer_1_out6), .en(decoder_1_out6), .clk(CLK), .Q(register_10_q), .clr(R));
  Register #(.trigger("falling"), .width(16)) register_11 (
    .D(demultiplexer_1_out10), .en(decoder_1_out10), .clk(CLK), .Q(register_11_q), .clr(R));
  Register #(.trigger("falling"), .width(16)) register_12 (
    .D(demultiplexer_1_out14), .en(decoder_1_out14), .clk(CLK), .Q(register_12_q), .clr(R));
  Register #(.trigger("falling"), .width(16)) register_13 (
    .D(demultiplexer_1_out3), .en(decoder_1_out3), .clk(CLK), .Q(register_13_q), .clr(R));
  Register #(.trigger("falling"), .width(16)) register_14 (
    .D(demultiplexer_1_out7), .en(decoder_1_out7), .clk(CLK), .Q(register_14_q), .clr(R));
  Register #(.trigger("falling"), .width(16)) register_15 (
    .D(demultiplexer_1_out11), .en(decoder_1_out11), .clk(CLK), .Q(register_15_q), .clr(R));
  Register #(.trigger("falling"), .width(16)) register_16 (
    .D(demultiplexer_1_out15), .en(decoder_1_out15), .clk(CLK), .Q(register_16_q), .clr(R));
  Multiplexer #(.enable("true"), .select(4), .width(16)) multiplexer_1 (
    .in0(register_1_q), .in1(register_5_q), .in2(register_9_q), .in3(register_13_q), .in4(register_2_q),
    .in5(register_6_q), .in6(register_10_q), .in7(register_14_q), .in8(register_3_q), .in9(register_7_q),
    .in10(register_11_q), .in11(register_15_q), .in12(register_4_q), .in13(register_8_q),
    .in14(register_12_q), .in15(register_16_q), .out(OUTPUT_S), .sel(AOUTPUT_S), .en(OE_S));
  Multiplexer #(.enable("true"), .select(4), .width(16)) multiplexer_2 (
    .in0(register_1_q), .in1(register_5_q), .in2(register_9_q), .in3(register_13_q), .in4(register_2_q),
    .in5(register_6_q), .in6(register_10_q), .in7(register_14_q), .in8(register_3_q), .in9(register_7_q),
    .in10(register_11_q), .in11(register_15_q), .in12(register_4_q), .in13(register_8_q),
    .in14(register_12_q), .in15(register_16_q), .out(OUTPUT_t), .sel(AOUTPUT_t), .en(OE_t));

  // Notes on the sheet:
  //   0
  //   4
  //   8
  //   c
  //   1
  //   5
  //   9
  //   d
  //   2
  //   6
  //   a
  //   e
  //   3
  //   7
  //   b
  //   f
endmodule

module Interface (
);

  wire clock_1_out, cpu_16bits_1_a0, cpu_16bits_1_a1, cpu_16bits_1_a2, cpu_16bits_1_a3, cpu_16bits_1_a4,
       cpu_16bits_1_a5, cpu_16bits_1_a6, cpu_16bits_1_a7, cpu_16bits_1_d0, cpu_16bits_1_d1, cpu_16bits_1_d2,
       cpu_16bits_1_d3, cpu_16bits_1_d4, cpu_16bits_1_d5, cpu_16bits_1_d6, cpu_16bits_1_d7, cpu_16bits_1_d8,
       cpu_16bits_1_d9, cpu_16bits_1_da, cpu_16bits_1_db, cpu_16bits_1_dc, cpu_16bits_1_dd, cpu_16bits_1_de,
       cpu_16bits_1_df, dipswitch_1_p1, dipswitch_4_p1, dipswitch_7_p1, dipswitch_8_p1, dipswitch_13_p1;
  wire [3:0] cpu_16bits_1_std_out1, cpu_16bits_1_std_out2, cpu_16bits_1_std_out3, cpu_16bits_1_std_out4;
  wire [7:0] undriven;
  wire [15:0] undriven_2;

  // DipSwitch #(.number(1)) dipswitch_1: pin names not known; wires that end beside it: dipswitch_1_p1
  LED led_1 (.in(cpu_16bits_1_a7));
  LED led_2 (.in(cpu_16bits_1_df));
  // DipSwitch #(.number(1)) dipswitch_2: pin names not known
  // DipSwitch #(.number(1)) dipswitch_3: pin names not known
  // DipSwitch #(.number(1)) dipswitch_4: pin names not known; wires that end beside it: dipswitch_4_p1
  LED led_3 (.in(cpu_16bits_1_a6));
  LED led_4 (.in(cpu_16bits_1_a5));
  LED led_5 (.in(cpu_16bits_1_a4));
  LED led_6 (.in(cpu_16bits_1_a3));
  LED led_7 (.in(cpu_16bits_1_de));
  LED led_8 (.in(cpu_16bits_1_dd));
  LED led_9 (.in(cpu_16bits_1_dc));
  LED led_10 (.in(cpu_16bits_1_db));
  // DipSwitch #(.number(1)) dipswitch_5: pin names not known
  // DipSwitch #(.number(1)) dipswitch_6: pin names not known
  // DipSwitch #(.number(1)) dipswitch_7: pin names not known; wires that end beside it: dipswitch_7_p1
  // DipSwitch #(.number(1)) dipswitch_8: pin names not known; wires that end beside it: dipswitch_8_p1
  LED led_11 (.in(cpu_16bits_1_a2));
  LED led_12 (.in(cpu_16bits_1_a1));
  LED led_13 (.in(cpu_16bits_1_a0));
  LED led_14 (.in(cpu_16bits_1_da));
  LED led_15 (.in(cpu_16bits_1_d9));
  LED led_16 (.in(cpu_16bits_1_d8));
  LED led_17 (.in(cpu_16bits_1_d7));
  // DipSwitch #(.number(1)) dipswitch_9: pin names not known
  // DipSwitch #(.number(1)) dipswitch_10: pin names not known
  // DipSwitch #(.number(1)) dipswitch_11: pin names not known
  // DipSwitch #(.number(1)) dipswitch_12: pin names not known
  // DipSwitch #(.number(1)) dipswitch_13: pin names not known; wires that end beside it: dipswitch_13_p1
  Hex_Digit_Display hex_digit_display_1 (.value(cpu_16bits_1_std_out4));  // open: dp
  LED led_18 (.in(cpu_16bits_1_d6));
  LED led_19 (.in(cpu_16bits_1_d5));
  LED led_20 (.in(cpu_16bits_1_d4));
  LED led_21 (.in(cpu_16bits_1_d3));
  // DipSwitch #(.number(1)) dipswitch_14: pin names not known
  // DipSwitch #(.number(1)) dipswitch_15: pin names not known
  Hex_Digit_Display hex_digit_display_2 (.value(cpu_16bits_1_std_out3));  // open: dp
  Hex_Digit_Display hex_digit_display_3 (.value(cpu_16bits_1_std_out2));  // open: dp
  LED led_22 (.in(cpu_16bits_1_d2));
  LED led_23 (.in(cpu_16bits_1_d1));
  LED led_24 (.in(cpu_16bits_1_d0));
  // DipSwitch #(.number(1)) dipswitch_16: pin names not known
  // DipSwitch #(.number(1)) dipswitch_17: pin names not known
  // DipSwitch #(.number(1)) dipswitch_18: pin names not known
  // DipSwitch #(.number(1)) dipswitch_19: pin names not known
  Hex_Digit_Display hex_digit_display_4 (.value(cpu_16bits_1_std_out1));  // open: dp
  // DipSwitch #(.number(1)) dipswitch_20: pin names not known
  // DipSwitch #(.number(1)) dipswitch_21: pin names not known
  // DipSwitch #(.number(1)) dipswitch_22: pin names not known
  CPU_16bits cpu_16bits_1 (
    .START(dipswitch_8_p1), .ADDR_in(undriven), .Data_in(undriven_2), .load(dipswitch_1_p1),
    .Step(dipswitch_7_p1), .look(dipswitch_4_p1), .Stepback(dipswitch_13_p1),
    .STD_out1(cpu_16bits_1_std_out1), .STD_out2(cpu_16bits_1_std_out2), .STD_out3(cpu_16bits_1_std_out3),
    .STD_out4(cpu_16bits_1_std_out4), .A0(cpu_16bits_1_a0), .A1(cpu_16bits_1_a1), .A2(cpu_16bits_1_a2),
    .A3(cpu_16bits_1_a3), .A4(cpu_16bits_1_a4), .A5(cpu_16bits_1_a5), .A6(cpu_16bits_1_a6),
    .A7(cpu_16bits_1_a7), .D0(cpu_16bits_1_d0), .D1(cpu_16bits_1_d1), .D2(cpu_16bits_1_d2),
    .D3(cpu_16bits_1_d3), .D4(cpu_16bits_1_d4), .D5(cpu_16bits_1_d5), .D6(cpu_16bits_1_d6),
    .D7(cpu_16bits_1_d7), .D8(cpu_16bits_1_d8), .D9(cpu_16bits_1_d9), .Da(cpu_16bits_1_da),
    .Db(cpu_16bits_1_db), .Dc(cpu_16bits_1_dc), .Dd(cpu_16bits_1_dd), .De(cpu_16bits_1_de),
    .Df(cpu_16bits_1_df));
  // DipSwitch #(.number(1)) dipswitch_23: pin names not known
  // DipSwitch #(.number(1)) dipswitch_24: pin names not known
  // DipSwitch #(.number(1)) dipswitch_25: pin names not known
  // DipSwitch #(.number(1)) dipswitch_26: pin names not known
  Clock clock_1 (.out(clock_1_out));
  // DipSwitch #(.number(1)) dipswitch_27: pin names not known; wires that end beside it: clock_1_out
  // DipSwitch #(.number(1)) dipswitch_28: pin names not known
  // DipSwitch #(.number(1)) dipswitch_29: pin names not known

  // Notes on the sheet:
  //   EXECUTE
endmodule
