// Logisim project TOY_8.circ as structural Verilog
module full_circuit (
  input  A,
  input  B,
  input  CIN,
  output SUM,
  output COUT
);

  wire and_1_out, and_2_out, xor_1_out;

  xor xor_1 (xor_1_out, A, B);
  and and_1 (and_1_out, A, B);
  xor xor_2 (SUM, xor_1_out, CIN);
  and and_2 (and_2_out, xor_1_out, CIN);
  or or_1 (COUT, and_1_out, and_2_out);
  // Probe on {COUT, SUM}
endmodule

module ADDER_8_bit (
  input  [7:0] A,
  input  [7:0] B,
  input  CIN,
  output [7:0] out_4,
  output out_5
);

  wire full_circuit_1_cout, full_circuit_2_cout, full_circuit_3_cout, full_circuit_4_cout,
       full_circuit_5_cout, full_circuit_6_cout, full_circuit_7_cout;

  // Probe on B
  // Probe on A
  full_circuit full_circuit_1 (.A(A[0]), .B(B[0]), .CIN(CIN), .SUM(out_4[0]), .COUT(full_circuit_1_cout));
  full_circuit full_circuit_2 (
    .A(A[1]), .B(B[1]), .CIN(full_circuit_1_cout), .SUM(out_4[1]), .COUT(full_circuit_2_cout));
  full_circuit full_circuit_3 (
    .A(A[2]), .B(B[2]), .CIN(full_circuit_2_cout), .SUM(out_4[2]), .COUT(full_circuit_3_cout));
  full_circuit full_circuit_4 (
    .A(A[3]), .B(B[3]), .CIN(full_circuit_3_cout), .SUM(out_4[3]), .COUT(full_circuit_4_cout));
  full_circuit full_circuit_5 (
    .A(A[4]), .B(B[4]), .CIN(full_circuit_4_cout), .SUM(out_4[4]), .COUT(full_circuit_5_cout));
  full_circuit full_circuit_6 (
    .A(A[5]), .B(B[5]), .CIN(full_circuit_5_cout), .SUM(out_4[5]), .COUT(full_circuit_6_cout));
  full_circuit full_circuit_7 (
    .A(A[6]), .B(B[6]), .CIN(full_circuit_6_cout), .SUM(out_4[6]), .COUT(full_circuit_7_cout));
  full_circuit full_circuit_8 (.A(A[7]), .B(B[7]), .CIN(full_circuit_7_cout), .SUM(out_4[7]), .COUT(out_5));
  // Probe on {out_5, out_4}
endmodule

module MUX (
  input  [3:0] in_1,
  input  [3:0] in_2,
  input  [3:0] in_3,
  input  [3:0] in_4,
  input  in_5,
  input  in_6,
  output [3:0] out_7
);

  wire and_1_out, and_2_out, and_3_out, nor_1_out, not_1_out, not_2_out;
  wire [3:0] controlled_buffer_1_out, controlled_buffer_2_out, controlled_buffer_3_out,
       controlled_buffer_4_out;

  assign controlled_buffer_1_out = nor_1_out ? in_1 : 4'bz;  // Controlled_Buffer controlled_buffer_1
  assign controlled_buffer_2_out = and_2_out ? in_2 : 4'bz;  // Controlled_Buffer controlled_buffer_2
  assign controlled_buffer_3_out = and_3_out ? in_3 : 4'bz;  // Controlled_Buffer controlled_buffer_3
  assign controlled_buffer_4_out = and_1_out ? in_4 : 4'bz;  // Controlled_Buffer controlled_buffer_4
  and and_1 (and_1_out, in_5, in_6);
  nor nor_1 (nor_1_out, in_5, in_6);
  not not_1 (not_1_out, in_5);
  Pull_Resistor pull_resistor_1 (.node(controlled_buffer_3_out));
  Pull_Resistor pull_resistor_2 (.node(controlled_buffer_4_out));
  and and_2 (and_2_out, not_1_out, in_6);
  Pull_Resistor pull_resistor_3 (.node(controlled_buffer_1_out));
  Pull_Resistor pull_resistor_4 (.node(controlled_buffer_2_out));
  and and_3 (and_3_out, not_2_out, in_5);
  not not_2 (not_2_out, in_6);
  assign out_7 = controlled_buffer_1_out | controlled_buffer_2_out | controlled_buffer_3_out | controlled_buffer_4_out;  // OR_Gate_part or_1, 4 bits wide
  // Probe on out_7
endmodule

module De_Coder (
  input  in_1,
  input  in_2,
  input  in_3,
  output _0,
  output _1,
  output _2,
  output _3,
  output _4,
  output _5,
  output _6,
  output _7
);

  wire not_1_out, not_2_out, not_3_out, not_4_out, not_5_out, not_6_out, not_7_out;

  // Probe on {in_1, in_2, in_3}
  not not_1 (not_1_out, in_2);
  not not_2 (not_2_out, in_1);
  not not_3 (not_3_out, in_3);
  not not_4 (not_4_out, in_1);
  not not_5 (not_5_out, in_1);
  not not_6 (not_6_out, in_3);
  not not_7 (not_7_out, in_2);
  and and_1 (_1, in_3, not_1_out, not_2_out);
  and and_2 (_2, not_3_out, in_2, not_4_out);
  and and_3 (_3, in_3, in_2, not_5_out);
  and and_4 (_4, not_6_out, not_7_out, in_1);
  and and_5 (_5, in_3, ~in_2, in_1);  // AND_Gate_part
  and and_6 (_6, ~in_3, in_2, in_1);  // AND_Gate_part
  and and_7 (_7, in_3, in_2, in_1);
  nor nor_1 (_0, in_3, in_2, in_1);
endmodule

module De_mux (
  input  in_1,
  input  in_2,
  input  in_3,
  input  [3:0] X,
  output [3:0] out_5,
  output [3:0] out_6,
  output [3:0] _2,
  output [3:0] _3,
  output [3:0] _4,
  output [3:0] _5,
  output [3:0] _6,
  output [3:0] _7
);

  wire and_1_out, and_2_out, and_3_out, and_4_out, and_5_out, and_6_out, and_7_out, nor_1_out, not_1_out,
       not_2_out, not_3_out, not_4_out, not_5_out, not_6_out, not_7_out;

  // Probe on {in_1, in_2, in_3}
  not not_1 (not_1_out, in_2);
  not not_2 (not_2_out, in_1);
  not not_3 (not_3_out, in_3);
  not not_4 (not_4_out, in_1);
  not not_5 (not_5_out, in_1);
  not not_6 (not_6_out, in_3);
  not not_7 (not_7_out, in_2);
  and and_1 (and_1_out, in_3, not_1_out, not_2_out);
  and and_2 (and_2_out, not_3_out, in_2, not_4_out);
  and and_3 (and_3_out, in_3, in_2, not_5_out);
  and and_4 (and_4_out, not_6_out, not_7_out, in_1);
  and and_5 (and_5_out, in_3, ~in_2, in_1);  // AND_Gate_part
  and and_6 (and_6_out, ~in_3, in_2, in_1);  // AND_Gate_part
  and and_7 (and_7_out, in_3, in_2, in_1);
  Pull_Resistor pull_resistor_1 (.node(out_5));
  assign out_5 = nor_1_out ? X : 4'bz;  // Controlled_Buffer controlled_buffer_1
  nor nor_1 (nor_1_out, in_3, in_2, in_1);
  Pull_Resistor pull_resistor_2 (.node(out_6));
  assign out_6 = and_1_out ? X : 4'bz;  // Controlled_Buffer controlled_buffer_2
  Pull_Resistor pull_resistor_3 (.node(_2));
  assign _2 = and_2_out ? X : 4'bz;  // Controlled_Buffer controlled_buffer_3
  Pull_Resistor pull_resistor_4 (.node(_3));
  assign _3 = and_3_out ? X : 4'bz;  // Controlled_Buffer controlled_buffer_4
  Pull_Resistor pull_resistor_5 (.node(_4));
  assign _4 = and_4_out ? X : 4'bz;  // Controlled_Buffer controlled_buffer_5
  Pull_Resistor pull_resistor_6 (.node(_5));
  assign _5 = and_5_out ? X : 4'bz;  // Controlled_Buffer controlled_buffer_6
  Pull_Resistor pull_resistor_7 (.node(_6));
  assign _6 = and_6_out ? X : 4'bz;  // Controlled_Buffer controlled_buffer_7
  Pull_Resistor pull_resistor_8 (.node(_7));
  assign _7 = and_7_out ? X : 4'bz;  // Controlled_Buffer controlled_buffer_8

  // Notes on the sheet:
  //   0
  //   1
endmodule

module De_coder_MUX (
  input  in_1,
  input  in_2,
  input  in_3,
  input  [3:0] X,
  output [3:0] out_5,
  output out_6,
  output [3:0] out_7,
  output out_8,
  output [3:0] _2,
  output out_10,
  output [3:0] _3,
  output out_12,
  output [3:0] _4,
  output out_14,
  output [3:0] _5,
  output out_16,
  output [3:0] _6,
  output out_18,
  output [3:0] _7,
  output out_20
);

  wire not_1_out, not_2_out, not_3_out, not_4_out, not_5_out, not_6_out, not_7_out;

  // Probe on {in_1, in_2, in_3}
  not not_1 (not_1_out, in_2);
  not not_2 (not_2_out, in_1);
  not not_3 (not_3_out, in_3);
  not not_4 (not_4_out, in_1);
  not not_5 (not_5_out, in_1);
  not not_6 (not_6_out, in_3);
  not not_7 (not_7_out, in_2);
  and and_1 (out_8, in_3, not_1_out, not_2_out);
  and and_2 (out_10, not_3_out, in_2, not_4_out);
  and and_3 (out_12, in_3, in_2, not_5_out);
  and and_4 (out_14, not_6_out, not_7_out, in_1);
  and and_5 (out_16, in_3, ~in_2, in_1);  // AND_Gate_part
  and and_6 (out_18, ~in_3, in_2, in_1);  // AND_Gate_part
  and and_7 (out_20, in_3, in_2, in_1);
  Pull_Resistor pull_resistor_1 (.node(out_5));
  assign out_5 = out_6 ? X : 4'bz;  // Controlled_Buffer controlled_buffer_1
  nor nor_1 (out_6, in_3, in_2, in_1);
  Pull_Resistor pull_resistor_2 (.node(out_7));
  assign out_7 = out_8 ? X : 4'bz;  // Controlled_Buffer controlled_buffer_2
  Pull_Resistor pull_resistor_3 (.node(_2));
  assign _2 = out_10 ? X : 4'bz;  // Controlled_Buffer controlled_buffer_3
  Pull_Resistor pull_resistor_4 (.node(_3));
  assign _3 = out_12 ? X : 4'bz;  // Controlled_Buffer controlled_buffer_4
  Pull_Resistor pull_resistor_5 (.node(_4));
  assign _4 = out_14 ? X : 4'bz;  // Controlled_Buffer controlled_buffer_5
  Pull_Resistor pull_resistor_6 (.node(_5));
  assign _5 = out_16 ? X : 4'bz;  // Controlled_Buffer controlled_buffer_6
  Pull_Resistor pull_resistor_7 (.node(_6));
  assign _6 = out_18 ? X : 4'bz;  // Controlled_Buffer controlled_buffer_7
  Pull_Resistor pull_resistor_8 (.node(_7));
  assign _7 = out_20 ? X : 4'bz;  // Controlled_Buffer controlled_buffer_8

  // Notes on the sheet:
  //   0
  //   1
endmodule

module ALU (
  input  [7:0] in_1,
  input  [7:0] in_2,
  input  in_3,
  input  in_4,
  input  in_5,
  output [7:0] out_6
);

  wire [7:0] adder_8_bit_1_out_4, and_gate_8bit_1_out_3, xor_gate_8bit_1_out_3;

  XOR_Gate_8bit xor_gate_8bit_1 (.in_1(in_1), .in_2(in_2), .out_3(xor_gate_8bit_1_out_3));
  AND_Gate_8bit and_gate_8bit_1 (.in_1(in_1), .in_2(in_2), .out_3(and_gate_8bit_1_out_3));
  ADDER_8_bit adder_8_bit_1 (.A(in_1), .B(in_2), .CIN(1'b0), .out_4(adder_8_bit_1_out_4));  // open: out_5
  assign out_6 = in_4 ? xor_gate_8bit_1_out_3 : 8'bz;  // Controlled_Buffer controlled_buffer_1
  assign out_6 = in_5 ? and_gate_8bit_1_out_3 : 8'bz;  // Controlled_Buffer controlled_buffer_2
  assign out_6 = in_3 ? adder_8_bit_1_out_4 : 8'bz;  // Controlled_Buffer controlled_buffer_3
  Pull_Resistor pull_resistor_1 (.node(out_6));
endmodule

module Right_bitshifter (
  input  [7:0] in_1,
  input  [7:0] in_2,
  output [7:0] out_3
);

  wire [7:0] mux_2to1_1_p4, mux_2to1_2_p4, mux_2to1_3_p4, mux_2to1_4_p4, mux_2to1_5_p4, mux_2to1_6_p4,
       mux_2to1_7_p4, mux_2to1_8_p4, mux_2to1_9_oi, mux_2to1_10_oi, mux_2to1_11_oi, mux_2to1_12_oi,
       mux_2to1_13_oi, mux_2to1_14_oi, mux_2to1_15_oi, mux_2to1_16_oi, pull_resistor_1_node;

  Pull_Resistor pull_resistor_1 (.node(pull_resistor_1_node));
  // MUX_2to1 mux_2to1_1: pin names not known; wires that end beside it: in_1[0], in_1[1], in_2[0], mux_2to1_1_p4
  // MUX_2to1 mux_2to1_2: pin names not known; wires that end beside it: in_1[1], in_1[2], in_2[0], mux_2to1_2_p4
  // MUX_2to1 mux_2to1_3: pin names not known; wires that end beside it: in_1[2], in_1[3], in_2[0], mux_2to1_3_p4
  // MUX_2to1 mux_2to1_4: pin names not known; wires that end beside it: in_1[3], in_1[4], in_2[0], mux_2to1_4_p4
  // MUX_2to1 mux_2to1_5: pin names not known; wires that end beside it: in_1[4], in_1[5], in_2[0], mux_2to1_5_p4
  // MUX_2to1 mux_2to1_6: pin names not known; wires that end beside it: in_1[5], in_1[6], in_2[0], mux_2to1_6_p4
  // MUX_2to1 mux_2to1_7: pin names not known; wires that end beside it: in_1[6], in_1[7], in_2[0], mux_2to1_7_p4
  // MUX_2to1 mux_2to1_8: pin names not known; wires that end beside it: in_1[7], pull_resistor_1_node, in_2[0], mux_2to1_8_p4
  MUX_2to1 mux_2to1_9 (.Ai(mux_2to1_1_p4), .Bi(mux_2to1_3_p4), .CA(in_2[1]), .Oi(mux_2to1_9_oi));  // open: CB
  MUX_2to1 mux_2to1_10 (.Ai(mux_2to1_2_p4), .Bi(mux_2to1_4_p4), .CA(in_2[1]), .Oi(mux_2to1_10_oi));  // open: CB
  MUX_2to1 mux_2to1_11 (.Ai(mux_2to1_3_p4), .Bi(mux_2to1_5_p4), .CA(in_2[1]), .Oi(mux_2to1_11_oi));  // open: CB
  MUX_2to1 mux_2to1_12 (.Ai(mux_2to1_4_p4), .Bi(mux_2to1_6_p4), .CA(in_2[1]), .Oi(mux_2to1_12_oi));  // open: CB
  MUX_2to1 mux_2to1_13 (.Ai(mux_2to1_5_p4), .Bi(mux_2to1_7_p4), .CA(in_2[1]), .Oi(mux_2to1_13_oi));  // open: CB
  MUX_2to1 mux_2to1_14 (.Ai(mux_2to1_6_p4), .Bi(mux_2to1_8_p4), .CA(in_2[1]), .Oi(mux_2to1_14_oi));  // open: CB
  MUX_2to1 mux_2to1_15 (.Ai(mux_2to1_7_p4), .Bi(pull_resistor_1_node), .CA(in_2[1]), .Oi(mux_2to1_15_oi));  // open: CB
  MUX_2to1 mux_2to1_16 (.Ai(mux_2to1_8_p4), .Bi(pull_resistor_1_node), .CA(in_2[1]), .Oi(mux_2to1_16_oi));  // open: CB
  // MUX_2to1 mux_2to1_17: pin names not known; wires that end beside it: mux_2to1_9_oi, mux_2to1_13_oi, in_2[2], out_3[0]
  // MUX_2to1 mux_2to1_18: pin names not known; wires that end beside it: mux_2to1_10_oi, mux_2to1_14_oi, in_2[2], out_3[1]
  // MUX_2to1 mux_2to1_19: pin names not known; wires that end beside it: mux_2to1_11_oi, mux_2to1_15_oi, in_2[2], out_3[2]
  // MUX_2to1 mux_2to1_20: pin names not known; wires that end beside it: mux_2to1_12_oi, mux_2to1_16_oi, in_2[2], out_3[3]
  // MUX_2to1 mux_2to1_21: pin names not known; wires that end beside it: mux_2to1_13_oi, pull_resistor_1_node, in_2[2], out_3[4]
  // MUX_2to1 mux_2to1_22: pin names not known; wires that end beside it: mux_2to1_14_oi, pull_resistor_1_node, in_2[2], out_3[5]
  // MUX_2to1 mux_2to1_23: pin names not known; wires that end beside it: mux_2to1_15_oi, pull_resistor_1_node, in_2[2], out_3[6]
  // MUX_2to1 mux_2to1_24: pin names not known; wires that end beside it: mux_2to1_16_oi, pull_resistor_1_node, in_2[2], out_3[7]
endmodule

module Left_bitshifter (
  input  [7:0] in_1,
  input  [7:0] in_2,
  output [7:0] out_3
);

  wire [7:0] mux_2to1_1_p4, mux_2to1_2_p4, mux_2to1_3_p4, mux_2to1_4_p4, mux_2to1_5_p4, mux_2to1_6_p4,
       mux_2to1_7_p4, mux_2to1_8_p4, mux_2to1_9_oi, mux_2to1_10_oi, mux_2to1_11_oi, mux_2to1_12_oi,
       mux_2to1_13_oi, mux_2to1_14_oi, mux_2to1_15_oi, mux_2to1_16_oi, pull_resistor_1_node;

  Pull_Resistor pull_resistor_1 (.node(pull_resistor_1_node));
  // MUX_2to1 mux_2to1_1: pin names not known; wires that end beside it: in_1[0], pull_resistor_1_node, in_2[0], mux_2to1_1_p4
  // MUX_2to1 mux_2to1_2: pin names not known; wires that end beside it: in_1[1], in_1[0], in_2[0], mux_2to1_2_p4
  // MUX_2to1 mux_2to1_3: pin names not known; wires that end beside it: in_1[2], in_1[1], in_2[0], mux_2to1_3_p4
  // MUX_2to1 mux_2to1_4: pin names not known; wires that end beside it: in_1[3], in_1[2], in_2[0], mux_2to1_4_p4
  // MUX_2to1 mux_2to1_5: pin names not known; wires that end beside it: in_1[4], in_1[3], in_2[0], mux_2to1_5_p4
  // MUX_2to1 mux_2to1_6: pin names not known; wires that end beside it: in_1[5], in_1[4], in_2[0], mux_2to1_6_p4
  // MUX_2to1 mux_2to1_7: pin names not known; wires that end beside it: in_1[6], in_1[5], in_2[0], mux_2to1_7_p4
  // MUX_2to1 mux_2to1_8: pin names not known; wires that end beside it: in_1[7], in_1[6], in_2[0], mux_2to1_8_p4
  MUX_2to1 mux_2to1_9 (.Ai(mux_2to1_1_p4), .Bi(pull_resistor_1_node), .CA(in_2[1]), .Oi(mux_2to1_9_oi));  // open: CB
  MUX_2to1 mux_2to1_10 (.Ai(mux_2to1_2_p4), .Bi(pull_resistor_1_node), .CA(in_2[1]), .Oi(mux_2to1_10_oi));  // open: CB
  MUX_2to1 mux_2to1_11 (.Ai(mux_2to1_3_p4), .Bi(mux_2to1_1_p4), .CA(in_2[1]), .Oi(mux_2to1_11_oi));  // open: CB
  MUX_2to1 mux_2to1_12 (.Ai(mux_2to1_4_p4), .Bi(mux_2to1_2_p4), .CA(in_2[1]), .Oi(mux_2to1_12_oi));  // open: CB
  MUX_2to1 mux_2to1_13 (.Ai(mux_2to1_5_p4), .Bi(mux_2to1_3_p4), .CA(in_2[1]), .Oi(mux_2to1_13_oi));  // open: CB
  MUX_2to1 mux_2to1_14 (.Ai(mux_2to1_6_p4), .Bi(mux_2to1_4_p4), .CA(in_2[1]), .Oi(mux_2to1_14_oi));  // open: CB
  MUX_2to1 mux_2to1_15 (.Ai(mux_2to1_7_p4), .Bi(mux_2to1_5_p4), .CA(in_2[1]), .Oi(mux_2to1_15_oi));  // open: CB
  MUX_2to1 mux_2to1_16 (.Ai(mux_2to1_8_p4), .Bi(mux_2to1_6_p4), .CA(in_2[1]), .Oi(mux_2to1_16_oi));  // open: CB
  // MUX_2to1 mux_2to1_17: pin names not known; wires that end beside it: mux_2to1_9_oi, pull_resistor_1_node, in_2[2], out_3[0]
  // MUX_2to1 mux_2to1_18: pin names not known; wires that end beside it: mux_2to1_10_oi, pull_resistor_1_node, in_2[2], out_3[1]
  // MUX_2to1 mux_2to1_19: pin names not known; wires that end beside it: mux_2to1_11_oi, pull_resistor_1_node, in_2[2], out_3[2]
  // MUX_2to1 mux_2to1_20: pin names not known; wires that end beside it: mux_2to1_12_oi, pull_resistor_1_node, in_2[2], out_3[3]
  // MUX_2to1 mux_2to1_21: pin names not known; wires that end beside it: mux_2to1_13_oi, mux_2to1_9_oi, in_2[2], out_3[4]
  // MUX_2to1 mux_2to1_22: pin names not known; wires that end beside it: mux_2to1_14_oi, mux_2to1_10_oi, in_2[2], out_3[5]
  // MUX_2to1 mux_2to1_23: pin names not known; wires that end beside it: mux_2to1_15_oi, mux_2to1_11_oi, in_2[2], out_3[6]
  // MUX_2to1 mux_2to1_24: pin names not known; wires that end beside it: mux_2to1_16_oi, mux_2to1_12_oi, in_2[2], out_3[7]
endmodule

module NOT_Gate (
  input  in_1,
  output out_2
);

  Pull_Resistor pull_resistor_1 (.node(out_2));
  Transistor transistor_1 (.in(1'b1), .out(out_2), .gate(in_1));
endmodule

module NAND_Gate (
  input  in_1,
  input  in_2,
  output out_3
);

  wire transistor_2_out;

  Pull_Resistor #(.pull(1)) pull_resistor_1 (.node(out_3));
  Transistor #(.\type ("n")) transistor_1 (.in(transistor_2_out), .out(out_3), .gate(in_1));
  Transistor #(.\type ("n")) transistor_2 (.in(1'b0), .out(transistor_2_out), .gate(in_2));
endmodule

module AND_Gate_8bit (
  input  [7:0] in_1,
  input  [7:0] in_2,
  output [7:0] out_3
);

  wire nand_gate_1_out_3, nand_gate_2_out_3, nand_gate_3_out_3, nand_gate_4_out_3, nand_gate_5_out_3,
       nand_gate_6_out_3, nand_gate_7_out_3, nand_gate_8_out_3;

  NAND_Gate nand_gate_1 (.in_1(in_1[0]), .in_2(in_2[0]), .out_3(nand_gate_1_out_3));
  NAND_Gate nand_gate_2 (.in_1(in_1[1]), .in_2(in_2[1]), .out_3(nand_gate_2_out_3));
  NAND_Gate nand_gate_3 (.in_1(in_1[2]), .in_2(in_2[2]), .out_3(nand_gate_3_out_3));
  NAND_Gate nand_gate_4 (.in_1(in_1[3]), .in_2(in_2[3]), .out_3(nand_gate_4_out_3));
  NAND_Gate nand_gate_5 (.in_1(in_1[4]), .in_2(in_2[4]), .out_3(nand_gate_5_out_3));
  NAND_Gate nand_gate_6 (.in_1(in_1[5]), .in_2(in_2[5]), .out_3(nand_gate_6_out_3));
  NAND_Gate nand_gate_7 (.in_1(in_1[6]), .in_2(in_2[6]), .out_3(nand_gate_7_out_3));
  NAND_Gate nand_gate_8 (.in_1(in_1[7]), .in_2(in_2[7]), .out_3(nand_gate_8_out_3));
  NOT_Gate not_gate_1 (.in_1(nand_gate_1_out_3), .out_2(out_3[0]));
  NOT_Gate not_gate_2 (.in_1(nand_gate_2_out_3), .out_2(out_3[1]));
  NOT_Gate not_gate_3 (.in_1(nand_gate_3_out_3), .out_2(out_3[2]));
  NOT_Gate not_gate_4 (.in_1(nand_gate_4_out_3), .out_2(out_3[3]));
  NOT_Gate not_gate_5 (.in_1(nand_gate_5_out_3), .out_2(out_3[4]));
  NOT_Gate not_gate_6 (.in_1(nand_gate_6_out_3), .out_2(out_3[5]));
  NOT_Gate not_gate_7 (.in_1(nand_gate_7_out_3), .out_2(out_3[6]));
  NOT_Gate not_gate_8 (.in_1(nand_gate_8_out_3), .out_2(out_3[7]));
endmodule

module NOR_Gate (
  input  in_1,
  input  in_2,
  output out_3
);

  wire transistor_2_out;

  Pull_Resistor pull_resistor_1 (.node(out_3));
  Transistor transistor_1 (.in(transistor_2_out), .out(out_3), .gate(in_1));
  Transistor transistor_2 (.in(1'b1), .out(transistor_2_out), .gate(in_2));
endmodule

module XOR_Gate (
  input  in_1,
  input  in_2,
  output out_3
);

  wire nand_gate_1_out_3, nand_gate_2_out_3, nor_gate_1_out_3, not_gate_1_out_2, not_gate_2_out_2,
       not_gate_3_out_2, not_gate_4_out_2;

  NOT_Gate not_gate_1 (.in_1(in_2), .out_2(not_gate_1_out_2));
  NOT_Gate not_gate_2 (.in_1(in_1), .out_2(not_gate_2_out_2));
  NAND_Gate nand_gate_1 (.in_1(in_1), .in_2(not_gate_1_out_2), .out_3(nand_gate_1_out_3));
  NAND_Gate nand_gate_2 (.in_1(not_gate_2_out_2), .in_2(in_2), .out_3(nand_gate_2_out_3));
  NOT_Gate not_gate_3 (.in_1(nand_gate_1_out_3), .out_2(not_gate_3_out_2));
  NOT_Gate not_gate_4 (.in_1(nand_gate_2_out_3), .out_2(not_gate_4_out_2));
  NOR_Gate nor_gate_1 (.in_1(not_gate_3_out_2), .in_2(not_gate_4_out_2), .out_3(nor_gate_1_out_3));
  NOT_Gate not_gate_5 (.in_1(nor_gate_1_out_3), .out_2(out_3));
endmodule

module XOR_Gate_8bit (
  input  [7:0] in_1,
  input  [7:0] in_2,
  output [7:0] out_3
);

  XOR_Gate xor_gate_1 (.in_1(in_1[0]), .in_2(in_2[0]), .out_3(out_3[0]));
  XOR_Gate xor_gate_2 (.in_1(in_1[1]), .in_2(in_2[1]), .out_3(out_3[1]));
  XOR_Gate xor_gate_3 (.in_1(in_1[2]), .in_2(in_2[2]), .out_3(out_3[2]));
  XOR_Gate xor_gate_4 (.in_1(in_1[3]), .in_2(in_2[3]), .out_3(out_3[3]));
  XOR_Gate xor_gate_5 (.in_1(in_1[4]), .in_2(in_2[4]), .out_3(out_3[4]));
  XOR_Gate xor_gate_6 (.in_1(in_1[5]), .in_2(in_2[5]), .out_3(out_3[5]));
  XOR_Gate xor_gate_7 (.in_1(in_1[6]), .in_2(in_2[6]), .out_3(out_3[6]));
  XOR_Gate xor_gate_8 (.in_1(in_1[7]), .in_2(in_2[7]), .out_3(out_3[7]));
endmodule

module AND_Gate (
  input  in_1,
  input  in_2,
  output out_3
);

  wire nand_gate_1_out_3;

  NAND_Gate nand_gate_1 (.in_1(in_1), .in_2(in_2), .out_3(nand_gate_1_out_3));
  NOT_Gate not_gate_1 (.in_1(nand_gate_1_out_3), .out_2(out_3));
endmodule

module OR_Gate (
  input  in_1,
  input  in_2,
  output out_3
);

  wire nor_gate_1_out_3;

  NOR_Gate nor_gate_1 (.in_1(in_1), .in_2(in_2), .out_3(nor_gate_1_out_3));
  NOT_Gate not_gate_1 (.in_1(nor_gate_1_out_3), .out_2(out_3));
endmodule

module XNOR_Gate (
  input  in_1,
  input  in_2,
  output out_3
);

  wire xor_gate_1_out_3;

  XOR_Gate xor_gate_1 (.in_1(in_1), .in_2(in_2), .out_3(xor_gate_1_out_3));
  NOT_Gate not_gate_1 (.in_1(xor_gate_1_out_3), .out_2(out_3));
endmodule

module AND_Gate_3_input (
  input  in_1,
  input  in_2,
  input  in_3,
  input  in_4,
  input  in_5,
  input  in_6,
  output out_7,
  output out_8
);

  wire not_gate_1_out_2, pull_resistor_1_node, pull_resistor_2_node, pull_resistor_3_node, transistor_2_out,
       transistor_4_out, transistor_6_out, transistor_7_out;

  Pull_Resistor #(.pull(1)) pull_resistor_1 (.node(pull_resistor_1_node));
  Transistor #(.\type ("n")) transistor_1 (.in(transistor_2_out), .out(pull_resistor_1_node), .gate(in_2));
  Transistor #(.\type ("n")) transistor_2 (.in(1'b0), .out(transistor_2_out), .gate(in_3));
  NOT_Gate not_gate_1 (.in_1(pull_resistor_1_node), .out_2(not_gate_1_out_2));
  Pull_Resistor #(.pull(1)) pull_resistor_2 (.node(pull_resistor_2_node));
  Transistor #(.\type ("n")) transistor_3 (.in(transistor_4_out), .out(pull_resistor_2_node), .gate(in_1));
  Transistor #(.\type ("n")) transistor_4 (.in(1'b0), .out(transistor_4_out), .gate(not_gate_1_out_2));
  NOT_Gate not_gate_2 (.in_1(pull_resistor_2_node), .out_2(out_7));
  Pull_Resistor #(.pull(1)) pull_resistor_3 (.node(pull_resistor_3_node));
  Transistor #(.\type ("n")) transistor_5 (.in(transistor_6_out), .out(pull_resistor_3_node), .gate(in_4));
  Transistor #(.\type ("n")) transistor_6 (.in(transistor_7_out), .out(transistor_6_out), .gate(in_5));
  Transistor #(.\type ("n")) transistor_7 (.in(1'b0), .out(transistor_7_out), .gate(in_6));
  NOT_Gate not_gate_3 (.in_1(pull_resistor_3_node), .out_2(out_8));
endmodule

module Multi_input_OR_Gate (
  input  in_1,
  input  in_2,
  input  in_3,
  input  in_4,
  input  in_5,
  input  in_6,
  output out_7,
  output out_8
);

  wire not_gate_1_out_2, pull_resistor_1_node, pull_resistor_2_node, pull_resistor_3_node, transistor_2_out,
       transistor_4_out, transistor_6_out, transistor_7_out;

  Pull_Resistor pull_resistor_1 (.node(pull_resistor_1_node));
  Transistor transistor_1 (.in(transistor_2_out), .out(pull_resistor_1_node), .gate(in_2));
  Transistor transistor_2 (.in(1'b1), .out(transistor_2_out), .gate(in_3));
  NOT_Gate not_gate_1 (.in_1(pull_resistor_1_node), .out_2(not_gate_1_out_2));
  Pull_Resistor pull_resistor_2 (.node(pull_resistor_2_node));
  Transistor transistor_3 (.in(transistor_4_out), .out(pull_resistor_2_node), .gate(in_1));
  Transistor transistor_4 (.in(1'b1), .out(transistor_4_out), .gate(not_gate_1_out_2));
  NOT_Gate not_gate_2 (.in_1(pull_resistor_2_node), .out_2(out_7));
  Pull_Resistor pull_resistor_3 (.node(pull_resistor_3_node));
  Transistor transistor_5 (.in(transistor_6_out), .out(pull_resistor_3_node), .gate(in_4));
  Transistor transistor_6 (.in(transistor_7_out), .out(transistor_6_out), .gate(in_5));
  Transistor transistor_7 (.in(1'b1), .out(transistor_7_out), .gate(in_6));
  NOT_Gate not_gate_3 (.in_1(pull_resistor_3_node), .out_2(out_8));
endmodule

module Half_adder (
  input  in_1,
  input  in_2,
  output out_3
);

  XOR_Gate xor_gate_1 (.in_1(in_1), .in_2(in_2), .out_3(out_3));
endmodule

module ODD (
  input  in_1,
  input  in_2,
  input  CIN,
  output out_4
);

  wire and_gate_1_out_3, and_gate_2_out_3, not_gate_1_out_2, not_gate_2_out_2, xor_gate_1_out_3;

  XOR_Gate xor_gate_1 (.in_1(in_1), .in_2(in_2), .out_3(xor_gate_1_out_3));
  NOT_Gate not_gate_1 (.in_1(xor_gate_1_out_3), .out_2(not_gate_1_out_2));
  NOT_Gate not_gate_2 (.in_1(CIN), .out_2(not_gate_2_out_2));
  AND_Gate and_gate_1 (.in_1(not_gate_1_out_2), .in_2(CIN), .out_3(and_gate_1_out_3));
  AND_Gate and_gate_2 (.in_1(not_gate_2_out_2), .in_2(xor_gate_1_out_3), .out_3(and_gate_2_out_3));
  OR_Gate or_gate_1 (.in_1(and_gate_2_out_3), .in_2(and_gate_1_out_3), .out_3(out_4));
endmodule

module MAJ (
  input  in_1,
  input  in_2,
  input  CIN,
  output out_4
);

  wire and_gate_1_out_3, and_gate_2_out_3, or_gate_1_out_3;

  OR_Gate or_gate_1 (.in_1(in_1), .in_2(in_2), .out_3(or_gate_1_out_3));
  AND_Gate and_gate_1 (.in_1(in_1), .in_2(in_2), .out_3(and_gate_1_out_3));
  AND_Gate and_gate_2 (.in_1(or_gate_1_out_3), .in_2(CIN), .out_3(and_gate_2_out_3));
  OR_Gate or_gate_2 (.in_1(and_gate_2_out_3), .in_2(and_gate_1_out_3), .out_3(out_4));
endmodule

module Full_Adder_1bit (
  input  A,
  input  B,
  input  CIN,
  output SUM,
  output COUT
);

  MAJ maj_1 (.in_1(A), .in_2(B), .CIN(CIN), .out_4(COUT));
  ODD odd_1 (.in_1(A), .in_2(B), .CIN(CIN), .out_4(SUM));
  // Probe on {COUT, SUM}
endmodule

module Ripple_Carry_Adder_8bit (
  input  [7:0] A,
  input  [7:0] B,
  input  CIN,
  output [7:0] out_4,
  output out_5
);

  wire full_adder_1bit_1_cout, full_adder_1bit_2_cout, full_adder_1bit_3_cout, full_adder_1bit_4_cout,
       full_adder_1bit_5_cout, full_adder_1bit_6_cout, full_adder_1bit_7_cout;

  // Probe on B
  // Probe on A
  Full_Adder_1bit full_adder_1bit_1 (.A(A[0]), .B(B[0]), .CIN(CIN), .SUM(out_4[0]), .COUT(full_adder_1bit_1_cout));
  Full_Adder_1bit full_adder_1bit_2 (
    .A(A[1]), .B(B[1]), .CIN(full_adder_1bit_1_cout), .SUM(out_4[1]), .COUT(full_adder_1bit_2_cout));
  Full_Adder_1bit full_adder_1bit_3 (
    .A(A[2]), .B(B[2]), .CIN(full_adder_1bit_2_cout), .SUM(out_4[2]), .COUT(full_adder_1bit_3_cout));
  Full_Adder_1bit full_adder_1bit_4 (
    .A(A[3]), .B(B[3]), .CIN(full_adder_1bit_3_cout), .SUM(out_4[3]), .COUT(full_adder_1bit_4_cout));
  Full_Adder_1bit full_adder_1bit_5 (
    .A(A[4]), .B(B[4]), .CIN(full_adder_1bit_4_cout), .SUM(out_4[4]), .COUT(full_adder_1bit_5_cout));
  Full_Adder_1bit full_adder_1bit_6 (
    .A(A[5]), .B(B[5]), .CIN(full_adder_1bit_5_cout), .SUM(out_4[5]), .COUT(full_adder_1bit_6_cout));
  Full_Adder_1bit full_adder_1bit_7 (
    .A(A[6]), .B(B[6]), .CIN(full_adder_1bit_6_cout), .SUM(out_4[6]), .COUT(full_adder_1bit_7_cout));
  Full_Adder_1bit full_adder_1bit_8 (.A(A[7]), .B(B[7]), .CIN(full_adder_1bit_7_cout), .SUM(out_4[7]), .COUT(out_5));
  // Probe on {out_5, out_4}
endmodule

module ALU_8bit (
  input  [7:0] A,
  input  [7:0] B,
  input  S2,
  input  S1,
  input  S0,
  output [7:0] O
);

  wire de_coder_1__1, de_coder_1__2, de_coder_1__3, de_coder_1__4, de_coder_1__5, de_coder_1__6;
  wire [7:0] and_gate_8bit_1_out_3, left_bitshifter_1_out_3, right_bitshifter_1_out_3,
       ripple_carry_adder_8bit_1_out_4, substractor_8_bit_1_out_4, xor_gate_8bit_1_out_3;

  // Probe on A
  // Probe on B
  Ripple_Carry_Adder_8bit ripple_carry_adder_8bit_1 (
    .A(A), .B(B), .CIN(1'b0), .out_4(ripple_carry_adder_8bit_1_out_4));  // open: out_5
  XOR_Gate_8bit xor_gate_8bit_1 (.in_1(A), .in_2(B), .out_3(xor_gate_8bit_1_out_3));
  AND_Gate_8bit and_gate_8bit_1 (.in_1(A), .in_2(B), .out_3(and_gate_8bit_1_out_3));
  Substractor_8_bit substractor_8_bit_1 (.A(A), .B(B), .CIN(1'b0), .out_4(substractor_8_bit_1_out_4));  // open: out_5
  Right_bitshifter right_bitshifter_1 (.in_1(A), .in_2(B), .out_3(right_bitshifter_1_out_3));
  Left_bitshifter left_bitshifter_1 (.in_1(A), .in_2(B), .out_3(left_bitshifter_1_out_3));
  De_Coder de_coder_1 (
    .in_1(S2), .in_2(S1), .in_3(S0), ._1(de_coder_1__1), ._2(de_coder_1__2), ._3(de_coder_1__3),
    ._4(de_coder_1__4), ._5(de_coder_1__5), ._6(de_coder_1__6));  // open: _0, _7
  one_hot_mux_8bit one_hot_mux_8bit_1 (
    .ADD(ripple_carry_adder_8bit_1_out_4), .X(xor_gate_8bit_1_out_3), .AN(and_gate_8bit_1_out_3),
    .SUB(substractor_8_bit_1_out_4), .RS(right_bitshifter_1_out_3), .LS(left_bitshifter_1_out_3),
    .CADD(de_coder_1__1), .CX(de_coder_1__2), .CAN(de_coder_1__3), .CSUB(de_coder_1__4), .CRS(de_coder_1__5),
    .CLS(de_coder_1__6), .O(O));
  // Probe on O
endmodule

module one_hot_mux_1bit (
  input  A,
  input  B,
  input  C,
  input  C1,
  input  C2,
  input  C3,
  output O
);

  wire and_gate_1_out_3, and_gate_2_out_3, and_gate_3_out_3;

  AND_Gate and_gate_1 (.in_1(A), .in_2(C1), .out_3(and_gate_1_out_3));
  AND_Gate and_gate_2 (.in_1(B), .in_2(C2), .out_3(and_gate_2_out_3));
  AND_Gate and_gate_3 (.in_1(C), .in_2(C3), .out_3(and_gate_3_out_3));
  or or_1 (O, and_gate_1_out_3, and_gate_2_out_3, and_gate_3_out_3);
endmodule

module one_hot_mux_8bit (
  input  [7:0] ADD,
  input  [7:0] X,
  input  [7:0] AN,
  input  [7:0] SUB,
  input  [7:0] RS,
  input  [7:0] LS,
  input  CADD,
  input  CX,
  input  CAN,
  input  CSUB,
  input  CRS,
  input  CLS,
  output [7:0] O
);

  wire [7:0] and_gate_8bit_1_out_3, and_gate_8bit_2_out_3, and_gate_8bit_3_out_3, and_gate_8bit_4_out_3,
       and_gate_8bit_5_out_3, and_gate_8bit_6_out_3, or_1_out, or_2_out;

  AND_Gate_8bit and_gate_8bit_1 (.in_1(ADD), .in_2({8{CADD}}), .out_3(and_gate_8bit_1_out_3));
  AND_Gate_8bit and_gate_8bit_2 (.in_1(X), .in_2({8{CX}}), .out_3(and_gate_8bit_2_out_3));
  AND_Gate_8bit and_gate_8bit_3 (.in_1(AN), .in_2({8{CAN}}), .out_3(and_gate_8bit_3_out_3));
  AND_Gate_8bit and_gate_8bit_4 (.in_1(SUB), .in_2({8{CSUB}}), .out_3(and_gate_8bit_4_out_3));
  AND_Gate_8bit and_gate_8bit_5 (.in_1(RS), .in_2({8{CRS}}), .out_3(and_gate_8bit_5_out_3));
  AND_Gate_8bit and_gate_8bit_6 (.in_1(LS), .in_2({8{CLS}}), .out_3(and_gate_8bit_6_out_3));
  assign or_1_out = and_gate_8bit_1_out_3 | and_gate_8bit_2_out_3 | and_gate_8bit_3_out_3;  // OR_Gate_part or_1, 8 bits wide
  assign or_2_out = and_gate_8bit_4_out_3 | and_gate_8bit_5_out_3 | and_gate_8bit_6_out_3;  // OR_Gate_part or_2, 8 bits wide
  assign O = or_1_out | or_2_out;  // OR_Gate_part or_3, 8 bits wide
endmodule

module Full_Substractor (
  input  A,
  input  B,
  input  CIN,
  output SUM,
  output COUT
);

  wire and_1_out, and_2_out, not_1_out, not_2_out, xor_1_out;

  not not_1 (not_1_out, A);
  xor xor_1 (xor_1_out, A, B);
  not not_2 (not_2_out, xor_1_out);
  and and_1 (and_1_out, not_1_out, B);
  xor xor_2 (SUM, xor_1_out, CIN);
  and and_2 (and_2_out, not_2_out, CIN);
  or or_1 (COUT, and_1_out, and_2_out);
  // Probe on {COUT, SUM}
endmodule

module Substractor_8_bit (
  input  [7:0] A,
  input  [7:0] B,
  input  CIN,
  output [7:0] out_4,
  output out_5
);

  wire full_substractor_1_cout, full_substractor_2_cout, full_substractor_3_cout, full_substractor_4_cout,
       full_substractor_5_cout, full_substractor_6_cout, full_substractor_7_cout;

  // Probe on B
  // Probe on A
  Full_Substractor full_substractor_1 (.A(A[0]), .B(B[0]), .CIN(CIN), .SUM(out_4[0]), .COUT(full_substractor_1_cout));
  Full_Substractor full_substractor_2 (
    .A(A[1]), .B(B[1]), .CIN(full_substractor_1_cout), .SUM(out_4[1]), .COUT(full_substractor_2_cout));
  Full_Substractor full_substractor_3 (
    .A(A[2]), .B(B[2]), .CIN(full_substractor_2_cout), .SUM(out_4[2]), .COUT(full_substractor_3_cout));
  Full_Substractor full_substractor_4 (
    .A(A[3]), .B(B[3]), .CIN(full_substractor_3_cout), .SUM(out_4[3]), .COUT(full_substractor_4_cout));
  Full_Substractor full_substractor_5 (
    .A(A[4]), .B(B[4]), .CIN(full_substractor_4_cout), .SUM(out_4[4]), .COUT(full_substractor_5_cout));
  Full_Substractor full_substractor_6 (
    .A(A[5]), .B(B[5]), .CIN(full_substractor_5_cout), .SUM(out_4[5]), .COUT(full_substractor_6_cout));
  Full_Substractor full_substractor_7 (
    .A(A[6]), .B(B[6]), .CIN(full_substractor_6_cout), .SUM(out_4[6]), .COUT(full_substractor_7_cout));
  Full_Substractor full_substractor_8 (.A(A[7]), .B(B[7]), .CIN(full_substractor_7_cout), .SUM(out_4[7]), .COUT(out_5));
  // Probe on {out_5, out_4}
  // Probe on out_4
endmodule

module ALU_8bit_WOD (
  input  [7:0] A,
  input  [7:0] B,
  input  CADD,
  input  CX,
  input  CAN,
  input  CSUB,
  input  CRS,
  input  CLS,
  output [7:0] O
);

  wire [7:0] and_gate_8bit_1_out_3, left_bitshifter_1_out_3, right_bitshifter_1_out_3,
       ripple_carry_adder_8bit_1_out_4, substractor_8_bit_1_out_4, xor_gate_8bit_1_out_3;

  // Probe on A
  // Probe on B
  Ripple_Carry_Adder_8bit ripple_carry_adder_8bit_1 (
    .A(A), .B(B), .CIN(1'b0), .out_4(ripple_carry_adder_8bit_1_out_4));  // open: out_5
  XOR_Gate_8bit xor_gate_8bit_1 (.in_1(A), .in_2(B), .out_3(xor_gate_8bit_1_out_3));
  AND_Gate_8bit and_gate_8bit_1 (.in_1(A), .in_2(B), .out_3(and_gate_8bit_1_out_3));
  Substractor_8_bit substractor_8_bit_1 (.A(A), .B(B), .CIN(1'b0), .out_4(substractor_8_bit_1_out_4));  // open: out_5
  Right_bitshifter right_bitshifter_1 (.in_1(A), .in_2(B), .out_3(right_bitshifter_1_out_3));
  Left_bitshifter left_bitshifter_1 (.in_1(A), .in_2(B), .out_3(left_bitshifter_1_out_3));
  one_hot_mux_8bit one_hot_mux_8bit_1 (
    .ADD(ripple_carry_adder_8bit_1_out_4), .X(xor_gate_8bit_1_out_3), .AN(and_gate_8bit_1_out_3),
    .SUB(substractor_8_bit_1_out_4), .RS(right_bitshifter_1_out_3), .LS(left_bitshifter_1_out_3),
    .CADD(CADD), .CX(CX), .CAN(CAN), .CSUB(CSUB), .CRS(CRS), .CLS(CLS), .O(O));
  // Probe on O
endmodule

module MUX_2to1 (
  input  [7:0] Ai,
  input  [7:0] Bi,
  input  CA,
  input  CB,
  output [7:0] Oi
);

  wire [7:0] and_1_out, and_2_out;

  assign and_1_out = Ai & {8{CA}};  // AND_Gate_part and_1, 8 bits wide
  assign and_2_out = {8{CB}} & Bi;  // AND_Gate_part and_2, 8 bits wide
  assign Oi = and_1_out | and_2_out;  // OR_Gate_part or_1, 8 bits wide
endmodule

module Flip_Flop (
  input  in_1,
  input  in_2,
  output out_3,
  output out_4
);

  wire clock_1_out, nand_1_out, nand_2_out;

  Clock clock_1 (.out(clock_1_out));
  nand nand_1 (nand_1_out, in_1, clock_1_out);
  nand nand_2 (nand_2_out, clock_1_out, in_2);
  nand nand_3 (out_3, nand_1_out, out_4);
  nand nand_4 (out_4, out_3, nand_2_out);
endmodule

module D_flip_flop (
  input  in_1,
  input  in_2,
  output out_3,
  output out_4
);

  wire nand_1_out, nand_2_out, not_1_out;

  not not_1 (not_1_out, in_1);
  nand nand_1 (nand_1_out, in_1, in_2);
  nand nand_2 (nand_2_out, in_2, not_1_out);
  nand nand_3 (out_3, nand_1_out, out_4);
  nand nand_4 (out_4, out_3, nand_2_out);
endmodule

module Control_Unit_Sequencer (
  output fetch,
  output fetchwrite,
  output execute,
  output Executewrite
);

  wire clock_1_out;

  Clock clock_1 (.out(clock_1_out));
  D_Flip_Flop d_ff_1 (.D(execute), .clk(clock_1_out), .Q(fetch), .Qn(execute));  // open: preset, reset
  and and_1 (fetchwrite, fetch, clock_1_out);
  and and_2 (Executewrite, execute, clock_1_out);
endmodule

module memory_cell (
  input  Din,
  input  WE,
  input  clock,
  input  Reset,
  output Dout
);

  wire and_1_out, and_2_out, not_1_out, or_1_out;

  not not_1 (not_1_out, WE);
  and and_1 (and_1_out, Din, WE);
  and and_2 (and_2_out, Dout, not_1_out);
  or or_1 (or_1_out, and_1_out, and_2_out);
  D_Flip_Flop d_ff_1 (.D(or_1_out), .clk(clock), .Q(Dout), .reset(Reset));  // open: Qn, preset
endmodule

module Controled_Buffer (
  input  in_1,
  input  in_2,
  output out_3
);

  wire not_1_out;

  not not_1 (not_1_out, in_1);
  Transistor #(.\type ("n")) transistor_1 (.in(in_2), .out(out_3), .gate(in_1));
  Transistor transistor_2 (.in(in_2), .out(out_3), .gate(not_1_out));
endmodule

module register_8bit (
  input  [7:0] D,
  input  WE,
  input  in_3,
  input  R,
  output [7:0] Q
);

  memory_cell memory_cell_1 (.Din(D[0]), .WE(WE), .clock(in_3), .Reset(R), .Dout(Q[0]));
  memory_cell memory_cell_2 (.Din(D[1]), .WE(WE), .clock(in_3), .Reset(R), .Dout(Q[1]));
  memory_cell memory_cell_3 (.Din(D[2]), .WE(WE), .clock(in_3), .Reset(R), .Dout(Q[2]));
  memory_cell memory_cell_4 (.Din(D[3]), .WE(WE), .clock(in_3), .Reset(R), .Dout(Q[3]));
  memory_cell memory_cell_5 (.Din(D[4]), .WE(WE), .clock(in_3), .Reset(R), .Dout(Q[4]));
  memory_cell memory_cell_6 (.Din(D[5]), .WE(WE), .clock(in_3), .Reset(R), .Dout(Q[5]));
  memory_cell memory_cell_7 (.Din(D[6]), .WE(WE), .clock(in_3), .Reset(R), .Dout(Q[6]));
  memory_cell memory_cell_8 (.Din(D[7]), .WE(WE), .clock(in_3), .Reset(R), .Dout(Q[7]));
endmodule

module register_4bit (
  input  [3:0] D,
  input  WE,
  input  R,
  output [3:0] Q
);

  wire clock_1_out;

  Clock clock_1 (.out(clock_1_out));
  memory_cell memory_cell_1 (.Din(D[0]), .WE(WE), .clock(clock_1_out), .Reset(R), .Dout(Q[0]));
  memory_cell memory_cell_2 (.Din(D[1]), .WE(WE), .clock(clock_1_out), .Reset(R), .Dout(Q[1]));
  memory_cell memory_cell_3 (.Din(D[2]), .WE(WE), .clock(clock_1_out), .Reset(R), .Dout(Q[2]));
  memory_cell memory_cell_4 (.Din(D[3]), .WE(WE), .clock(clock_1_out), .Reset(R), .Dout(Q[3]));
endmodule

module register_16bits (
  input  [15:0] D,
  input  WE,
  input  CLK,
  input  R,
  output [15:0] Q
);

  register_8bit register_8bit_1 (.D(D[7:0]), .WE(WE), .in_3(CLK), .R(R), .Q(Q[7:0]));
  register_8bit register_8bit_2 (.D(D[15:8]), .WE(WE), .in_3(CLK), .R(R), .Q(Q[15:8]));
endmodule

module Memory_bank_16x16_bits (
  input  [15:0] D,
  input  [3:0] A,
  input  WE,
  input  OE,
  input  CLK,
  input  R,
  output [15:0] out_7
);

  wire and_1_out, and_2_out, and_3_out, and_4_out, and_5_out, and_6_out, and_7_out, and_8_out, and_9_out,
       and_10_out, and_11_out, and_12_out, and_13_out, and_14_out, and_15_out, and_16_out,
       de_coder_de_mux_16bits_1_c1, de_coder_de_mux_16bits_1_c2, de_coder_de_mux_16bits_1_c3,
       de_coder_de_mux_16bits_1_c4, de_coder_de_mux_16bits_1_c5, de_coder_de_mux_16bits_1_c6,
       de_coder_de_mux_16bits_1_c7, de_coder_de_mux_16bits_1_c8, de_coder_de_mux_16bits_1_c9,
       de_coder_de_mux_16bits_1_c10, de_coder_de_mux_16bits_1_c11, de_coder_de_mux_16bits_1_c12,
       de_coder_de_mux_16bits_1_c13, de_coder_de_mux_16bits_1_c14, de_coder_de_mux_16bits_1_c15,
       de_coder_de_mux_16bits_1_c16;
  wire [15:0] de_coder_de_mux_16bits_1__2, de_coder_de_mux_16bits_1__3, de_coder_de_mux_16bits_1__4,
       de_coder_de_mux_16bits_1__5, de_coder_de_mux_16bits_1__6, de_coder_de_mux_16bits_1__7,
       de_coder_de_mux_16bits_1_a_2, de_coder_de_mux_16bits_1_b, de_coder_de_mux_16bits_1_c,
       de_coder_de_mux_16bits_1_d_2, de_coder_de_mux_16bits_1_e, de_coder_de_mux_16bits_1_f,
       de_coder_de_mux_16bits_1_out_3, de_coder_de_mux_16bits_1_out_5, de_coder_de_mux_16bits_1_out_19,
       de_coder_de_mux_16bits_1_out_21, mux_4_bits_1_out_18, register_16bits_1_q, register_16bits_2_q,
       register_16bits_3_q, register_16bits_4_q, register_16bits_5_q, register_16bits_6_q,
       register_16bits_7_q, register_16bits_8_q, register_16bits_9_q, register_16bits_10_q,
       register_16bits_11_q, register_16bits_12_q, register_16bits_13_q, register_16bits_14_q,
       register_16bits_15_q, register_16bits_16_q;

  DE_coder_De_mux_16bits de_coder_de_mux_16bits_1 (
    .D(D), .A(A), .out_3(de_coder_de_mux_16bits_1_out_3), .C1(de_coder_de_mux_16bits_1_c1),
    .out_5(de_coder_de_mux_16bits_1_out_5), .C2(de_coder_de_mux_16bits_1_c2),
    ._2(de_coder_de_mux_16bits_1__2), .C3(de_coder_de_mux_16bits_1_c3), ._3(de_coder_de_mux_16bits_1__3),
    .C4(de_coder_de_mux_16bits_1_c4), ._4(de_coder_de_mux_16bits_1__4), .C5(de_coder_de_mux_16bits_1_c5),
    ._5(de_coder_de_mux_16bits_1__5), .C6(de_coder_de_mux_16bits_1_c6), ._6(de_coder_de_mux_16bits_1__6),
    .C7(de_coder_de_mux_16bits_1_c7), ._7(de_coder_de_mux_16bits_1__7), .C8(de_coder_de_mux_16bits_1_c8),
    .out_19(de_coder_de_mux_16bits_1_out_19), .C9(de_coder_de_mux_16bits_1_c9),
    .out_21(de_coder_de_mux_16bits_1_out_21), .C10(de_coder_de_mux_16bits_1_c10),
    .a_2(de_coder_de_mux_16bits_1_a_2), .C11(de_coder_de_mux_16bits_1_c11), .b(de_coder_de_mux_16bits_1_b),
    .C12(de_coder_de_mux_16bits_1_c12), .c(de_coder_de_mux_16bits_1_c), .C13(de_coder_de_mux_16bits_1_c13),
    .d_2(de_coder_de_mux_16bits_1_d_2), .C14(de_coder_de_mux_16bits_1_c14), .e(de_coder_de_mux_16bits_1_e),
    .C15(de_coder_de_mux_16bits_1_c15), .f(de_coder_de_mux_16bits_1_f), .C16(de_coder_de_mux_16bits_1_c16));
  and and_1 (and_1_out, de_coder_de_mux_16bits_1_c1, WE);
  buf and_2 (and_2_out, de_coder_de_mux_16bits_1_c5);  // AND_Gate_part
  and and_3 (and_3_out, de_coder_de_mux_16bits_1_c9, WE);
  and and_4 (and_4_out, de_coder_de_mux_16bits_1_c13, WE);
  register_16bits register_16bits_1 (
    .D(de_coder_de_mux_16bits_1_out_3), .WE(and_1_out), .CLK(CLK), .R(R), .Q(register_16bits_1_q));
  register_16bits register_16bits_2 (
    .D(de_coder_de_mux_16bits_1__4), .WE(and_2_out), .CLK(CLK), .R(R), .Q(register_16bits_2_q));
  register_16bits register_16bits_3 (
    .D(de_coder_de_mux_16bits_1_out_19), .WE(and_3_out), .CLK(CLK), .R(R), .Q(register_16bits_3_q));
  register_16bits register_16bits_4 (
    .D(de_coder_de_mux_16bits_1_c), .WE(and_4_out), .CLK(CLK), .R(R), .Q(register_16bits_4_q));
  and and_5 (and_5_out, de_coder_de_mux_16bits_1_c2, WE);
  and and_6 (and_6_out, de_coder_de_mux_16bits_1_c6, WE);
  and and_7 (and_7_out, de_coder_de_mux_16bits_1_c10, WE);
  and and_8 (and_8_out, de_coder_de_mux_16bits_1_c14, WE);
  register_16bits register_16bits_5 (
    .D(de_coder_de_mux_16bits_1_out_5), .WE(and_5_out), .CLK(CLK), .R(R), .Q(register_16bits_5_q));
  register_16bits register_16bits_6 (
    .D(de_coder_de_mux_16bits_1__5), .WE(and_6_out), .CLK(CLK), .R(R), .Q(register_16bits_6_q));
  register_16bits register_16bits_7 (
    .D(de_coder_de_mux_16bits_1_out_21), .WE(and_7_out), .CLK(CLK), .R(R), .Q(register_16bits_7_q));
  register_16bits register_16bits_8 (
    .D(de_coder_de_mux_16bits_1_d_2), .WE(and_8_out), .CLK(CLK), .R(R), .Q(register_16bits_8_q));
  and and_9 (and_9_out, de_coder_de_mux_16bits_1_c3, WE);
  and and_10 (and_10_out, de_coder_de_mux_16bits_1_c7, WE);
  and and_11 (and_11_out, de_coder_de_mux_16bits_1_c11, WE);
  and and_12 (and_12_out, de_coder_de_mux_16bits_1_c15, WE);
  register_16bits register_16bits_9 (
    .D(de_coder_de_mux_16bits_1__2), .WE(and_9_out), .CLK(CLK), .R(R), .Q(register_16bits_9_q));
  register_16bits register_16bits_10 (
    .D(de_coder_de_mux_16bits_1__6), .WE(and_10_out), .CLK(CLK), .R(R), .Q(register_16bits_10_q));
  register_16bits register_16bits_11 (
    .D(de_coder_de_mux_16bits_1_a_2), .WE(and_11_out), .CLK(CLK), .R(R), .Q(register_16bits_11_q));
  register_16bits register_16bits_12 (
    .D(de_coder_de_mux_16bits_1_e), .WE(and_12_out), .CLK(CLK), .R(R), .Q(register_16bits_12_q));
  and and_13 (and_13_out, de_coder_de_mux_16bits_1_c4, WE);
  and and_14 (and_14_out, de_coder_de_mux_16bits_1_c8, WE);
  and and_15 (and_15_out, de_coder_de_mux_16bits_1_c12, WE);
  and and_16 (and_16_out, de_coder_de_mux_16bits_1_c16, WE);
  register_16bits register_16bits_13 (
    .D(de_coder_de_mux_16bits_1__3), .WE(and_13_out), .CLK(CLK), .R(R), .Q(register_16bits_13_q));
  register_16bits register_16bits_14 (
    .D(de_coder_de_mux_16bits_1__7), .WE(and_14_out), .CLK(CLK), .R(R), .Q(register_16bits_14_q));
  register_16bits register_16bits_15 (
    .D(de_coder_de_mux_16bits_1_b), .WE(and_15_out), .CLK(CLK), .R(R), .Q(register_16bits_15_q));
  register_16bits register_16bits_16 (
    .D(de_coder_de_mux_16bits_1_f), .WE(and_16_out), .CLK(CLK), .R(R), .Q(register_16bits_16_q));
  mux_4_bits mux_4_bits_1 (
    .A(A), .in_2(register_16bits_1_q), .in_3(register_16bits_5_q), .in_4(register_16bits_9_q),
    .in_5(register_16bits_13_q), .in_6(register_16bits_2_q), .in_7(register_16bits_6_q),
    .in_8(register_16bits_10_q), .in_9(register_16bits_14_q), .in_10(register_16bits_3_q),
    .in_11(register_16bits_7_q), .in_12(register_16bits_11_q), .in_13(register_16bits_15_q),
    .in_14(register_16bits_4_q), .in_15(register_16bits_8_q), .in_16(register_16bits_12_q),
    .in_17(register_16bits_16_q), .out_18(mux_4_bits_1_out_18));
  assign out_7 = OE ? mux_4_bits_1_out_18 : 16'bz;  // Controlled_Buffer controlled_buffer_1
  Pull_Resistor pull_resistor_1 (.node(out_7));
endmodule

module DE_coder_De_mux_16bits (
  input  [15:0] D,
  input  [3:0] A,
  output [15:0] out_3,
  output C1,
  output [15:0] out_5,
  output C2,
  output [15:0] _2,
  output C3,
  output [15:0] _3,
  output C4,
  output [15:0] _4,
  output C5,
  output [15:0] _5,
  output C6,
  output [15:0] _6,
  output C7,
  output [15:0] _7,
  output C8,
  output [15:0] out_19,
  output C9,
  output [15:0] out_21,
  output C10,
  output [15:0] a_2,
  output C11,
  output [15:0] b,
  output C12,
  output [15:0] c,
  output C13,
  output [15:0] d_2,
  output C14,
  output [15:0] e,
  output C15,
  output [15:0] f,
  output C16
);

  // Probe on A
  and and_1 (C2, A[0], ~A[1], ~A[2], ~A[3]);  // AND_Gate_part
  and and_2 (C3, ~A[0], A[1], ~A[2], ~A[3]);  // AND_Gate_part
  and and_3 (C4, A[0], A[1], ~A[2], ~A[3]);  // AND_Gate_part
  and and_4 (C5, ~A[0], ~A[1], A[2], ~A[3]);  // AND_Gate_part
  and and_5 (C6, A[0], ~A[1], A[2], ~A[3]);  // AND_Gate_part
  and and_6 (C7, ~A[0], A[1], A[2], ~A[3]);  // AND_Gate_part
  and and_7 (C8, A[0], A[1], A[2], ~A[3]);  // AND_Gate_part
  and and_8 (C9, ~A[0], ~A[1], ~A[2], A[3]);  // AND_Gate_part
  and and_9 (C10, A[0], ~A[1], ~A[2], A[3]);  // AND_Gate_part
  and and_10 (C11, ~A[0], A[1], ~A[2], A[3]);  // AND_Gate_part
  and and_11 (C12, A[0], A[1], ~A[2], A[3]);  // AND_Gate_part
  and and_12 (C13, ~A[0], ~A[1], A[2], A[3]);  // AND_Gate_part
  and and_13 (C14, A[0], ~A[1], A[2], A[3]);  // AND_Gate_part
  and and_14 (C15, ~A[0], A[1], A[2], A[3]);  // AND_Gate_part
  and and_15 (C16, A[0], A[1], A[2], A[3]);
  Pull_Resistor pull_resistor_1 (.node(out_3));
  assign out_3 = C1 ? D : 16'bz;  // Controlled_Buffer controlled_buffer_1
  nor nor_1 (C1, A[0], A[1], A[2], A[3]);
  Pull_Resistor pull_resistor_2 (.node(out_5));
  assign out_5 = C2 ? D : 16'bz;  // Controlled_Buffer controlled_buffer_2
  Pull_Resistor pull_resistor_3 (.node(_2));
  assign _2 = C3 ? D : 16'bz;  // Controlled_Buffer controlled_buffer_3
  Pull_Resistor pull_resistor_4 (.node(_3));
  assign _3 = C4 ? D : 16'bz;  // Controlled_Buffer controlled_buffer_4
  Pull_Resistor pull_resistor_5 (.node(_4));
  assign _4 = C5 ? D : 16'bz;  // Controlled_Buffer controlled_buffer_5
  Pull_Resistor pull_resistor_6 (.node(_5));
  assign _5 = C6 ? D : 16'bz;  // Controlled_Buffer controlled_buffer_6
  Pull_Resistor pull_resistor_7 (.node(_6));
  assign _6 = C7 ? D : 16'bz;  // Controlled_Buffer controlled_buffer_7
  Pull_Resistor pull_resistor_8 (.node(_7));
  assign _7 = C8 ? D : 16'bz;  // Controlled_Buffer controlled_buffer_8
  Pull_Resistor pull_resistor_9 (.node(out_19));
  assign out_19 = C9 ? D : 16'bz;  // Controlled_Buffer controlled_buffer_9
  Pull_Resistor pull_resistor_10 (.node(out_21));
  assign out_21 = C10 ? D : 16'bz;  // Controlled_Buffer controlled_buffer_10
  Pull_Resistor pull_resistor_11 (.node(a_2));
  assign a_2 = C11 ? D : 16'bz;  // Controlled_Buffer controlled_buffer_11
  Pull_Resistor pull_resistor_12 (.node(b));
  assign b = C12 ? D : 16'bz;  // Controlled_Buffer controlled_buffer_12
  Pull_Resistor pull_resistor_13 (.node(c));
  assign c = C13 ? D : 16'bz;  // Controlled_Buffer controlled_buffer_13
  Pull_Resistor pull_resistor_14 (.node(d_2));
  assign d_2 = C14 ? D : 16'bz;  // Controlled_Buffer controlled_buffer_14
  Pull_Resistor pull_resistor_15 (.node(e));
  assign e = C15 ? D : 16'bz;  // Controlled_Buffer controlled_buffer_15
  Pull_Resistor pull_resistor_16 (.node(f));
  assign f = C16 ? D : 16'bz;  // Controlled_Buffer controlled_buffer_16

  // Notes on the sheet:
  //   0
  //   1
  //   8
  //   9
endmodule

module PC (
  input  [7:0] D,
  input  Increment,
  input  Load,
  input  CLK,
  input  R,
  output [7:0] Q
);

  wire or_1_out;
  wire [7:0] incrementer_1_out_2, mux_2to1_1_oi;

  or or_1 (or_1_out, Increment, Load);
  INCREMENTER incrementer_1 (.in_1(Q), .out_2(incrementer_1_out_2));
  MUX_2to1 mux_2to1_1 (.Ai(incrementer_1_out_2), .Bi(D), .CA(Increment), .CB(Load), .Oi(mux_2to1_1_oi));
  register_8bit register_8bit_1 (.D(mux_2to1_1_oi), .WE(or_1_out), .in_3(CLK), .R(R), .Q(Q));
endmodule

module INCREMENTER (
  input  [7:0] in_1,
  output [7:0] out_2
);

  Ripple_Carry_Adder_8bit ripple_carry_adder_8bit_1 (.A(in_1), .B(8'h1), .CIN(1'b0), .out_4(out_2));  // open: out_5
endmodule

module mux_4_bits (
  input  [3:0] A,
  input  [15:0] in_2,
  input  [15:0] in_3,
  input  [15:0] in_4,
  input  [15:0] in_5,
  input  [15:0] in_6,
  input  [15:0] in_7,
  input  [15:0] in_8,
  input  [15:0] in_9,
  input  [15:0] in_10,
  input  [15:0] in_11,
  input  [15:0] in_12,
  input  [15:0] in_13,
  input  [15:0] in_14,
  input  [15:0] in_15,
  input  [15:0] in_16,
  input  [15:0] in_17,
  output [15:0] out_18
);

  wire and_1_out, and_2_out, and_3_out, and_4_out, and_5_out, and_6_out, and_7_out, and_8_out, and_9_out,
       and_10_out, and_11_out, and_12_out, and_13_out, and_14_out, and_15_out, nor_1_out;

  // Probe on A
  and and_1 (and_1_out, A[0], ~A[1], ~A[2], ~A[3]);  // AND_Gate_part
  and and_2 (and_2_out, ~A[0], A[1], ~A[2], ~A[3]);  // AND_Gate_part
  and and_3 (and_3_out, A[0], A[1], ~A[2], ~A[3]);  // AND_Gate_part
  and and_4 (and_4_out, ~A[0], ~A[1], A[2], ~A[3]);  // AND_Gate_part
  and and_5 (and_5_out, A[0], ~A[1], A[2], ~A[3]);  // AND_Gate_part
  and and_6 (and_6_out, ~A[0], A[1], A[2], ~A[3]);  // AND_Gate_part
  and and_7 (and_7_out, A[0], A[1], A[2], ~A[3]);  // AND_Gate_part
  and and_8 (and_8_out, ~A[0], ~A[1], ~A[2], A[3]);  // AND_Gate_part
  and and_9 (and_9_out, A[0], ~A[1], ~A[2], A[3]);  // AND_Gate_part
  and and_10 (and_10_out, ~A[0], A[1], ~A[2], A[3]);  // AND_Gate_part
  and and_11 (and_11_out, A[0], A[1], ~A[2], A[3]);  // AND_Gate_part
  and and_12 (and_12_out, ~A[0], ~A[1], A[2], A[3]);  // AND_Gate_part
  and and_13 (and_13_out, A[0], ~A[1], A[2], A[3]);  // AND_Gate_part
  and and_14 (and_14_out, ~A[0], A[1], A[2], A[3]);  // AND_Gate_part
  and and_15 (and_15_out, A[0], A[1], A[2], A[3]);
  nor nor_1 (nor_1_out, A[0], A[1], A[2], A[3]);
  assign out_18 = nor_1_out ? in_2 : 16'bz;  // Controlled_Buffer controlled_buffer_1
  assign out_18 = and_1_out ? in_3 : 16'bz;  // Controlled_Buffer controlled_buffer_2
  assign out_18 = and_2_out ? in_4 : 16'bz;  // Controlled_Buffer controlled_buffer_3
  assign out_18 = and_3_out ? in_5 : 16'bz;  // Controlled_Buffer controlled_buffer_4
  assign out_18 = and_4_out ? in_6 : 16'bz;  // Controlled_Buffer controlled_buffer_5
  assign out_18 = and_5_out ? in_7 : 16'bz;  // Controlled_Buffer controlled_buffer_6
  assign out_18 = and_6_out ? in_8 : 16'bz;  // Controlled_Buffer controlled_buffer_7
  assign out_18 = and_7_out ? in_9 : 16'bz;  // Controlled_Buffer controlled_buffer_8
  assign out_18 = and_8_out ? in_10 : 16'bz;  // Controlled_Buffer controlled_buffer_9
  assign out_18 = and_9_out ? in_11 : 16'bz;  // Controlled_Buffer controlled_buffer_10
  assign out_18 = and_10_out ? in_12 : 16'bz;  // Controlled_Buffer controlled_buffer_11
  assign out_18 = and_11_out ? in_13 : 16'bz;  // Controlled_Buffer controlled_buffer_12
  assign out_18 = and_12_out ? in_14 : 16'bz;  // Controlled_Buffer controlled_buffer_13
  assign out_18 = and_13_out ? in_15 : 16'bz;  // Controlled_Buffer controlled_buffer_14
  assign out_18 = and_14_out ? in_16 : 16'bz;  // Controlled_Buffer controlled_buffer_15
  assign out_18 = and_15_out ? in_17 : 16'bz;  // Controlled_Buffer controlled_buffer_16
endmodule

module main (
);

  ALU_8bit_WOD alu_8bit_wod_1 ();  // open: A, B, CADD, CX, CAN, CSUB, CRS, CLS, O
  R_mux r_mux_1 ();  // open: Ai, Bi, Ci, CA, CB, CC, Oi
  register_8bit register_8bit_1 ();  // open: D, WE, in_3, R, Q
  register_8bit register_8bit_2 ();  // open: D, WE, in_3, R, Q
  PC pc_1 ();  // open: D, Increment, Load, CLK, R, Q
  MUX_2to1 mux_2to1_1 ();  // open: Ai, Bi, CA, CB, Oi
  Memory_bank_16x16_bits memory_bank_16x16_bits_1 ();  // open: D, A, WE, OE, CLK, R, out_7
endmodule

module R_mux (
  input  [7:0] Ai,
  input  [7:0] Bi,
  input  [7:0] Ci,
  input  CA,
  input  CB,
  input  CC,
  output [7:0] Oi
);

  wire [7:0] and_1_out, and_2_out, and_3_out;

  assign and_1_out = Ai & {8{CA}};  // AND_Gate_part and_1, 8 bits wide
  assign and_2_out = {8{CB}} & Bi;  // AND_Gate_part and_2, 8 bits wide
  assign and_3_out = {8{CC}} & Ci;  // AND_Gate_part and_3, 8 bits wide
  assign Oi = and_1_out | and_3_out | and_2_out;  // OR_Gate_part or_1, 8 bits wide
endmodule
